// Digital circuit ALU.dig as structural Verilog
module ALU (
  input  [31:0] A,
  input  [31:0] B,
  input  [4:0] Shift,
  input  [3:0] Cod_Op,
  input  Carry_In,
  input  Negate,
  output [31:0] S,
  output [3:0] Flags
);

  wire add_1_c_o, add_2_c_o, and_1_out, and_2_out, and_6_out, and_7_out, and_8_out, bitselector_1_out,
       bitselector_2_out, comparator_1_eq, multiplexer_2_out, multiplexer_5_out, multiplexer_6_out,
       not_3_out, not_4_out, or_2_out, sub_1_c_o, xor_2_out, xor_3_out;
  wire [1:0] multiplexer_3_out;
  wire [4:0] sub_2_s, sub_3_s;
  wire [31:0] add_1_s, add_2_s, and_3_out, and_4_out, and_5_out, barrelshifter_1_out, barrelshifter_2_out,
       barrelshifter_3_out, barrelshifter_4_out, multiplexer_1_out, multiplexer_4_out, neg_1_out, not_1_out,
       not_2_out, or_1_out, sub_1_s, xor_1_out;
  wire [63:0] mul_1_mul;

  and and_1 (and_1_out, Cod_Op[2], Carry_In);
  and and_2 (and_2_out, Cod_Op[2], ~Carry_In);  // And
  assign and_3_out = A & B;  // And and_3, 32 bits wide
  assign xor_1_out = A ^ B;  // XOr xor_1, 32 bits wide
  BarrelShifter #(.Bits(32)) barrelshifter_1 (.in(A), .shift({1'b0, Shift}), .out(barrelshifter_1_out));
  BarrelShifter #(.Bits(32), .direction("right")) barrelshifter_2 (
    .in(A), .shift({1'b0, Shift}), .out(barrelshifter_2_out));
  BarrelShifter #(.barrelShifterMode("arithmetic"), .Bits(32), .direction("right")) barrelshifter_3 (
    .in(A), .shift({1'b0, Shift}), .out(barrelshifter_3_out));
  Add #(.Bits(32)) add_1 (.a(A), .b(B), .c_i(and_1_out), .s(add_1_s), .c_o(add_1_c_o));
  Sub #(.Bits(32)) sub_1 (.a(A), .b(B), .c_i(and_2_out), .s(sub_1_s), .c_o(sub_1_c_o));
  BarrelShifter #(.barrelShifterMode("rotate"), .Bits(32), .direction("right")) barrelshifter_4 (
    .in(A), .shift({1'b0, Shift}), .out(barrelshifter_4_out));
  assign and_4_out = A & B;  // And and_4, 32 bits wide
  Add #(.Bits(32)) add_2 (.a(not_1_out), .b(32'h1), .c_i(1'b0), .s(add_2_s), .c_o(add_2_c_o));
  assign not_1_out = ~B;  // Not not_1, 32 bits wide
  assign or_1_out = A | B;  // Or or_1, 32 bits wide
  Mul #(.Bits(32)) mul_1 (.a(A), .b(B), .mul(mul_1_mul));
  assign and_5_out = A & ~B;  // And and_5, 32 bits wide
  assign not_2_out = ~B;  // Not not_2, 32 bits wide
  not not_3 (not_3_out, sub_1_c_o);
  Multiplexer #(.Selector_Bits(4), .Bits(32)) multiplexer_1 (
    .sel(Cod_Op), .in_0(and_3_out), .in_1(xor_1_out), .in_2(barrelshifter_1_out), .in_3(barrelshifter_2_out),
    .in_4(barrelshifter_3_out), .in_5(add_1_s), .in_6(sub_1_s), .in_7(barrelshifter_4_out), .in_8(and_4_out),
    .in_9(add_2_s), .in_10(sub_1_s), .in_11(add_1_s), .in_12(or_1_out), .in_13(mul_1_mul[31:0]),
    .in_14(and_5_out), .in_15(not_2_out), .out(multiplexer_1_out));
  Multiplexer multiplexer_2 (.sel(not_4_out), .in_0(add_1_c_o), .in_1(not_3_out), .out(multiplexer_2_out));
  not not_4 (not_4_out, Cod_Op[0]);
  Multiplexer #(.Selector_Bits(4), .Bits(2)) multiplexer_3 (
    .sel(Cod_Op), .in_0(2'b00), .in_1(2'b00), .in_2(2'b11), .in_3(2'b10), .in_4(2'b10), .in_5(2'b01),
    .in_6(2'b01), .in_7(2'b10), .in_8(2'b00), .in_9(2'b01), .in_10(2'b01), .in_11(2'b01), .in_12(2'b00),
    .in_13(2'b00), .in_14(2'b00), .in_15(2'b00), .out(multiplexer_3_out));
  Neg #(.Bits(32)) neg_1 (.in(multiplexer_1_out), .out(neg_1_out));
  Comparator #(.Bits(4)) comparator_1 (.a(Cod_Op), .b(4'b1001), .eq(comparator_1_eq));  // open: gt, lt
  Sub #(.Bits(5)) sub_2 (.a({5{1'b0}}), .b(Shift), .c_i(1'b0), .s(sub_2_s));  // open: c_o
  Sub #(.Bits(5)) sub_3 (.a(Shift), .b(5'b00001), .c_i(1'b0), .s(sub_3_s));  // open: c_o
  Multiplexer #(.Bits(32)) multiplexer_4 (
    .sel(Negate), .in_0(multiplexer_1_out), .in_1(neg_1_out), .out(multiplexer_4_out));
  Multiplexer multiplexer_5 (.sel(and_6_out), .in_0(multiplexer_2_out), .in_1(add_2_c_o), .out(multiplexer_5_out));
  and and_6 (and_6_out, ~Cod_Op[1], ~Cod_Op[2]);  // And
  BitSelector #(.Selector_Bits(5)) bitselector_1 (.in(A), .sel(sub_2_s), .out(bitselector_1_out));
  Multiplexer multiplexer_6 (.sel(comparator_1_eq), .in_0(A[31]), .in_1(1'b0), .out(multiplexer_6_out));
  and and_7 (and_7_out, ~comparator_1_eq, Cod_Op[0]);  // And
  BitSelector #(.Selector_Bits(5)) bitselector_2 (.in(A), .sel(sub_3_s), .out(bitselector_2_out));
  or or_2 (or_2_out, ~Cod_Op[0], Cod_Op[1]);  // Or
  Comparator #(.Signed("true"), .Bits(32)) comparator_2 (
    .a(multiplexer_4_out), .b({32{1'b0}}), .eq(Flags[2]), .lt(Flags[3]));  // open: gt
  Multiplexer #(.Selector_Bits(2)) multiplexer_7 (
    .sel(multiplexer_3_out), .in_0(1'b0), .in_1(multiplexer_5_out), .in_2(bitselector_1_out),
    .in_3(bitselector_2_out), .out(Flags[1]));
  xor xor_2 (xor_2_out, Flags[3], multiplexer_6_out);
  xor xor_3 (xor_3_out, multiplexer_6_out, B[31], and_7_out);
  Multiplexer #(.Bits(32)) multiplexer_8 (.sel(and_8_out), .in_0(multiplexer_4_out), .in_1(A), .out(S));
  and and_8 (and_8_out, or_2_out, ~Cod_Op[2], Cod_Op[3]);  // And
  and and_9 (Flags[0], xor_2_out, xor_3_out, multiplexer_3_out[0]);

  // Other names for the same wires on the sheet: Op[3:0] = Cod_Op; S_t[4:0] = Shift
endmodule
