// Digital circuit BCD.dig as structural Verilog
module BCD (
  input  [31:0] In,
  output [31:0] Out
);

  wire [31:0] div_1_q, div_2_q, div_3_q, div_4_q, div_5_q, div_6_q, div_7_q;
  wire [31:4] div_1_r, div_2_r, div_3_r, div_4_r, div_5_r, div_6_r, div_7_r, div_8_r;

  Div #(.Bits(32)) div_1 (.a(In), .b(32'ha), .q(div_1_q), .r({div_1_r, Out[31:28]}));
  Div #(.Bits(32)) div_2 (.a(div_1_q), .b(32'ha), .q(div_2_q), .r({div_2_r, Out[27:24]}));
  Div #(.Bits(32)) div_3 (.a(div_2_q), .b(32'ha), .q(div_3_q), .r({div_3_r, Out[23:20]}));
  Div #(.Bits(32)) div_4 (.a(div_3_q), .b(32'ha), .q(div_4_q), .r({div_4_r, Out[19:16]}));
  Div #(.Bits(32)) div_5 (.a(div_4_q), .b(32'ha), .q(div_5_q), .r({div_5_r, Out[15:12]}));
  Div #(.Bits(32)) div_6 (.a(div_5_q), .b(32'ha), .q(div_6_q), .r({div_6_r, Out[11:8]}));
  Div #(.Bits(32)) div_7 (.a(div_6_q), .b(32'ha), .q(div_7_q), .r({div_7_r, Out[7:4]}));
  Div #(.Bits(32)) div_8 (.a(div_7_q), .b(32'ha), .r({div_8_r, Out[3:0]}));  // open: q
endmodule
