// Digital circuit BancDeRegistres.dig as structural Verilog
module BancDeRegistres (
  input  [31:0] Data_In,
  input  [3:0] Reg_Dest,
  input  Write_En,
  input  Rst,
  input  [3:0] Reg_B,
  input  [3:0] Reg_A,
  input  Clk,
  input  Link,
  input  PC_Hold,
  input  Force_Word_Align,
  output [31:0] A_Out,
  output [31:0] B_Out,
  output [31:0] R_0,
  output [31:0] R_1,
  output [31:0] R_2,
  output [31:0] R_3,
  output [31:0] R_4,
  output [31:0] R_5,
  output [31:0] R_6,
  output [31:0] R_7,
  output [31:0] R_8,
  output [31:0] R_9,
  output [31:0] R_10,
  output [31:0] R_11,
  output [31:0] R_12,
  output [31:0] R_13,
  output [31:0] R_14,
  output [31:0] R_15,
  output [31:0] D_Out
);

  wire and_1_out, and_2_out, and_4_out, and_5_out, comparator_1_eq, comparator_2_eq, demultiplexer_1_out_0,
       demultiplexer_1_out_1, demultiplexer_1_out_2, demultiplexer_1_out_3, demultiplexer_1_out_4,
       demultiplexer_1_out_5, demultiplexer_1_out_6, demultiplexer_1_out_7, demultiplexer_1_out_8,
       demultiplexer_1_out_9, demultiplexer_1_out_10, demultiplexer_1_out_11, demultiplexer_1_out_12,
       demultiplexer_1_out_13, or_1_out;
  wire [31:0] add_1_s, add_2_s, and_3_out, and_6_out, multiplexer_1_out, multiplexer_2_out,
       multiplexer_3_out, multiplexer_5_out;

  and and_1 (and_1_out, Write_En, Clk);
  Demultiplexer #(.Selector_Bits(4)) demultiplexer_1 (
    .sel(Reg_Dest), .in(and_1_out), .out_0(demultiplexer_1_out_0), .out_1(demultiplexer_1_out_1),
    .out_2(demultiplexer_1_out_2), .out_3(demultiplexer_1_out_3), .out_4(demultiplexer_1_out_4),
    .out_5(demultiplexer_1_out_5), .out_6(demultiplexer_1_out_6), .out_7(demultiplexer_1_out_7),
    .out_8(demultiplexer_1_out_8), .out_9(demultiplexer_1_out_9), .out_10(demultiplexer_1_out_10),
    .out_11(demultiplexer_1_out_11), .out_12(demultiplexer_1_out_12), .out_13(demultiplexer_1_out_13));  // open: out_14, out_15
  Comparator #(.Bits(4)) comparator_1 (.a(4'b1110), .b(Reg_Dest), .eq(comparator_1_eq));  // open: gt, lt
  Add #(.Bits(32)) add_1 (.a(R_15), .b(32'h2), .c_i(1'b0), .s(add_1_s));  // open: c_o
  Comparator #(.Bits(4)) comparator_2 (.a(4'b1111), .b(Reg_Dest), .eq(comparator_2_eq));  // open: gt, lt
  and and_2 (and_2_out, Write_En, comparator_1_eq);
  Multiplexer #(.Bits(32)) multiplexer_1 (.sel(and_2_out), .in_0(R_14), .in_1(Data_In), .out(multiplexer_1_out));
  assign and_3_out = Data_In & ~32'h1;  // And and_3, 32 bits wide
  and and_4 (and_4_out, Write_En, comparator_2_eq);
  or or_1 (or_1_out, and_4_out, ~PC_Hold);  // Or
  Multiplexer #(.Bits(32)) multiplexer_2 (.sel(and_4_out), .in_0(add_1_s), .in_1(and_3_out), .out(multiplexer_2_out));
  and and_5 (and_5_out, Clk, or_1_out);
  Multiplexer #(.Bits(32)) multiplexer_3 (
    .sel(Link), .in_0(multiplexer_1_out), .in_1(add_1_s), .out(multiplexer_3_out));
  D_FF_AS #(.Bits(32)) u_R_0 (.Set(1'b0), .D(Data_In), .C(demultiplexer_1_out_0), .Clr(Rst), .Q(R_0));  // open: nQ
  D_FF_AS #(.Bits(32)) u_R_1 (.Set(1'b0), .D(Data_In), .C(demultiplexer_1_out_1), .Clr(Rst), .Q(R_1));  // open: nQ
  D_FF_AS #(.Bits(32)) u_R_2 (.Set(1'b0), .D(Data_In), .C(demultiplexer_1_out_2), .Clr(Rst), .Q(R_2));  // open: nQ
  D_FF_AS #(.Bits(32)) u_R_3 (.Set(1'b0), .D(Data_In), .C(demultiplexer_1_out_3), .Clr(Rst), .Q(R_3));  // open: nQ
  D_FF_AS #(.Bits(32)) u_R_4 (.Set(1'b0), .D(Data_In), .C(demultiplexer_1_out_4), .Clr(Rst), .Q(R_4));  // open: nQ
  D_FF_AS #(.Bits(32)) u_R_5 (.Set(1'b0), .D(Data_In), .C(demultiplexer_1_out_5), .Clr(Rst), .Q(R_5));  // open: nQ
  D_FF_AS #(.Bits(32)) u_R_6 (.Set(1'b0), .D(Data_In), .C(demultiplexer_1_out_6), .Clr(Rst), .Q(R_6));  // open: nQ
  D_FF_AS #(.Bits(32)) u_R_7 (.Set(1'b0), .D(Data_In), .C(demultiplexer_1_out_7), .Clr(Rst), .Q(R_7));  // open: nQ
  D_FF_AS #(.Bits(32)) u_R_8 (.Set(1'b0), .D(Data_In), .C(demultiplexer_1_out_8), .Clr(Rst), .Q(R_8));  // open: nQ
  D_FF_AS #(.Bits(32)) u_R_9 (.Set(1'b0), .D(Data_In), .C(demultiplexer_1_out_9), .Clr(Rst), .Q(R_9));  // open: nQ
  D_FF_AS #(.Bits(32)) u_R_10 (.Set(1'b0), .D(Data_In), .C(demultiplexer_1_out_10), .Clr(Rst), .Q(R_10));  // open: nQ
  D_FF_AS #(.Bits(32)) u_R_11 (.Set(1'b0), .D(Data_In), .C(demultiplexer_1_out_11), .Clr(Rst), .Q(R_11));  // open: nQ
  D_FF_AS #(.Bits(32)) u_R_12 (.Set(1'b0), .D(Data_In), .C(demultiplexer_1_out_12), .Clr(Rst), .Q(R_12));  // open: nQ
  D_FF_AS #(.Bits(32)) R_SP (.Set(1'b0), .D(Data_In), .C(demultiplexer_1_out_13), .Clr(Rst), .Q(R_13));  // open: nQ
  D_FF_AS #(.Bits(32)) R_LR (.Set(1'b0), .D(multiplexer_3_out), .C(Clk), .Clr(Rst), .Q(R_14));  // open: nQ
  D_FF_AS #(.Bits(32), .Default(-2)) R_PC (
    .Set(1'b0), .D(multiplexer_2_out), .C(and_5_out), .Clr(Rst), .Q(R_15));  // open: nQ
  Register #(.Bits(32), .isProgramCounter("true")) PcReg (.D(multiplexer_2_out), .C(and_5_out), .en(1'b1));  // open: Q
  Multiplexer #(.Selector_Bits(4), .Bits(32)) multiplexer_4 (
    .sel(Reg_A), .in_0(R_0), .in_1(R_1), .in_2(R_2), .in_3(R_3), .in_4(R_4), .in_5(R_5), .in_6(R_6),
    .in_7(R_7), .in_8(R_8), .in_9(R_9), .in_10(R_10), .in_11(R_11), .in_12(R_12), .in_13(R_13), .in_14(R_14),
    .in_15(and_6_out), .out(A_Out));
  Add #(.Bits(32)) add_2 (.a(32'h4), .b(R_15), .c_i(1'b0), .s(add_2_s));  // open: c_o
  Multiplexer #(.Bits(32)) multiplexer_5 (.sel(Force_Word_Align), .in_0(32'h1), .in_1(32'h2), .out(multiplexer_5_out));
  assign and_6_out = add_2_s & ~multiplexer_5_out;  // And and_6, 32 bits wide
  Multiplexer #(.Selector_Bits(4), .Bits(32)) multiplexer_6 (
    .sel(Reg_B), .in_0(R_0), .in_1(R_1), .in_2(R_2), .in_3(R_3), .in_4(R_4), .in_5(R_5), .in_6(R_6),
    .in_7(R_7), .in_8(R_8), .in_9(R_9), .in_10(R_10), .in_11(R_11), .in_12(R_12), .in_13(R_13), .in_14(R_14),
    .in_15(and_6_out), .out(B_Out));
  Multiplexer #(.Selector_Bits(4), .Bits(32)) multiplexer_7 (
    .sel(Reg_Dest), .in_0(R_0), .in_1(R_1), .in_2(R_2), .in_3(R_3), .in_4(R_4), .in_5(R_5), .in_6(R_6),
    .in_7(R_7), .in_8(R_8), .in_9(R_9), .in_10(R_10), .in_11(R_11), .in_12(R_12), .in_13(R_13), .in_14(R_14),
    .in_15(and_6_out), .out(D_Out));

  // Notes on the sheet:
  //   Write_En: default 1
  //   Clk: default 1
endmodule
