// Digital circuit Conditional.dig as structural Verilog
module Conditional (
  input  Enable,
  input  [15:0] Instruction,
  input  Z,
  input  C,
  input  N,
  input  V,
  output Verified,
  output [10:0] Offset
);

  wire multiplexer_2_out, not_1_out, not_2_out, not_3_out, not_4_out, not_5_out, not_6_out, not_7_out,
       or_1_out, or_2_out, or_3_out, xor_1_out;
  wire [10:0] bitextender_1_out, multiplexer_1_out;

  xor xor_1 (xor_1_out, N, V);
  not not_1 (not_1_out, Z);
  not not_2 (not_2_out, C);
  not not_3 (not_3_out, N);
  not not_4 (not_4_out, V);
  or or_1 (or_1_out, ~C, Z);  // Or
  or or_2 (or_2_out, or_1_out, xor_1_out);
  BitExtender #(.outputBits(11)) bitextender_1 (.in(Instruction[7:0]), .out(bitextender_1_out));
  Multiplexer #(.Bits(11)) multiplexer_1 (
    .sel(Instruction[13]), .in_0(bitextender_1_out), .in_1(Instruction[10:0]), .out(multiplexer_1_out));
  not not_5 (not_5_out, or_1_out);
  not not_6 (not_6_out, xor_1_out);
  not not_7 (not_7_out, or_2_out);
  Multiplexer #(.Selector_Bits(4)) multiplexer_2 (
    .sel(Instruction[11:8]), .in_0(Z), .in_1(not_1_out), .in_2(C), .in_3(not_2_out), .in_4(N),
    .in_5(not_3_out), .in_6(V), .in_7(not_4_out), .in_8(not_5_out), .in_9(or_1_out), .in_10(not_6_out),
    .in_11(xor_1_out), .in_12(not_7_out), .in_13(or_2_out), .in_14(1'b1), .in_15(1'b0),
    .out(multiplexer_2_out));
  or or_3 (or_3_out, Instruction[13], multiplexer_2_out);
  assign Offset = Enable ? multiplexer_1_out : 11'bz;  // Driver driver_1
  assign Verified = Enable ? or_3_out : 1'bz;  // Driver driver_2
endmodule
