// Digital circuit Flags_APSR.dig as structural Verilog
module Flags_APSR (
  input  [3:0] Update_Mask,
  input  [3:0] Flags_In,
  input  Clk,
  input  Rst,
  output [3:0] Flags_Out
);

  wire [3:0] and_1_out, and_2_out, or_1_out;

  assign and_1_out = Flags_Out & ~Update_Mask;  // And and_1, 4 bits wide
  assign and_2_out = Update_Mask & Flags_In;  // And and_2, 4 bits wide
  assign or_1_out = and_1_out | and_2_out;  // Or or_1, 4 bits wide
  D_FF_AS #(.Bits(4)) Flags (.Set(1'b0), .D(or_1_out), .C(Clk), .Clr(Rst), .Q(Flags_Out));  // open: nQ
endmodule
