// Digital circuit Load_Address.dig as structural Verilog
module Load_Address (
  input  Enable,
  input  [15:0] Instruction,
  input  [31:0] Program_Counter,
  input  [31:0] Stack_Pointer,
  output Imm32_Enable,
  output [3:0] ALU_Opcode,
  output [31:0] Imm32,
  output [2:0] Rd
);

  wire [31:0] add_1_s, add_2_s, and_1_out, barrelshifter_1_out, multiplexer_1_out, neg_1_out;

  Add #(.Bits(32)) add_1 (.a(Program_Counter), .b(32'h4), .c_i(1'b0), .s(add_1_s));  // open: c_o
  assign Rd = Enable ? Instruction[10:8] : 3'bz;  // Driver driver_1
  BarrelShifter #(.Bits(32)) barrelshifter_1 (
    .in({{24{1'b0}}, Instruction[7:0]}), .shift(6'b000010), .out(barrelshifter_1_out));
  PullDown #(.Bits(3)) pulldown_1 (.out(Rd));
  assign and_1_out = add_1_s & ~32'h2;  // And and_1, 32 bits wide
  Multiplexer #(.Bits(32)) multiplexer_1 (
    .sel(Instruction[11]), .in_0(and_1_out), .in_1(Stack_Pointer), .out(multiplexer_1_out));
  assign ALU_Opcode = Enable ? 4'b1001 : 4'bz;  // Driver driver_2
  Add #(.Bits(32)) add_2 (.a(barrelshifter_1_out), .b(multiplexer_1_out), .c_i(1'b0), .s(add_2_s));  // open: c_o
  Neg #(.Bits(32)) neg_1 (.in(add_2_s), .out(neg_1_out));
  assign Imm32 = Enable ? neg_1_out : 32'bz;  // Driver driver_3

  assign Imm32_Enable = Enable;
endmodule
