// Digital circuit http.dig as structural Verilog
module http (
  input  clk
);

  wire counter_1_ovf, d_ff_as_1_q, d_ff_as_2_q, telnet_1_av, telnet_1_out;
  wire [6:0] counter_1_out;
  wire [7:0] rom_1_d;

  D_FF_AS d_ff_as_1 (.Set(1'b0), .D(1'b1), .C(telnet_1_av), .Clr(counter_1_ovf), .Q(d_ff_as_1_q));  // open: nQ
  Telnet #(.telnetEscape("false"), .port(4567)) telnet_1 (
    .in(rom_1_d), .C(clk), .wr(d_ff_as_2_q), .rd(1'b1), .out(telnet_1_out), .av(telnet_1_av));
  D_FF_AS d_ff_as_2 (.Set(1'b0), .D(d_ff_as_1_q), .C(~telnet_1_av), .Clr(counter_1_ovf), .Q(d_ff_as_2_q));  // open: nQ
  Counter #(.Bits(7)) counter_1 (.en(d_ff_as_2_q), .C(clk), .clr(1'b0), .out(counter_1_out), .ovf(counter_1_ovf));
  Terminal terminal_1 (.D(telnet_1_out), .C(clk), .en(telnet_1_av));
  ROM #(.AddrBits(7), .Bits(8)) rom_1 (.A(counter_1_out), .sel(1'b1), .D(rom_1_d));

  // Notes on the sheet:
  //   clk: Hz: 2147483647
  //   rom_1 loads rep_http.txt
endmodule
