// Digital circuit machine.dig as structural Verilog
module machine (
  input  clk,
  input  horl,
  input  clk_2
);

  wire ALU_Enable_Carry, ALU_Force_Carry, ALU_Neg, and_3_out, and_8_out, and_9_out, and_10_out, and_12_out,
       and_13_out, and_14_out, and_15_out, and_16_out, and_17_out, and_18_out, and_19_out, and_20_out,
       and_21_out, and_23_out, and_24_out, and_26_out, and_28_out, and_30_out, and_31_out, and_32_out,
       and_33_out, and_34_out, and_35_out, and_46_out, BL_1, BL_2, BreakReg_q, button_1_out, button_2_out,
       button_3_out, button_4_out, Clock, comparator_1_eq, comparator_2_eq, comparator_3_eq, comparator_4_eq,
       comparator_5_gt, comparator_6_gt, comparator_7_gt, comparator_8_gt, comparator_9_eq, comparator_11_eq,
       comparator_12_eq, conditional_1_verified, Continue, d_ff_1_q, d_ff_2_q, d_ff_3_q, d_ff_as_3_nq,
       d_ff_as_5_q, d_ff_as_7_q, d_ff_as_8_nq, d_ff_as_8_q, d_ff_as_9_nq, d_ff_as_9_q, decoder_2_out_0,
       decoder_2_out_1, delay_3_out, delay_4_out, delay_5_out, delay_6_out, demultiplexer_1_out_0,
       demultiplexer_1_out_1, demultiplexer_1_out_2, demultiplexer_1_out_12, demultiplexer_1_out_15,
       demultiplexer_2_out_0, demultiplexer_3_out_2, demultiplexer_4_out_0, demultiplexer_4_out_1, Disp_Buf,
       Disp_Clock, driver_116_out, driver_117_out, Fetch, Force_Word_Align, Imm5_En, Imm32_En, Instr_01_02,
       Instr_03, Instr_04, Instr_05, Instr_06, Instr_07_08, Instr_09, Instr_10, Instr_11, Instr_12, Instr_13,
       Instr_14_4, Instr_14_9, Instr_14_Delay, Instr_16, Instr_18, Instr_19, Instr_Cond, Instr_Ldm,
       Instr_Pop, Instr_Push, Instr_SignEx, Instr_Stm, Keyb_Read, Link, Load, Load_Req, Mem_Area_Disp,
       Mem_Area_Mmio, Mem_Area_Ram, Mem_Area_Rom, Mem_Signed, Mem_Signed_Real, Midi_Note, Midi_On, Midi_Prog,
       Midi_Vol, Mmio_Clock, multiplexer_3_out, not_2_out, not_3_out, not_4_out, not_5_out, not_6_out,
       not_7_out, not_8_out, not_10_out, not_11_out, not_12_out, not_13_out, not_14_out, not_16_out,
       or_3_out, or_4_out, or_5_out, or_6_out, or_7_out, or_8_out, or_9_out, or_10_out, or_11_out, or_12_out,
       or_13_out, PC_Fetch_Anyway, PC_Hold, PC_Hold_Manual, PC_Hold_Still, PP_Active, PP_DoingStuff,
       PP_Finished, PP_Upd_SP, priorityencoder_1_any, Ram_Clock, Reg_WEn, register_4_q, Rng_Read, Store,
       Store_Req, Telnet_Av, Telnet_Read, TelnetBuf_Av, TelnetBuf_IsFull, TelnetData_Read, xor_1_out,
       xor_2_out;
  wire [0:0] keyboard_1_av;
  wire [1:0] Mem_Area, Mem_Mode, Mem_Mode_Real, multiplexer_2_out, multiplexer_4_out, multiplexer_12_out;
  wire [1:1] not_1_out;
  wire [3:0] add_6_s, ALU_Cod_Op, ALU_Out_Flags, Flags, Flags_Mask, lotohi_1_out, lotohi_2_out, lotohi_3_out,
       lotohi_4_out, lotohi_5_out, lotohi_6_out, lotohi_7_out, lotohi_8_out, lotohi_9_out, lotohi_10_out,
       lotohi_11_out, lotohi_12_out, lotohi_13_out, lotohi_14_out, lotohi_15_out, lotohi_16_out,
       lotohi_17_out, lotohi_18_out, lotohi_19_out, lotohi_20_out, multiplexer_1_out, multiplexer_5_out,
       multiplexer_6_out, multiplexer_7_out, multiplexer_9_out, multiplexer_16_out, multiplexer_17_out,
       multiplexer_18_out, multiplexer_29_out, multiplexer_30_out, PP_Addr, PP_Counter, PP_Queue_Msb,
       PP_Real_Reg, PP_Reglist_Cnt, priorityencoder_1_num, Reg_A, Reg_B, Reg_W, sub_2_s;
  wire [3:3] and_7_out;
  wire [4:0] Imm5, multiplexer_20_out;
  wire [6:0] multiplexer_15_out, register_2_q, register_3_q;
  wire [7:0] Telnet_Out, TelnetBuf_RdData;
  wire [8:0] and_6_out, barrelshifter_1_out, multiplexer_11_out, PP_Queue;
  wire [10:0] conditional_1_offset;
  wire [14:0] counter_2_out;
  wire [15:0] Instr, keyboard_1_d;
  wire [19:0] TelnetBuf_Len_out;
  wire [23:0] counter_3_out, TelnetBuf_RdPos_out, TelnetBuf_WrPos_out;
  wire [23:15] counter_2_out_2;
  wire [31:0] add_1_s, add_2_s, add_3_s, add_4_s, add_7_s, add_7_s_2, ALU_Out, barrelshifter_2_out,
       bcd_1_out, bitextender_2_out, bitextender_3_out, bitextender_4_out, bitextender_6_out,
       bitextender_7_out, Code_Addr, counter_1_out, d_ff_4_q, Data_Addr, div_1_q, div_1_r, div_2_q, div_2_r,
       Imm32, Mem_Addr, Mem_In, Mem_Out, Mem_Out_Raw, Mem_Out_Raw_Whole, Mmio_Out, mul_2_mul, mul_3_mul,
       multiplexer_8_out, multiplexer_10_out, multiplexer_21_out, multiplexer_22_out, multiplexer_23_out,
       multiplexer_24_out, multiplexer_28_out, multiplexer_34_out, notconnected_1_out, notconnected_2_out,
       notconnected_3_out, notconnected_4_out, notconnected_5_out, notconnected_6_out, notconnected_7_out,
       notconnected_8_out, notconnected_9_out, notconnected_10_out, notconnected_11_out, notconnected_12_out,
       notconnected_13_out, notconnected_14_out, notconnected_15_out, notconnected_16_out, prng_1_r, Ram_Out,
       Reg_0, Reg_1, Reg_2, Reg_3, Reg_Lr, Reg_Sp, Reg_Val, register_1_q, RegVal_A, RegVal_B, Res_q, Rom_Out,
       sub_3_s, sub_4_s;
  wire [31:8] bitextender_5_out;
  wire [31:12] bitextender_1_out;
  wire [63:0] mul_1_mul;
  wire [63:32] add_5_s, mul_2_mul_2, mul_3_mul_2;

  D_FF_AS d_ff_as_1 (.Set(1'b0), .D(Instr_14_4), .C(~Clock), .Clr(1'b0), .Q(Instr_14_Delay));  // open: nQ
  and and_1 (BL_2, Instr[11], Instr_19);
  and and_2 (BL_1, ~Instr[11], Instr_19);  // And
  or or_1 (Instr_Cond, Instr_16, Instr_18);
  BitExtender #(.inputBits(11), .outputBits(20)) bitextender_1 (.in(Instr[10:0]), .out(bitextender_1_out));
  BitExtender #(.inputBits(16), .outputBits(32)) bitextender_2 (.in(RegVal_A[15:0]), .out(bitextender_2_out));
  BitExtender #(.outputBits(32)) bitextender_3 (.in(RegVal_A[7:0]), .out(bitextender_3_out));
  BarrelShifter #(.Bits(9)) barrelshifter_1 (.in(9'h1), .shift(PP_Queue_Msb), .out(barrelshifter_1_out));
  PullDown pulldown_1 (.out(PC_Hold_Manual));
  Multiplexer #(.Bits(4)) multiplexer_1 (.sel(Instr[9]), .in_0(4'b0101), .in_1(4'b0110), .out(multiplexer_1_out));
  and and_3 (and_3_out, ~Instr[11], ~Instr[12]);  // And
  Multiplexer #(.Selector_Bits(4), .Bits(2)) multiplexer_2 (
    .sel(Instr[9:6]), .in_0(2'b01), .in_1(2'b01), .in_2(2'b01), .in_3(2'b01), .in_4(2'b01), .in_5(2'b11),
    .in_6(2'b11), .in_7(2'b01), .in_8(2'b01), .in_9(2'b11), .in_10(2'b11), .in_11(2'b11), .in_12(2'b01),
    .in_13(2'b00), .in_14(2'b01), .in_15(2'b01), .out(multiplexer_2_out));
  Multiplexer #(.Selector_Bits(3)) multiplexer_3 (
    .sel(Instr[11:9]), .in_0(1'b0), .in_1(1'b0), .in_2(1'b0), .in_3(1'b1), .in_4(1'b1), .in_5(1'b1),
    .in_6(1'b1), .in_7(1'b1), .out(multiplexer_3_out));
  Multiplexer #(.Selector_Bits(3), .Bits(2)) multiplexer_4 (
    .sel(Instr[11:9]), .in_0(2'b00), .in_1(2'b01), .in_2(2'b10), .in_3(2'b10), .in_4(2'b00), .in_5(2'b01),
    .in_6(2'b10), .in_7(2'b01), .out(multiplexer_4_out));
  LoToHi lotohi_1 (.Reg(Instr[2:0]), .Out(lotohi_1_out));
  LoToHi lotohi_2 (.Reg(Instr[5:3]), .Out(lotohi_2_out));
  LoToHi lotohi_3 (.Reg(Instr[10:8]), .Out(lotohi_3_out));
  LoToHi lotohi_4 (.Reg(Instr[2:0]), .Out(lotohi_4_out));
  LoToHi lotohi_5 (.Reg(Instr[5:3]), .Out(lotohi_5_out));
  Add #(.Bits(32)) add_1 (.a({bitextender_1_out, 12'h1}), .b(Code_Addr), .c_i(1'b1), .s(add_1_s));  // open: c_o
  Add #(.Bits(32)) add_2 (.a({{20{1'b0}}, Instr[10:0], 1'b1}), .b(Reg_Lr), .c_i(1'b1), .s(add_2_s));  // open: c_o
  and and_4 (Instr_Pop, Instr[11], Instr_14_Delay);
  and and_5 (Instr_Push, ~Instr[11], Instr_14_Delay);  // And
  assign and_6_out = PP_Queue & ~barrelshifter_1_out;  // And and_6, 9 bits wide
  // Probe on barrelshifter_1_out
  Comparator #(.Bits(32)) comparator_1 (.a(Mem_Addr), .b(32'h7ffe28ff), .eq(comparator_1_eq));  // open: gt, lt
  or or_2 (PC_Hold, Load, PC_Hold_Manual, Store);
  assign Flags_Mask = Instr_01_02 ? {3'b111, Instr[9]} : 4'bz;  // Driver driver_1
  Multiplexer #(.Selector_Bits(2), .Bits(4)) multiplexer_5 (
    .sel(Instr[12:11]), .in_0(4'b0010), .in_1(4'b0011), .in_2(4'b0100), .in_3(multiplexer_1_out),
    .out(multiplexer_5_out));
  LoToHi lotohi_6 (.Reg(Instr[2:0]), .Out(lotohi_6_out));
  LoToHi lotohi_7 (.Reg(Instr[5:3]), .Out(lotohi_7_out));
  LoToHi lotohi_8 (.Reg(Instr[8:6]), .Out(lotohi_8_out));
  not not_1 (not_1_out[1], and_3_out);
  Multiplexer #(.Selector_Bits(2), .Bits(4)) multiplexer_6 (
    .sel(Instr[12:11]), .in_0(4'b1001), .in_1(4'b1010), .in_2(4'b0101), .in_3(4'b0110),
    .out(multiplexer_6_out));
  and and_7 (and_7_out[3], Instr[8], ~Instr[9]);  // And
  Multiplexer #(.Selector_Bits(2), .Bits(4)) multiplexer_7 (
    .sel(Instr[9:8]), .in_0(4'b0101), .in_1(4'b1010), .in_2(4'b1001), .in_3(4'b1001), .out(multiplexer_7_out));
  LoToHi lotohi_9 (.Reg(Instr[10:8]), .Out(lotohi_9_out));
  LoToHi lotohi_10 (.Reg(Instr[2:0]), .Out(lotohi_10_out));
  LoToHi lotohi_11 (.Reg(Instr[5:3]), .Out(lotohi_11_out));
  LoToHi lotohi_12 (.Reg(Instr[8:6]), .Out(lotohi_12_out));
  not not_2 (not_2_out, multiplexer_3_out);
  Multiplexer #(.Bits(32)) multiplexer_8 (
    .sel(Instr[12]), .in_0({{25{1'b0}}, Instr[10:6], 2'b00}), .in_1({{27{1'b0}}, Instr[10:6]}),
    .out(multiplexer_8_out));
  Multiplexer #(.Bits(4)) multiplexer_9 (.sel(Instr[11]), .in_0(4'b1111), .in_1(4'b1101), .out(multiplexer_9_out));
  Multiplexer #(.Selector_Bits(2), .Bits(32)) multiplexer_10 (
    .sel(Instr[7:6]), .in_0(bitextender_2_out), .in_1(bitextender_3_out),
    .in_2({{16{1'b0}}, RegVal_A[15:0]}), .in_3({{24{1'b0}}, RegVal_A[7:0]}), .out(multiplexer_10_out));
  Conditional conditional_1 (
    .Enable(Instr_Cond), .Instruction(Instr), .Z(Flags[2]), .C(Flags[1]), .N(Flags[3]), .V(Flags[0]),
    .Verified(conditional_1_verified), .Offset(conditional_1_offset));
  D_FF_AS d_ff_as_2 (.Set(1'b0), .D(1'b1), .C(Instr_14_Delay), .Clr(PP_Finished), .Q(PP_Active));  // open: nQ
  not not_3 (not_3_out, PP_Finished);
  Multiplexer #(.Bits(9)) multiplexer_11 (
    .sel(PP_DoingStuff), .in_0(Instr[8:0]), .in_1(and_6_out), .out(multiplexer_11_out));
  Comparator #(.Bits(32)) comparator_2 (.a(Code_Addr), .b(32'h208d612), .eq(comparator_2_eq));  // open: gt, lt
  Comparator #(.Bits(32)) comparator_3 (.a(Code_Addr), .b(32'h180ecff), .eq(comparator_3_eq));  // open: gt, lt
  and and_8 (and_8_out, comparator_1_eq, Store);
  PullDown pulldown_2 (.out(PC_Hold));
  assign Reg_WEn = Instr_01_02 ? 1'b1 : 1'bz;  // Driver driver_2
  assign ALU_Cod_Op = Instr_01_02 ? multiplexer_5_out : 4'bz;  // Driver driver_3
  assign Reg_W = Instr_01_02 ? lotohi_6_out : 4'bz;  // Driver driver_4
  assign Reg_A = Instr_01_02 ? lotohi_7_out : 4'bz;  // Driver driver_5
  assign Reg_B = Instr_01_02 ? lotohi_8_out : 4'bz;  // Driver driver_6
  assign Reg_WEn = Instr_03 ? 1'b1 : 1'bz;  // Driver driver_7
  assign ALU_Cod_Op = Instr_03 ? multiplexer_6_out : 4'bz;  // Driver driver_8
  assign Reg_WEn = Instr_04 ? 1'b1 : 1'bz;  // Driver driver_9
  assign ALU_Cod_Op = Instr_04 ? Instr[9:6] : 4'bz;  // Driver driver_10
  assign Flags_Mask = Instr_04 ? {2'b11, multiplexer_2_out} : 4'bz;  // Driver driver_11
  assign Reg_WEn = Instr_05 ? 1'b1 : 1'bz;  // Driver driver_12
  assign ALU_Cod_Op = Instr_05 ? multiplexer_7_out : 4'bz;  // Driver driver_13
  assign Reg_W = Instr_07_08 ? lotohi_10_out : 4'bz;  // Driver driver_14
  assign Reg_A = Instr_07_08 ? lotohi_11_out : 4'bz;  // Driver driver_15
  assign Reg_B = Instr_07_08 ? lotohi_12_out : 4'bz;  // Driver driver_16
  assign Store_Req = Instr_07_08 ? not_2_out : 1'bz;  // Driver driver_17
  assign Load_Req = Instr_07_08 ? multiplexer_3_out : 1'bz;  // Driver driver_18
  assign Mem_Mode = Instr_07_08 ? multiplexer_4_out : 2'bz;  // Driver driver_19
  assign Reg_W = Instr_09 ? lotohi_1_out : 4'bz;  // Driver driver_20
  assign Reg_A = Instr_09 ? lotohi_2_out : 4'bz;  // Driver driver_21
  Multiplexer #(.Bits(2)) multiplexer_12 (.sel(Instr[12]), .in_0(2'b00), .in_1(2'b10), .out(multiplexer_12_out));
  not not_4 (not_4_out, Instr[11]);
  assign Imm32 = Instr_12 ? {{22{1'b0}}, Instr[7:0], 2'b00} : 32'bz;  // Driver driver_22
  assign Reg_W = Instr_12 ? lotohi_3_out : 4'bz;  // Driver driver_23
  assign Reg_A = Instr_12 ? multiplexer_9_out : 4'bz;  // Driver driver_24
  assign Imm32_En = Instr_12 ? 1'b1 : 1'bz;  // Driver driver_25
  assign Reg_WEn = Instr_12 ? 1'b1 : 1'bz;  // Driver driver_26
  assign ALU_Cod_Op = Instr_12 ? 4'b0101 : 4'bz;  // Driver driver_27
  assign Force_Word_Align = Instr_12 ? 1'b1 : 1'bz;  // Driver driver_28
  assign Reg_W = Instr_SignEx ? lotohi_4_out : 4'bz;  // Driver driver_29
  assign Reg_A = Instr_SignEx ? lotohi_5_out : 4'bz;  // Driver driver_30
  BitExtender #(.inputBits(11), .outputBits(32)) bitextender_4 (.in(conditional_1_offset), .out(bitextender_4_out));
  D_FF_AS d_ff_as_3 (.Set(1'b0), .D(d_ff_as_3_nq), .C(PP_Active), .Clr(d_ff_2_q), .Q(PP_Upd_SP), .nQ(d_ff_as_3_nq));
  not not_5 (not_5_out, TelnetBuf_IsFull);
  and and_9 (and_9_out, not_5_out, Telnet_Av);
  Register #(.Bits(32)) register_1 (.D(Reg_Lr), .C(button_1_out), .en(1'b1), .Q(register_1_q));
  Button button_1 (.out(button_1_out));
  or or_3 (or_3_out, comparator_2_eq, and_8_out, comparator_3_eq);
  // Probe PC_Hold on PC_Hold
  PullDown pulldown_3 (.out(PC_Fetch_Anyway));
  or or_4 (or_4_out, PC_Fetch_Anyway, ~PC_Hold);  // Or
  Multiplexer #(.Bits(5)) multiplexer_13 (
    .sel(Instr[12]), .in_0(Instr[10:6]), .in_1({2'b00, Instr[8:6]}));  // open: out
  assign Flags_Mask = Instr_03 ? {2'b11, {2{not_1_out[1]}}} : 4'bz;  // Driver driver_31
  assign Flags_Mask = Instr_05 ? {4{and_7_out[3]}} : 4'bz;  // Driver driver_32
  assign Imm32 = Instr_06 ? {{22{1'b0}}, Instr[7:0], 2'b00} : 32'bz;  // Driver driver_33
  assign Reg_W = Instr_06 ? lotohi_9_out : 4'bz;  // Driver driver_34
  assign Imm32_En = Instr_06 ? 1'b1 : 1'bz;  // Driver driver_35
  assign Load_Req = Instr_06 ? 1'b1 : 1'bz;  // Driver driver_36
  assign Reg_A = Instr_06 ? 4'b1111 : 4'bz;  // Driver driver_37
  assign Force_Word_Align = Instr_06 ? 1'b1 : 1'bz;  // Driver driver_38
  assign Imm32 = Instr_09 ? multiplexer_8_out : 32'bz;  // Driver driver_39
  assign Mem_Mode = Instr_09 ? multiplexer_12_out : 2'bz;  // Driver driver_40
  assign Store_Req = Instr_09 ? not_4_out : 1'bz;  // Driver driver_41
  assign Load_Req = Instr_09 ? Instr[11] : 1'bz;  // Driver driver_42
  assign Imm32_En = Instr_09 ? 1'b1 : 1'bz;  // Driver driver_43
  assign Imm32 = Instr_SignEx ? multiplexer_10_out : 32'bz;  // Driver driver_44
  Add #(.Bits(32)) add_3 (.a(bitextender_4_out), .b(32'h2), .c_i(1'b0), .s(add_3_s));  // open: c_o
  BarrelShifter #(.Bits(32), .barrelSigned("true")) barrelshifter_2 (
    .in(add_3_s), .shift(7'b0000001), .out(barrelshifter_2_out));
  Add #(.Bits(32)) add_4 (.a(barrelshifter_2_out), .b(Code_Addr), .c_i(1'b0), .s(add_4_s));  // open: c_o
  assign Imm32 = BL_1 ? add_1_s : 32'bz;  // Driver driver_45
  assign Reg_W = BL_1 ? 4'b1110 : 4'bz;  // Driver driver_46
  assign Link = BL_2 ? 1'b1 : 1'bz;  // Driver driver_47
  assign Reg_W = BL_2 ? 4'b1111 : 4'bz;  // Driver driver_48
  assign Imm32 = BL_2 ? add_2_s : 32'bz;  // Driver driver_49
  assign PC_Hold_Manual = PP_Active ? 1'b1 : 1'bz;  // Driver driver_50
  D_FF_AS #(.Bits(9)) d_ff_as_4 (
    .Set(1'b0), .D(multiplexer_11_out), .C(~Clock), .Clr(~not_3_out), .Q(PP_Queue));  // open: nQ
  and and_10 (and_10_out, TelnetData_Read, TelnetBuf_Av);
  PullDown pulldown_4 (.out(Reg_WEn));
  and and_11 (Fetch, Clock, or_4_out);
  and and_12 (and_12_out, Instr[9], Instr[10]);
  assign Imm32 = Instr_Cond ? add_4_s : 32'bz;  // Driver driver_51
  // Probe on PP_Queue
  xor xor_1 (xor_1_out, and_10_out, and_9_out);
  and and_13 (and_13_out, Mem_Area_Mmio, Store);
  D_FF d_ff_1 (.D(1'b1), .C(button_1_out), .Q(d_ff_1_q));  // open: nQ
  Comparator #(.Bits(32)) comparator_4 (.a(Code_Addr), .b(register_1_q), .eq(comparator_4_eq));  // open: gt, lt
  Register #(.Bits(7)) register_2 (.D(Mem_In[6:0]), .C(Mmio_Clock), .en(Midi_Note), .Q(register_2_q));
  Register #(.Bits(7)) register_3 (.D(Mem_In[6:0]), .C(Mmio_Clock), .en(Midi_Vol), .Q(register_3_q));
  Register register_4 (.D(Mem_In[0]), .C(Mmio_Clock), .en(Midi_On), .Q(register_4_q));
  PullDown #(.Bits(4)) pulldown_5 (.out(Reg_B));
  LoToHi lotohi_13 (.Reg(Instr[2:0]), .Out(lotohi_13_out));
  LoToHi lotohi_14 (.Reg(Instr[5:3]), .Out(lotohi_14_out));
  PullDown pulldown_6 (.out(conditional_1_verified));
  Demultiplexer #(.Selector_Bits(5)) demultiplexer_1 (
    .sel(Mem_Addr[6:2]), .in(and_13_out), .out_0(demultiplexer_1_out_0), .out_1(demultiplexer_1_out_1),
    .out_2(demultiplexer_1_out_2), .out_3(Midi_Note), .out_4(Midi_Vol), .out_5(Midi_On), .out_6(Midi_Prog),
    .out_12(demultiplexer_1_out_12), .out_15(demultiplexer_1_out_15));  // open: out_7, out_8, out_9, out_10, out_11, out_13, out_14, out_16, out_17, out_18, out_19, out_20, out_21, out_22, out_23, out_24, out_25, out_26, out_27, out_28, out_29, out_30, out_31
  and and_14 (and_14_out, d_ff_1_q, comparator_4_eq);
  Comparator #(.Bits(32)) comparator_5 (.a(Mem_Addr), .b(32'hffffff), .gt(comparator_5_gt));  // open: eq, lt
  Comparator #(.Bits(32)) comparator_6 (.a(Mem_Addr), .b(32'hffdfffff), .gt(comparator_6_gt));  // open: eq, lt
  Comparator #(.Bits(32)) comparator_7 (.a(Mem_Addr), .b(32'hfffffeff), .gt(comparator_7_gt));  // open: eq, lt
  PullDown #(.Bits(4)) pulldown_7 (.out(Reg_A));
  PullDown #(.Bits(32)) pulldown_8 (.out(Data_Addr));
  Multiplexer #(.Bits(32)) multiplexer_14 (.sel(Fetch), .in_0(Data_Addr), .in_1(Code_Addr), .out(Mem_Addr));
  and and_15 (and_15_out, Instr[11], Instr[12]);
  and and_16 (and_16_out, Instr[10], Instr[11], Instr[12]);
  and and_17 (and_17_out, Instr[9], Instr[11], Instr[12]);
  and and_18 (and_18_out, Instr[11], Instr[12]);
  and and_19 (and_19_out, ~Instr[11], ~Instr[12]);  // And
  LoToHi lotohi_15 (.Reg(Instr[10:8]), .Out(lotohi_15_out));
  and and_20 (and_20_out, Instr[8], Instr[9]);
  assign Mem_Signed = Instr_07_08 ? and_12_out : 1'bz;  // Driver driver_52
  assign ALU_Neg = Instr_SignEx ? 1'b1 : 1'bz;  // Driver driver_53
  assign Imm32_En = Instr_SignEx ? 1'b1 : 1'bz;  // Driver driver_54
  assign Reg_WEn = Instr_SignEx ? 1'b1 : 1'bz;  // Driver driver_55
  assign ALU_Cod_Op = Instr_SignEx ? 4'b1001 : 4'bz;  // Driver driver_56
  assign ALU_Neg = Instr_Cond ? 1'b1 : 1'bz;  // Driver driver_57
  assign Imm32_En = Instr_Cond ? 1'b1 : 1'bz;  // Driver driver_58
  assign Reg_WEn = Instr_Cond ? conditional_1_verified : 1'bz;  // Driver driver_59
  assign ALU_Cod_Op = Instr_Cond ? 4'b1001 : 4'bz;  // Driver driver_60
  assign Reg_W = conditional_1_verified ? 4'b1111 : 4'bz;  // Driver driver_61
  assign ALU_Neg = Instr_19 ? 1'b1 : 1'bz;  // Driver driver_62
  assign Imm32_En = Instr_19 ? 1'b1 : 1'bz;  // Driver driver_63
  assign Reg_WEn = Instr_19 ? 1'b1 : 1'bz;  // Driver driver_64
  assign ALU_Cod_Op = Instr_19 ? 4'b1001 : 4'bz;  // Driver driver_65
  BitCount #(.Bits(9)) bitcount_1 (.in(Instr[8:0]), .out(PP_Reglist_Cnt));
  D_FF_AS d_ff_as_5 (.Set(1'b0), .D(PP_Upd_SP), .C(Clock), .Clr(1'b0), .Q(d_ff_as_5_q));  // open: nQ
  D_FF d_ff_2 (.D(d_ff_as_5_q), .C(~Clock), .Q(d_ff_2_q));  // open: nQ
  D_FF_AS d_ff_as_6 (.Set(d_ff_2_q), .D(1'b0), .C(1'b0), .Clr(PP_Finished), .Q(PP_DoingStuff));  // open: nQ
  PriorityEncoder #(.Selector_Bits(4)) priorityencoder_1 (
    .in0(PP_Queue[8]), .in1(PP_Queue[7]), .in2(PP_Queue[6]), .in3(PP_Queue[5]), .in4(PP_Queue[4]),
    .in5(PP_Queue[3]), .in6(PP_Queue[2]), .in7(PP_Queue[1]), .in8(PP_Queue[0]), .in9(1'b0), .in10(1'b0),
    .in11(1'b0), .in12(1'b0), .in13(1'b0), .in14(1'b0), .in15(1'b0), .num(priorityencoder_1_num),
    .any(priorityencoder_1_any));
  CounterPreset #(.Bits(20)) TelnetBuf_Len (
    .en(xor_1_out), .C(Clock), .dir(and_10_out), .in({20{1'b0}}), .ld(1'b0), .clr(1'b0),
    .out(TelnetBuf_Len_out), .ovf(TelnetBuf_IsFull));
  or or_5 (or_5_out, and_14_out, demultiplexer_1_out_15, or_3_out);
  Multiplexer #(.Bits(7)) multiplexer_15 (
    .sel(Midi_Prog), .in_0(register_2_q), .in_1(Mem_In[6:0]), .out(multiplexer_15_out));
  PullDown #(.Bits(4)) pulldown_9 (.out(Reg_W));
  or or_6 (or_6_out, PC_Hold_Still, PC_Hold);
  PullDown pulldown_10 (.out(Force_Word_Align));
  // Probe on Code_Addr
  Register #(.Bits(16)) u_Instr (.D(Mem_Out[15:0]), .C(~Fetch), .en(1'b1), .Q(Instr));
  not not_6 (not_6_out, and_15_out);
  assign ALU_Force_Carry = Instr_03 ? and_18_out : 1'bz;  // Driver driver_66
  assign Imm32_En = Instr_03 ? 1'b1 : 1'bz;  // Driver driver_67
  assign Imm32 = Instr_03 ? {{24{1'b0}}, Instr[7:0]} : 32'bz;  // Driver driver_68
  assign ALU_Neg = Instr_03 ? and_19_out : 1'bz;  // Driver driver_69
  assign Reg_W = Instr_03 ? lotohi_15_out : 4'bz;  // Driver driver_70
  assign Reg_A = Instr_03 ? lotohi_15_out : 4'bz;  // Driver driver_71
  assign Reg_A = Instr_04 ? lotohi_13_out : 4'bz;  // Driver driver_72
  assign Reg_W = Instr_04 ? lotohi_13_out : 4'bz;  // Driver driver_73
  assign Reg_B = Instr_04 ? lotohi_14_out : 4'bz;  // Driver driver_74
  assign ALU_Enable_Carry = Instr_04 ? 1'b1 : 1'bz;  // Driver driver_75
  and and_21 (and_21_out, Instr[7], and_20_out);
  Multiplexer #(.Bits(4)) multiplexer_16 (.sel(Instr[7]), .in_0(4'b0101), .in_1(4'b0110), .out(multiplexer_16_out));
  and and_22 (PC_Hold_Still, Instr_14_4, Instr[8], ~PP_Active, Instr_Pop);  // And
  // Probe on priorityencoder_1_num
  not not_7 (not_7_out, priorityencoder_1_any);
  Counter #(.Bits(24)) TelnetBuf_WrPos (.en(and_9_out), .C(Clock), .clr(1'b0), .out(TelnetBuf_WrPos_out));  // open: ovf
  PullDown pulldown_11 (.out(Link));
  and and_23 (and_23_out, not_6_out, Instr_01_02);
  assign Imm5 = and_23_out ? Instr[10:6] : 5'bz;  // Driver driver_76
  and and_24 (and_24_out, and_16_out, Instr_01_02);
  assign Imm32 = and_24_out ? {{29{1'b0}}, Instr[8:6]} : 32'bz;  // Driver driver_77
  assign ALU_Force_Carry = Instr_01_02 ? and_17_out : 1'bz;  // Driver driver_78
  Multiplexer #(.Bits(4)) multiplexer_17 (
    .sel(and_20_out), .in_0({Instr[7], Instr[2:0]}), .in_1(4'b1111), .out(multiplexer_17_out));
  LoToHi lotohi_16 (.Reg(Instr[10:8]), .Out(lotohi_16_out));
  LoToHi lotohi_17 (.Reg(Instr[2:0]), .Out(lotohi_17_out));
  LoToHi lotohi_18 (.Reg(Instr[5:3]), .Out(lotohi_18_out));
  not not_8 (not_8_out, Instr[11]);
  Sub #(.Bits(4)) sub_1 (.a(4'b1000), .b(priorityencoder_1_num), .c_i(1'b0), .s(PP_Queue_Msb));  // open: c_o
  Comparator #(.Bits(4)) comparator_8 (.a(PP_Counter), .b(4'b0000), .gt(comparator_8_gt));  // open: eq, lt
  Comparator #(.Bits(20)) comparator_9 (.a({20{1'b0}}), .b(TelnetBuf_Len_out), .eq(comparator_9_eq));  // open: gt, lt
  Counter #(.Bits(24)) TelnetBuf_RdPos (
    .en(and_10_out), .C(Clock), .clr(1'b0), .out(TelnetBuf_RdPos_out));  // open: ovf
  Telnet #(.telnetEscape("false"), .port(4567), .telnetBufferSize(1048576)) telnet_1 (
    .in(Mem_In[7:0]), .C(Clock), .wr(demultiplexer_1_out_2), .rd(Telnet_Av), .out(Telnet_Out), .av(Telnet_Av));
  Register register_5 (.D(Mem_In[0]), .C(Mmio_Clock), .en(demultiplexer_1_out_12), .Q(Disp_Buf));
  Mul #(.Bits(32)) mul_1 (.a(Reg_0), .b(Reg_2), .mul(mul_1_mul));
  Mul #(.Bits(32)) mul_2 (.a(Reg_1), .b(Reg_2), .mul({mul_2_mul_2, mul_2_mul}));
  Mul #(.Bits(32)) mul_3 (.a(Reg_0), .b(Reg_3), .mul({mul_3_mul_2, mul_3_mul}));
  D_FF d_ff_3 (.D(1'b0), .C(1'b0), .Q(d_ff_3_q));  // open: nQ
  D_FF_AS BreakReg (.Set(button_2_out), .D(1'b1), .C(or_5_out), .Clr(button_3_out), .Q(BreakReg_q));  // open: nQ
  Button button_2 (.out(button_2_out));
  Button button_3 (.out(button_3_out));
  D_FF_AS d_ff_as_7 (.Set(1'b0), .D(Midi_On), .C(~Mmio_Clock), .Clr(~Midi_On), .Q(d_ff_as_7_q));  // open: nQ
  PriorityEncoder #(.Selector_Bits(2)) priorityencoder_2 (
    .in0(1'b1), .in1(comparator_5_gt), .in2(comparator_6_gt), .in3(comparator_7_gt), .num(Mem_Area));  // open: any
  Decoder #(.Selector_Bits(2)) decoder_1 (
    .sel(Mem_Area), .out_0(Mem_Area_Rom), .out_1(Mem_Area_Ram), .out_2(Mem_Area_Disp), .out_3(Mem_Area_Mmio));
  BancDeRegistres bancderegistres_1 (
    .Data_In(Reg_Val), .Reg_Dest(Reg_W), .Write_En(Reg_WEn), .Rst(1'b0), .Reg_B(Reg_B), .Reg_A(Reg_A),
    .Clk(Clock), .Link(Link), .PC_Hold(or_6_out), .Force_Word_Align(Force_Word_Align), .A_Out(RegVal_A),
    .B_Out(RegVal_B), .R_0(Reg_0), .R_1(Reg_1), .R_2(Reg_2), .R_3(Reg_3), .R_13(Reg_Sp), .R_14(Reg_Lr),
    .R_15(Code_Addr), .D_Out(Mem_In));  // open: R_4, R_5, R_6, R_7, R_8, R_9, R_10, R_11, R_12
  // Probe on Instr
  assign Imm5_En = Instr_01_02 ? not_6_out : 1'bz;  // Driver driver_79
  assign Imm32_En = Instr_01_02 ? and_16_out : 1'bz;  // Driver driver_80
  assign Link = Instr_05 ? and_21_out : 1'bz;  // Driver driver_81
  assign ALU_Neg = Instr_05 ? Instr[9] : 1'bz;  // Driver driver_82
  assign Reg_W = Instr_05 ? multiplexer_17_out : 4'bz;  // Driver driver_83
  assign Reg_A = Instr_05 ? multiplexer_17_out : 4'bz;  // Driver driver_84
  assign Reg_B = Instr_05 ? Instr[6:3] : 4'bz;  // Driver driver_85
  Decoder decoder_2 (.sel(Instr[11]), .out_0(decoder_2_out_0), .out_1(decoder_2_out_1));
  assign Reg_W = Instr_10 ? lotohi_17_out : 4'bz;  // Driver driver_86
  assign Reg_A = Instr_10 ? lotohi_18_out : 4'bz;  // Driver driver_87
  assign Imm32 = Instr_10 ? {{26{1'b0}}, Instr[10:6], 1'b0} : 32'bz;  // Driver driver_88
  assign Store_Req = Instr_10 ? not_8_out : 1'bz;  // Driver driver_89
  assign Load_Req = Instr_10 ? Instr[11] : 1'bz;  // Driver driver_90
  assign Imm32_En = Instr_10 ? 1'b1 : 1'bz;  // Driver driver_91
  assign Mem_Mode = Instr_10 ? 2'b01 : 2'bz;  // Driver driver_92
  assign Imm32 = Instr_13 ? {{23{1'b0}}, Instr[6:0], 2'b00} : 32'bz;  // Driver driver_93
  assign Reg_W = Instr_13 ? 4'b1101 : 4'bz;  // Driver driver_94
  assign Reg_A = Instr_13 ? 4'b1101 : 4'bz;  // Driver driver_95
  assign Imm32_En = Instr_13 ? 1'b1 : 1'bz;  // Driver driver_96
  assign Reg_WEn = Instr_13 ? 1'b1 : 1'bz;  // Driver driver_97
  assign ALU_Cod_Op = Instr_13 ? multiplexer_16_out : 4'bz;  // Driver driver_98
  assign ALU_Force_Carry = Instr_13 ? Instr[7] : 1'bz;  // Driver driver_99
  // Probe reg on PP_Queue_Msb
  and and_25 (PP_Finished, comparator_8_gt, not_7_out);
  not not_9 (TelnetBuf_Av, comparator_9_eq);
  PullDown #(.Bits(8)) pulldown_12 (.out(Telnet_Out));
  or or_7 (or_7_out, d_ff_3_q, BreakReg_q);
  PullDown #(.Bits(4)) pulldown_13 (.out(Flags_Mask));
  Flags_APSR flags_apsr_1 (
    .Update_Mask(Flags_Mask), .Flags_In(ALU_Out_Flags), .Clk(Clock), .Rst(1'b0), .Flags_Out(Flags));
  PullDown pulldown_14 (.out(Store_Req));
  PullDown pulldown_15 (.out(Load_Req));
  assign Imm32 = Instr_11 ? {{22{1'b0}}, Instr[7:0], 2'b00} : 32'bz;  // Driver driver_100
  assign Reg_W = Instr_11 ? lotohi_16_out : 4'bz;  // Driver driver_101
  assign Imm32_En = Instr_11 ? 1'b1 : 1'bz;  // Driver driver_102
  assign Store_Req = Instr_11 ? decoder_2_out_0 : 1'bz;  // Driver driver_103
  assign Load_Req = Instr_11 ? decoder_2_out_1 : 1'bz;  // Driver driver_104
  assign Reg_A = Instr_11 ? 4'b1101 : 4'bz;  // Driver driver_105
  Sub #(.Bits(4)) sub_2 (.a(PP_Reglist_Cnt), .b(PP_Counter), .c_i(1'b0), .s(sub_2_s));  // open: c_o
  RAMDualAccess #(.AddrBits(24), .Bits(8)) ramdualaccess_1 (
    .str(and_9_out), .C(Clock), .ld(1'b0), .A1(TelnetBuf_WrPos_out), .Din1(Telnet_Out),
    .A2(TelnetBuf_RdPos_out), .D2(TelnetBuf_RdData));  // open: D1
  Comparator #(.Bits(24)) comparator_10 (.a(TelnetBuf_RdPos_out), .b(TelnetBuf_WrPos_out));  // open: gt, eq, lt
  Add #(.Bits(32)) add_5 (.a(mul_2_mul), .b(mul_3_mul), .c_i(1'b0), .s(add_5_s));  // open: c_o
  or or_8 (or_8_out, Midi_Prog, d_ff_as_7_q);
  // Probe on Mem_Area
  // Probe Flags on Flags
  assign Reg_WEn = Load ? 1'b1 : 1'bz;  // Driver driver_106
  or or_9 (or_9_out, Load, Store);
  D_FF_AS d_ff_as_8 (
    .Set(1'b0), .D(d_ff_as_8_nq), .C(not_10_out), .Clr(not_11_out), .Q(d_ff_as_8_q), .nQ(d_ff_as_8_nq));
  not not_10 (not_10_out, Clock);
  not not_11 (not_11_out, Store_Req);
  D_FF_AS d_ff_as_9 (
    .Set(1'b0), .D(d_ff_as_9_nq), .C(not_12_out), .Clr(not_13_out), .Q(d_ff_as_9_q), .nQ(d_ff_as_9_nq));
  not not_12 (not_12_out, Clock);
  not not_13 (not_13_out, Load_Req);
  Multiplexer #(.Bits(4)) multiplexer_18 (.sel(Instr_Push), .in_0(4'b0101), .in_1(4'b0110), .out(multiplexer_18_out));
  Add #(.Bits(4)) add_6 (.a(PP_Counter), .b(4'b0000), .c_i(PP_DoingStuff), .s(add_6_s));  // open: c_o
  Multiplexer #(.Bits(4)) multiplexer_19 (.sel(Instr_Pop), .in_0(PP_Counter), .in_1(sub_2_s), .out(PP_Addr));
  Terminal #(.termWidth(80)) terminal_1 (.D(Mem_In), .C(Mmio_Clock), .en(demultiplexer_1_out_0));
  Register #(.Bits(32)) Res (.D(Mem_In), .C(Mmio_Clock), .en(demultiplexer_1_out_1), .Q(Res_q));
  Keyboard keyboard_1 (.C(Mmio_Clock), .en(Keyb_Read), .D(keyboard_1_d), .av(keyboard_1_av[0]));
  Add #(.Bits(64)) add_7 (.a(mul_1_mul), .b({add_5_s, {32{1'b0}}}), .c_i(1'b0), .s({add_7_s_2, add_7_s}));  // open: c_o
  // MIDI #(.midiProgChange("true")) midi_1: pin names not known; wires that end beside it: multiplexer_15_out, register_3_q, register_4_q, Midi_Prog, 1'b1, or_8_out
  Seven_Seg_Hex seven_seg_hex_1 (.d(Mem_Out_Raw_Whole[31:28]), .dp(1'b0));
  Demultiplexer #(.Selector_Bits(2)) demultiplexer_2 (
    .sel(Mem_Area), .in(Clock), .out_0(demultiplexer_2_out_0), .out_1(Ram_Clock), .out_2(Disp_Clock),
    .out_3(Mmio_Clock));
  BitExtender #(.outputBits(24)) bitextender_5 (.in(RegVal_A[7:0]), .out(bitextender_5_out));
  // Probe Res on Res_q
  not not_14 (not_14_out, Telnet_Av);
  Break #(.Cycles(100000000)) break_1 (.brk(or_7_out));
  Seven_Seg_Hex seven_seg_hex_2 (.d(Mem_Out_Raw_Whole[23:20]), .dp(1'b0));
  Seven_Seg_Hex seven_seg_hex_3 (.d(Mem_Out_Raw_Whole[27:24]), .dp(1'b0));
  BitExtender #(.inputBits(16), .outputBits(32)) bitextender_6 (.in(Mem_Out_Raw[15:0]), .out(bitextender_6_out));
  BitExtender #(.outputBits(32)) bitextender_7 (.in(Mem_Out_Raw[7:0]), .out(bitextender_7_out));
  Multiplexer #(.Bits(5)) multiplexer_20 (.sel(Imm5_En), .in_0(RegVal_B[4:0]), .in_1(Imm5), .out(multiplexer_20_out));
  PullDown #(.Bits(5)) pulldown_16 (.out(Imm5));
  PullDown pulldown_17 (.out(Imm5_En));
  assign Data_Addr = or_9_out ? ALU_Out : 32'bz;  // Driver driver_107
  and and_26 (and_26_out, or_9_out, ~PC_Hold_Manual);  // And
  // And and_27 has open pins: In_1=d_ff_as_8_q, In_2=Store_Req, out=open
  and and_28 (and_28_out, d_ff_as_8_nq, Store_Req);
  // And and_29 has open pins: In_1=d_ff_as_9_q, In_2=Load_Req, out=open
  and and_30 (and_30_out, d_ff_as_9_nq, Load_Req);
  assign Imm32 = PP_Upd_SP ? {{26{1'b0}}, PP_Reglist_Cnt, 2'b00} : 32'bz;  // Driver driver_108
  assign Reg_W = PP_Upd_SP ? 4'b1101 : 4'bz;  // Driver driver_109
  assign Reg_A = PP_Upd_SP ? 4'b1101 : 4'bz;  // Driver driver_110
  assign Imm32_En = PP_Upd_SP ? 1'b1 : 1'bz;  // Driver driver_111
  assign Reg_WEn = PP_Upd_SP ? 1'b1 : 1'bz;  // Driver driver_112
  assign ALU_Cod_Op = PP_Upd_SP ? multiplexer_18_out : 4'bz;  // Driver driver_113
  assign ALU_Force_Carry = PP_Upd_SP ? Instr_Push : 1'bz;  // Driver driver_114
  D_FF_AS #(.Bits(4)) d_ff_as_10 (.Set(1'b0), .D(add_6_s), .C(~Clock), .Clr(PP_Finished), .Q(PP_Counter));  // open: nQ
  and and_31 (and_31_out, Instr_Pop, PP_DoingStuff);
  BCD bcd_1 (.In(Res_q), .Out(bcd_1_out));
  PullDown #(.Bits(16)) pulldown_18 (.out(keyboard_1_d));
  Counter #(.Bits(32)) counter_1 (.en(1'b1), .C(clk_2), .clr(1'b0), .out(counter_1_out));  // open: ovf
  Seven_Seg_Hex seven_seg_hex_4 (.d(Mem_Out_Raw_Whole[15:12]), .dp(1'b0));
  Seven_Seg_Hex seven_seg_hex_5 (.d(Mem_Out_Raw_Whole[19:16]), .dp(1'b0));
  Multiplexer #(.Selector_Bits(2), .Bits(32)) multiplexer_21 (
    .sel(Mem_Mode_Real), .in_0(Mem_Out_Raw), .in_1({{16{1'b0}}, Mem_Out_Raw[15:0]}),
    .in_2({{24{1'b0}}, Mem_Out_Raw[7:0]}), .in_3({32{1'b0}}), .out(multiplexer_21_out));
  Multiplexer #(.Selector_Bits(2), .Bits(32)) multiplexer_22 (
    .sel(Mem_Mode_Real), .in_0(Mem_Out_Raw), .in_1(bitextender_6_out), .in_2(bitextender_7_out),
    .in_3({32{1'b0}}), .out(multiplexer_22_out));
  PullDown #(.Bits(32)) pulldown_19 (.out(Imm32));
  and and_32 (and_32_out, Flags[1], ALU_Enable_Carry);
  assign ALU_Cod_Op = and_26_out ? 4'b0101 : 4'bz;  // Driver driver_115
  PRNG #(.Bits(32)) prng_1 (.S({32{1'b0}}), .se(1'b0), .ne(Rng_Read), .C(Mmio_Clock), .R(prng_1_r));
  Multiplexer #(.Bits(32)) multiplexer_23 (
    .sel(TelnetBuf_Av), .in_0(32'hffff01ff), .in_1({{24{1'b0}}, TelnetBuf_RdData}), .out(multiplexer_23_out));
  Seven_Seg_Hex seven_seg_hex_6 (.d(Mem_Out_Raw_Whole[7:4]), .dp(1'b0));
  Seven_Seg_Hex seven_seg_hex_7 (.d(Mem_Out_Raw_Whole[11:8]), .dp(1'b0));
  PullDown pulldown_20 (.out(Imm32_En));
  Multiplexer #(.Bits(32)) multiplexer_24 (.sel(Imm32_En), .in_0(RegVal_B), .in_1(Imm32), .out(multiplexer_24_out));
  PullDown pulldown_21 (.out(ALU_Force_Carry));
  or or_10 (or_10_out, ALU_Force_Carry, and_32_out);
  PullDown pulldown_22 (.out(ALU_Enable_Carry));
  assign driver_116_out = Store_Req ? and_28_out : 1'bz;  // Driver driver_116
  PullDown pulldown_23 (.out(driver_116_out));
  assign driver_117_out = Load_Req ? and_30_out : 1'bz;  // Driver driver_117
  PullDown pulldown_24 (.out(driver_117_out));
  LoToHi lotohi_19 (.Reg(Instr[2:0]), .Out(lotohi_19_out));
  LoToHi lotohi_20 (.Reg(Instr[5:3]), .Out(lotohi_20_out));
  // Probe on PP_Counter
  assign ALU_Force_Carry = and_31_out ? 1'b1 : 1'bz;  // Driver driver_118
  Div #(.Bits(32)) div_1 (.a(Reg_0), .b(Reg_1), .q(div_1_q), .r(div_1_r));
  Div #(.Signed("true"), .Bits(32)) div_2 (.a(Reg_0), .b(Reg_1), .q(div_2_q), .r(div_2_r));
  Button button_4 (.out(button_4_out));
  Seven_Seg_Hex seven_seg_hex_8 (.d(Mem_Out_Raw_Whole[3:0]), .dp(1'b0));
  Multiplexer #(.Selector_Bits(2), .Bits(32)) multiplexer_25 (
    .sel(Mem_Area), .in_0(Rom_Out), .in_1(Ram_Out), .in_2({32{1'b0}}), .in_3(Mmio_Out),
    .out(Mem_Out_Raw_Whole));
  Multiplexer #(.Bits(32)) multiplexer_26 (
    .sel(Mem_Signed_Real), .in_0(multiplexer_21_out), .in_1(multiplexer_22_out), .out(Mem_Out));
  PullDown #(.Bits(4)) pulldown_25 (.out(ALU_Cod_Op));
  Multiplexer #(.Bits(32)) multiplexer_27 (.sel(Load), .in_0(ALU_Out), .in_1(Mem_Out), .out(Reg_Val));
  PullDown pulldown_26 (.out(Load));
  Delay #(.delayTime(5)) delay_1 (.in(driver_116_out), .out(Store));
  Delay #(.delayTime(5)) delay_2 (.in(driver_117_out), .out(Load));
  Multiplexer #(.Selector_Bits(2), .Bits(32)) multiplexer_28 (
    .sel(Instr[7:6]), .in_0({RegVal_A[7:0], RegVal_A[15:8], RegVal_A[23:16], RegVal_A[31:24]}),
    .in_1({RegVal_A[23:16], RegVal_A[31:24], RegVal_A[7:0], RegVal_A[15:8]}), .in_2({32{1'b0}}),
    .in_3({bitextender_5_out, RegVal_A[15:8]}), .out(multiplexer_28_out));
  Comparator #(.Bits(4)) comparator_11 (.a(4'b1000), .b(PP_Queue_Msb), .eq(comparator_11_eq));  // open: gt, lt
  Multiplexer #(.Bits(4)) multiplexer_29 (.sel(Instr_Pop), .in_0(4'b1110), .in_1(4'b1111), .out(multiplexer_29_out));
  Multiplexer #(.Bits(4)) multiplexer_30 (.sel(and_31_out), .in_0(4'b0101), .in_1(4'b0110), .out(multiplexer_30_out));
  Multiplexer #(.Selector_Bits(5), .Bits(32)) multiplexer_31 (
    .sel(Mem_Addr[6:2]), .in_0(notconnected_1_out), .in_1(Res_q), .in_2({{24{1'b0}}, Telnet_Out}),
    .in_3({{31{1'b0}}, Telnet_Av}), .in_4(bcd_1_out), .in_5(prng_1_r), .in_6({{31{1'b0}}, keyboard_1_av[0]}),
    .in_7({{16{1'b0}}, keyboard_1_d}), .in_8(div_1_q), .in_9(div_1_r), .in_10(div_2_q), .in_11(div_2_r),
    .in_12({{31{1'b0}}, Disp_Buf}), .in_13(add_7_s), .in_14(add_7_s_2), .in_15(counter_1_out),
    .in_16(multiplexer_23_out), .in_17(notconnected_2_out), .in_18(notconnected_3_out),
    .in_19(notconnected_4_out), .in_20(notconnected_5_out), .in_21(notconnected_6_out),
    .in_22(notconnected_7_out), .in_23(notconnected_8_out), .in_24(notconnected_9_out),
    .in_25(notconnected_10_out), .in_26(notconnected_11_out), .in_27(notconnected_12_out),
    .in_28(notconnected_13_out), .in_29(notconnected_14_out), .in_30(notconnected_15_out),
    .in_31(notconnected_16_out), .out(Mmio_Out));
  // NotConnected on notconnected_1_out
  // NotConnected on notconnected_2_out
  // NotConnected on notconnected_3_out
  // NotConnected on notconnected_4_out
  // NotConnected on notconnected_5_out
  // NotConnected on notconnected_6_out
  // NotConnected on notconnected_7_out
  // NotConnected on notconnected_8_out
  // NotConnected on notconnected_9_out
  // NotConnected on notconnected_10_out
  // NotConnected on notconnected_11_out
  // NotConnected on notconnected_12_out
  // NotConnected on notconnected_13_out
  // NotConnected on notconnected_14_out
  // NotConnected on notconnected_15_out
  // NotConnected on notconnected_16_out
  assign Continue = button_4_out ? 1'b1 : 1'bz;  // Driver driver_119
  ALU alu_1 (
    .A(RegVal_A), .B(multiplexer_24_out), .Shift(multiplexer_20_out), .Cod_Op(ALU_Cod_Op),
    .Carry_In(or_10_out), .Negate(ALU_Neg), .S(ALU_Out), .Flags(ALU_Out_Flags));
  PullDown pulldown_27 (.out(ALU_Neg));
  assign Reg_W = Instr_14_9 ? lotohi_19_out : 4'bz;  // Driver driver_120
  assign Reg_A = Instr_14_9 ? lotohi_20_out : 4'bz;  // Driver driver_121
  Multiplexer #(.Bits(4)) multiplexer_32 (
    .sel(comparator_11_eq), .in_0(PP_Queue_Msb), .in_1(multiplexer_29_out), .out(PP_Real_Reg));
  assign ALU_Cod_Op = PP_DoingStuff ? multiplexer_30_out : 4'bz;  // Driver driver_122
  assign Reg_A = PP_DoingStuff ? 4'b1101 : 4'bz;  // Driver driver_123
  or or_11 (or_11_out, horl, clk);
  assign Imm32 = Instr_14_9 ? multiplexer_28_out : 32'bz;  // Driver driver_124
  Demultiplexer #(.Selector_Bits(5)) demultiplexer_3 (
    .sel(Mem_Addr[6:2]), .in(Mem_Area_Mmio), .out_2(demultiplexer_3_out_2), .out_5(Rng_Read),
    .out_7(Keyb_Read), .out_16(TelnetData_Read));  // open: out_0, out_1, out_3, out_4, out_6, out_8, out_9, out_10, out_11, out_12, out_13, out_14, out_15, out_17, out_18, out_19, out_20, out_21, out_22, out_23, out_24, out_25, out_26, out_27, out_28, out_29, out_30, out_31
  and and_33 (and_33_out, or_11_out, ~1'b0);  // And
  or or_12 (or_12_out, Load, Store);
  or or_13 (or_13_out, and_33_out, Continue);
  PullDown pulldown_28 (.out(Continue));
  GraphicCard #(.graphicHeight(360), .graphicWidth(480), .Bits(32)) Display (
    .A(Mem_Addr[20:2]), .str(Store), .C(Disp_Clock), .ld(1'b0), .B(Disp_Buf), .D(Mem_In));
  ROM #(.AddrBits(22), .isProgramMemory("true"), .Bits(32)) rom_1 (.A(Mem_Addr[23:2]), .sel(1'b1), .D(Rom_Out));
  PullDown #(.Bits(2)) pulldown_29 (.out(Mem_Mode));
  assign Mem_Mode_Real = or_12_out ? Mem_Mode : 2'bz;  // Driver driver_125
  // Probe Reg_A on Reg_A
  Demultiplexer demultiplexer_4 (
    .sel(Instr_Pop), .in(1'b1), .out_0(demultiplexer_4_out_0), .out_1(demultiplexer_4_out_1));
  and and_34 (and_34_out, Telnet_Av, 1'b0);
  PullDown #(.Bits(2)) pulldown_30 (.out(Mem_Mode_Real));
  assign Mem_Signed_Real = or_12_out ? Mem_Signed : 1'bz;  // Driver driver_126
  PullDown pulldown_31 (.out(Mem_Signed));
  assign Imm32 = PP_DoingStuff ? {{26{1'b0}}, PP_Addr, 2'b00} : 32'bz;  // Driver driver_127
  assign Reg_W = PP_DoingStuff ? PP_Real_Reg : 4'bz;  // Driver driver_128
  assign Imm32_En = PP_DoingStuff ? 1'b1 : 1'bz;  // Driver driver_129
  assign Store = PP_DoingStuff ? demultiplexer_4_out_0 : 1'bz;  // Driver driver_130
  assign Load = PP_DoingStuff ? demultiplexer_4_out_1 : 1'bz;  // Driver driver_131
  and and_35 (and_35_out, demultiplexer_3_out_2, and_34_out);
  xor xor_2 (xor_2_out, demultiplexer_3_out_2, and_34_out);
  Sub #(.Bits(32)) sub_3 (.a(Mem_Addr), .b(32'h1000000), .c_i(1'b0), .s(sub_3_s));  // open: c_o
  not not_15 (Clock, or_13_out);
  // Probe Clock on Clock
  PullDown pulldown_32 (.out(Mem_Signed_Real));
  // Probe Reg_B on Reg_B
  assign ALU_Neg = Instr_14_9 ? 1'b1 : 1'bz;  // Driver driver_132
  assign Imm32_En = Instr_14_9 ? 1'b1 : 1'bz;  // Driver driver_133
  assign Reg_WEn = Instr_14_9 ? 1'b1 : 1'bz;  // Driver driver_134
  assign ALU_Cod_Op = Instr_14_9 ? 4'b1001 : 4'bz;  // Driver driver_135
  Break break_2 (.brk(and_35_out));
  Multiplexer #(.Selector_Bits(2), .Bits(32)) multiplexer_33 (
    .sel(Mem_Addr[1:0]), .in_0(Rom_Out), .in_1({{8{1'b0}}, Rom_Out[31:8]}),
    .in_2({{16{1'b0}}, Rom_Out[31:16]}), .in_3({{24{1'b0}}, Rom_Out[31:24]}));  // open: out
  // Probe ALU_Out on ALU_Out
  // Probe ALU_Out_Flags on ALU_Out_Flags
  // Probe Imm5 on Imm5
  // Probe Imm5_En on Imm5_En
  // Probe Imm32 on Imm32
  // Probe Imm32_En on Imm32_En
  // Probe Flags_Mask on Flags_Mask
  Delay #(.delayTime(5)) delay_3 (.in(xor_2_out), .out(delay_3_out));
  // RAM32Bit #(.generic("addrBits := 24;")) RAM: pin names not known; wires that end beside it: sub_3_s[23:0], Mem_In, Store, Mem_Mode_Real, Mem_Signed_Real, Ram_Clock, Ram_Out
  Multiplexer #(.Selector_Bits(2), .Bits(32)) multiplexer_34 (
    .sel(Mem_Addr[1:0]), .in_0(Mem_Out_Raw_Whole), .in_1({{8{1'b0}}, Mem_Out_Raw_Whole[31:8]}),
    .in_2({{16{1'b0}}, Mem_Out_Raw_Whole[31:16]}), .in_3({{24{1'b0}}, Mem_Out_Raw_Whole[31:24]}),
    .out(multiplexer_34_out));
  // Probe Reg_W on Reg_W
  and and_36 (Instr_01_02, ~Instr[13], ~Instr[14], ~Instr[15]);  // And
  and and_37 (Instr_03, Instr[13], ~Instr[14], ~Instr[15]);  // And
  and and_38 (Instr_04, ~Instr[10], ~Instr[11], ~Instr[12], ~Instr[13], Instr[14], ~Instr[15]);  // And
  and and_39 (Instr_05, Instr[10], ~Instr[11], ~Instr[12], ~Instr[13], Instr[14], ~Instr[15]);  // And
  and and_40 (Instr_06, Instr[11], ~Instr[12], ~Instr[13], Instr[14], ~Instr[15]);  // And
  and and_41 (Instr_07_08, Instr[12], ~Instr[13], Instr[14], ~Instr[15]);  // And
  and and_42 (Instr_09, Instr[13], Instr[14], ~Instr[15]);  // And
  and and_43 (Instr_10, ~Instr[12], ~Instr[13], ~Instr[14], Instr[15]);  // And
  and and_44 (Instr_11, Instr[12], ~Instr[13], ~Instr[14], Instr[15]);  // And
  and and_45 (Instr_12, ~Instr[12], Instr[13], ~Instr[14], Instr[15]);  // And
  and and_46 (and_46_out, Instr[12], Instr[13], ~Instr[14], Instr[15]);  // And
  and and_47 (Instr_Stm, ~Instr[11], ~Instr[12], ~Instr[13], Instr[14], Instr[15]);  // And
  and and_48 (Instr_Ldm, Instr[11], ~Instr[12], ~Instr[13], Instr[14], Instr[15]);  // And
  and and_49 (Instr_16, Instr[12], ~Instr[13], Instr[14], Instr[15]);  // And
  and and_50 (Instr_18, ~Instr[11], ~Instr[12], Instr[13], Instr[14], Instr[15]);  // And
  and and_51 (Instr_19, Instr[12], Instr[13], Instr[14], Instr[15]);
  Delay #(.delayTime(5)) delay_4 (.in(delay_3_out), .out(delay_4_out));
  Delay #(.delayTime(5)) delay_5 (.in(delay_4_out), .out(delay_5_out));
  Delay #(.delayTime(5)) delay_6 (.in(delay_5_out), .out(delay_6_out));
  // Probe Reg_WEn on Reg_WEn
  // Probe Mem_Addr on Mem_Addr
  // Probe Mem_Out_Raw on Mem_Out_Raw
  // Probe Mem_Out on Mem_Out
  // Probe Load on Load
  // Probe Store_Req on Store_Req
  // Probe Store on Store
  and and_52 (Instr_13, and_46_out, ~Instr[8], ~Instr[9], ~Instr[10], ~Instr[11]);  // And
  and and_53 (Instr_SignEx, and_46_out, ~Instr[8], Instr[9], ~Instr[10], ~Instr[11]);  // And
  and and_54 (Instr_14_4, and_46_out, ~Instr[9], Instr[10]);  // And
  and and_55 (Instr_14_9, and_46_out, Instr[11], ~Instr[10], Instr[9], ~Instr[8]);  // And
  Delay #(.delayTime(5)) delay_7 (.in(delay_6_out), .out(Telnet_Read));
  Multiplexer #(.Bits(32)) multiplexer_35 (
    .sel(Mem_Area_Ram), .in_0(multiplexer_34_out), .in_1(Ram_Out), .out(Mem_Out_Raw));
  Sub #(.Bits(32)) sub_4 (.a(Mem_Addr), .b(32'h100000), .c_i(1'b0), .s(sub_4_s));  // open: c_o
  not not_16 (not_16_out, comparator_12_eq);
  Counter #(.Bits(24)) counter_2 (
    .en(1'b1), .C(Clock), .clr(1'b0), .out({counter_2_out_2, counter_2_out}));  // open: ovf
  BlockRAMDualPort #(.AddrBits(24), .Bits(32)) blockramdualport_1 (
    .A({counter_2_out_2, counter_2_out}), .Din(Code_Addr), .str(1'b1), .C(Clock));  // open: D
  RAMDualPort #(.AddrBits(23), .Bits(32)) ramdualport_1 (
    .A(sub_4_s[24:2]), .Din(Mem_In), .str(Store), .C(Ram_Clock), .ld(Load));  // open: D
  Counter #(.Bits(24)) counter_3 (.en(not_16_out), .C(Clock), .clr(1'b0), .out(counter_3_out));  // open: ovf
  BlockRAMDualPort #(.AddrBits(24), .Bits(32)) blockramdualport_2 (
    .A(counter_3_out), .Din(Reg_Lr), .str(not_16_out), .C(Clock));  // open: D
  GraphicCard #(.Bits(16)) graphiccard_1 (.A(counter_2_out), .str(1'b0), .C(Clock), .ld(1'b0), .B(1'b0), .D(Instr));
  D_FF #(.Bits(32)) d_ff_4 (.D(Reg_Lr), .C(Clock), .Q(d_ff_4_q));  // open: nQ
  Comparator #(.Bits(32)) comparator_12 (.a(Reg_Lr), .b(d_ff_4_q), .eq(comparator_12_eq));  // open: gt, lt

  // Other names for the same wires on the sheet: Flags_V = Flags[0]; Flags_C = Flags[1]; Flags_Z = Flags[2];
  //   Flags_N = Flags[3]; PP_Reglist_Stored[8:0] = Instr[8:0]; Reglist[8:0] = Instr[8:0];
  //   Mmio_Addr[4:0] = Mem_Addr[6:2]; Reg_Pc[31:0] = Code_Addr; Reg_Val_W[31:0] = Mem_In

  // Notes on the sheet:
  //   clk: Hz: 2147483647
  //   clk_2: Hz: 100
  //   rom_1 loads digital_out.raw
  //   Bug in Digital's Telnet.
  //   writeOutputs() returns peeked byte.
  //   readInputs() drops it. If Telnet is used at high enough speed bytes will be dropped.
  //   the Telnet component should drop the byte as soon as it's read and cache it, so both are synchronized.
  //   historique pc et lr
endmodule
