// Digital circuit machine_old.dig as structural Verilog
module machine_old (
  input  clk
);

  wire Break, Clock, Mem_Addr, Ram_In, Ram_Load, Ram_Out, Ram_Store;
  wire [23:0] Addr_Code, Addr_Data;
  wire [31:0] Ram_Code, Ram_Data_Read, Ram_Data_Write;

  and and_1 (Clock, clk, ~Break);  // And
  RAMDualAccess #(.AddrBits(24), .Bits(32), .isProgramMemory("true")) RAM (
    .str(Ram_Store), .C(Clock), .ld(Ram_Load), .A1(Addr_Data), .Din1(Ram_Data_Write), .A2(Addr_Code),
    .D1(Ram_Data_Read), .D2(Ram_Code));
  // RAM32Bit #(.generic("addrBits := 24;")) ram32bit_1: pin names not known; wires that end beside it: Mem_Addr, Ram_In, 1'b0, Clock, Ram_Out
  GraphicCard #(.Bits(32)) Display ();  // open: A, str, C, ld, B, D
endmodule
