// Digital circuit midi.dig as structural Verilog
module midi (
  input  clk
);

  wire [6:0] add_1_s, counter_1_out;

  Counter #(.Bits(7)) counter_1 (.en(1'b1), .C(clk), .clr(1'b0), .out(counter_1_out));  // open: ovf
  Add #(.Bits(7)) add_1 (.a(counter_1_out), .b(7'b0110000), .c_i(1'b1), .s(add_1_s));  // open: c_o
  // MIDI #(.midiInstrument("Halo Pad")) midi_1: pin names not known; wires that end beside it: add_1_s, {7{1'b1}}, 1'b1, 1'b1, clk

  // Notes on the sheet:
  //   clk: Hz: 5
endmodule
