// Digital circuit terminal.dig as structural Verilog
module terminal (
  input  clk
);

  wire keyboard_1_av, telnet_1_av, telnet_1_out;
  wire [15:0] keyboard_1_d;

  Keyboard keyboard_1 (.C(clk), .en(1'b1), .D(keyboard_1_d), .av(keyboard_1_av));
  Telnet #(.telnetEscape("false"), .port(4567)) telnet_1 (
    .in(keyboard_1_d[7:0]), .C(clk), .wr(keyboard_1_av), .rd(1'b1), .out(telnet_1_out), .av(telnet_1_av));
  Terminal terminal_1 (.D(telnet_1_out), .C(clk), .en(telnet_1_av));

  // Other names for the same wires on the sheet: Clock = clk

  // Notes on the sheet:
  //   clk: Hz: 100
endmodule
