// Digital circuit vgatest.dig as structural Verilog
module vgatest (
  input  clk
);

  wire comparator_1_gt, comparator_2_eq, comparator_3_gt, comparator_4_eq, counter_1_ovf, counter_3_ovf,
       counter_4_ovf, not_1_out, not_2_out;
  wire [7:0] counter_1_out, counter_3_out, counter_4_out;
  wire [9:0] add_1_s, counter_2_out, counter_5_out, counter_6_out, div_1_q, div_2_q;
  wire [19:0] mul_1_mul;

  Counter #(.Bits(8)) counter_1 (.en(1'b1), .C(clk), .clr(1'b0), .out(counter_1_out), .ovf(counter_1_ovf));
  Add #(.Bits(10)) add_1 (.a(mul_1_mul[9:0]), .b(counter_2_out), .c_i(1'b0), .s(add_1_s));  // open: c_o
  Counter #(.Bits(10)) counter_2 (.en(1'b1), .C(clk), .clr(comparator_2_eq), .out(counter_2_out));  // open: ovf
  Counter #(.Bits(8)) counter_3 (.en(1'b1), .C(counter_1_ovf), .clr(1'b0), .out(counter_3_out), .ovf(counter_3_ovf));
  Div #(.Bits(10)) div_1 (.a(add_1_s), .b(10'h3), .q(div_1_q));  // open: r
  Comparator #(.Bits(10)) comparator_1 (.a(counter_2_out), .b(10'h2bf), .gt(comparator_1_gt));  // open: eq, lt
  Comparator #(.Bits(10)) comparator_2 (.a(counter_2_out), .b(10'h31f), .eq(comparator_2_eq));  // open: gt, lt
  Counter #(.Bits(8)) counter_4 (.en(1'b1), .C(counter_3_ovf), .clr(1'b0), .out(counter_4_out), .ovf(counter_4_ovf));
  not not_1 (not_1_out, comparator_1_gt);
  Counter #(.Bits(10)) counter_5 (
    .en(1'b1), .C(comparator_2_eq), .clr(comparator_4_eq), .out(counter_5_out));  // open: ovf
  VGA vga_1 (.R(div_1_q[7:0]), .G(div_2_q[7:0]), .B({8{1'b0}}), .H(not_1_out), .V(not_2_out), .C(clk));
  Div #(.Bits(10)) div_2 (.a(counter_5_out), .b(10'h2), .q(div_2_q));  // open: r
  Comparator #(.Bits(10)) comparator_3 (.a(counter_5_out), .b(10'h20a), .gt(comparator_3_gt));  // open: eq, lt
  Comparator #(.Bits(10)) comparator_4 (.a(counter_5_out), .b(10'h20c), .eq(comparator_4_eq));  // open: gt, lt
  Counter #(.Bits(10)) counter_6 (.en(1'b1), .C(comparator_4_eq), .clr(1'b0), .out(counter_6_out));  // open: ovf
  not not_2 (not_2_out, comparator_3_gt);
  Mul #(.Bits(10)) mul_1 (.a(counter_6_out), .b(10'ha), .mul(mul_1_mul));

  // Notes on the sheet:
  //   clk: Hz: 2147483647
endmodule
