// Logisim project 4096compt_7SegDecod.circ as structural Verilog: 2 circuits, main circuit main
module main (
);

  wire clock_1_out, counter_1_carry, counter_2_carry, counter_3_carry, counter_4_carry, counter_5_carry,
       counter_6_carry, counter_7_carry, d_ff_1_q, d_ff_2_q, d_ff_3_q, d_ff_4_q, d_ff_5_q, d_ff_6_q,
       sevenSegDecoder_1_segment_a, sevenSegDecoder_1_segment_b, sevenSegDecoder_1_segment_c,
       sevenSegDecoder_1_segment_d, sevenSegDecoder_1_segment_e, sevenSegDecoder_1_segment_f,
       sevenSegDecoder_1_segment_g, sevenSegDecoder_2_segment_a, sevenSegDecoder_2_segment_b,
       sevenSegDecoder_2_segment_c, sevenSegDecoder_2_segment_d, sevenSegDecoder_2_segment_e,
       sevenSegDecoder_2_segment_f, sevenSegDecoder_2_segment_g, sevenSegDecoder_3_segment_a,
       sevenSegDecoder_3_segment_b, sevenSegDecoder_3_segment_c, sevenSegDecoder_3_segment_d,
       sevenSegDecoder_3_segment_e, sevenSegDecoder_3_segment_f, sevenSegDecoder_3_segment_g,
       sevenSegDecoder_4_segment_a, sevenSegDecoder_4_segment_b, sevenSegDecoder_4_segment_c,
       sevenSegDecoder_4_segment_d, sevenSegDecoder_4_segment_e, sevenSegDecoder_4_segment_f,
       sevenSegDecoder_4_segment_g, sevenSegDecoder_5_segment_a, sevenSegDecoder_5_segment_b,
       sevenSegDecoder_5_segment_c, sevenSegDecoder_5_segment_d, sevenSegDecoder_5_segment_e,
       sevenSegDecoder_5_segment_f, sevenSegDecoder_5_segment_g, sevenSegDecoder_6_segment_a,
       sevenSegDecoder_6_segment_b, sevenSegDecoder_6_segment_c, sevenSegDecoder_6_segment_d,
       sevenSegDecoder_6_segment_e, sevenSegDecoder_6_segment_f, sevenSegDecoder_6_segment_g,
       sevenSegDecoder_7_segment_a, sevenSegDecoder_7_segment_b, sevenSegDecoder_7_segment_c,
       sevenSegDecoder_7_segment_d, sevenSegDecoder_7_segment_e, sevenSegDecoder_7_segment_f,
       sevenSegDecoder_7_segment_g, sevenSegDecoder_8_segment_a, sevenSegDecoder_8_segment_b,
       sevenSegDecoder_8_segment_c, sevenSegDecoder_8_segment_d, sevenSegDecoder_8_segment_e,
       sevenSegDecoder_8_segment_f, sevenSegDecoder_8_segment_g, undriven;
  wire [3:0] counter_1_q, counter_2_q, counter_3_q, counter_4_q, counter_5_q, counter_6_q, counter_7_q,
       counter_8_q;

  Clock clock_1 (.out(clock_1_out));
  Counter #(.width(4), .max('h9), .ongoal("load")) counter_1 (
    .load(1'b0), .up(1'b1), .count(1'b1), .clk(clock_1_out), .carry(counter_1_carry), .Q(counter_1_q));  // open: clr, D
  sevenSegDecoder sevenSegDecoder_1 (
    .e1(counter_1_q[3]), .e2(counter_1_q[2]), .e3(counter_1_q[1]), .e4(counter_1_q[0]),
    .segment_a(sevenSegDecoder_1_segment_a), .segment_b(sevenSegDecoder_1_segment_b),
    .segment_c(sevenSegDecoder_1_segment_c), .segment_d(sevenSegDecoder_1_segment_d),
    .segment_e(sevenSegDecoder_1_segment_e), .segment_f(sevenSegDecoder_1_segment_f),
    .segment_g(sevenSegDecoder_1_segment_g));
  _7_Segment_Display L_7_Segment_Display_1 (
    .g(sevenSegDecoder_1_segment_g), .f(sevenSegDecoder_1_segment_f), .a(sevenSegDecoder_1_segment_a),
    .b(sevenSegDecoder_1_segment_b), .e(sevenSegDecoder_1_segment_e), .d(sevenSegDecoder_1_segment_d),
    .c(sevenSegDecoder_1_segment_c), .dp(1'b0));
  Counter #(.width(4), .max('h9)) counter_2 (
    .clr(d_ff_1_q), .load(1'b0), .up(1'b1), .count(counter_1_carry), .clk(clock_1_out),
    .carry(counter_2_carry), .Q(counter_2_q));  // open: D
  sevenSegDecoder sevenSegDecoder_2 (
    .e1(counter_2_q[3]), .e2(counter_2_q[2]), .e3(counter_2_q[1]), .e4(counter_2_q[0]),
    .segment_a(sevenSegDecoder_2_segment_a), .segment_b(sevenSegDecoder_2_segment_b),
    .segment_c(sevenSegDecoder_2_segment_c), .segment_d(sevenSegDecoder_2_segment_d),
    .segment_e(sevenSegDecoder_2_segment_e), .segment_f(sevenSegDecoder_2_segment_f),
    .segment_g(sevenSegDecoder_2_segment_g));
  D_Flip_Flop d_ff_1 (.D(counter_2_carry), .clk(clock_1_out), .Q(d_ff_1_q));  // open: Qn, preset, reset
  _7_Segment_Display L_7_Segment_Display_2 (
    .g(sevenSegDecoder_2_segment_g), .f(sevenSegDecoder_2_segment_f), .a(sevenSegDecoder_2_segment_a),
    .b(sevenSegDecoder_2_segment_b), .e(sevenSegDecoder_2_segment_e), .d(sevenSegDecoder_2_segment_d),
    .c(sevenSegDecoder_2_segment_c), .dp(1'b0));
  Counter #(.width(4), .max('h9)) counter_3 (
    .clr(d_ff_2_q), .load(1'b0), .up(1'b1), .count(counter_2_carry), .clk(clock_1_out),
    .carry(counter_3_carry), .Q(counter_3_q));  // open: D
  D_Flip_Flop d_ff_2 (.D(counter_3_carry), .clk(clock_1_out), .Q(d_ff_2_q));  // open: Qn, preset, reset
  sevenSegDecoder sevenSegDecoder_3 (
    .e1(counter_3_q[3]), .e2(counter_3_q[2]), .e3(counter_3_q[1]), .e4(counter_3_q[0]),
    .segment_a(sevenSegDecoder_3_segment_a), .segment_b(sevenSegDecoder_3_segment_b),
    .segment_c(sevenSegDecoder_3_segment_c), .segment_d(sevenSegDecoder_3_segment_d),
    .segment_e(sevenSegDecoder_3_segment_e), .segment_f(sevenSegDecoder_3_segment_f),
    .segment_g(sevenSegDecoder_3_segment_g));
  Counter #(.width(4), .max('h9), .ongoal("load")) counter_4 (
    .clr(d_ff_3_q), .load(1'b0), .up(1'b1), .count(counter_3_carry), .clk(clock_1_out),
    .carry(counter_4_carry), .Q(counter_4_q));  // open: D
  _7_Segment_Display L_7_Segment_Display_3 (
    .g(sevenSegDecoder_3_segment_g), .f(sevenSegDecoder_3_segment_f), .a(sevenSegDecoder_3_segment_a),
    .b(sevenSegDecoder_3_segment_b), .e(sevenSegDecoder_3_segment_e), .d(sevenSegDecoder_3_segment_d),
    .c(sevenSegDecoder_3_segment_c), .dp(1'b0));
  D_Flip_Flop d_ff_3 (.D(counter_4_carry), .clk(clock_1_out), .Q(d_ff_3_q));  // open: Qn, preset, reset
  sevenSegDecoder sevenSegDecoder_4 (
    .e1(counter_4_q[3]), .e2(counter_4_q[2]), .e3(counter_4_q[1]), .e4(counter_4_q[0]),
    .segment_a(sevenSegDecoder_4_segment_a), .segment_b(sevenSegDecoder_4_segment_b),
    .segment_c(sevenSegDecoder_4_segment_c), .segment_d(sevenSegDecoder_4_segment_d),
    .segment_e(sevenSegDecoder_4_segment_e), .segment_f(sevenSegDecoder_4_segment_f),
    .segment_g(sevenSegDecoder_4_segment_g));
  _7_Segment_Display L_7_Segment_Display_4 (
    .g(sevenSegDecoder_4_segment_g), .f(sevenSegDecoder_4_segment_f), .a(sevenSegDecoder_4_segment_a),
    .b(sevenSegDecoder_4_segment_b), .e(sevenSegDecoder_4_segment_e), .d(sevenSegDecoder_4_segment_d),
    .c(sevenSegDecoder_4_segment_c), .dp(1'b0));
  Counter #(.width(4), .max('h9)) counter_5 (
    .clr(d_ff_4_q), .load(1'b0), .up(1'b1), .count(counter_4_carry), .clk(clock_1_out),
    .carry(counter_5_carry), .Q(counter_5_q));  // open: D
  sevenSegDecoder sevenSegDecoder_5 (
    .e1(counter_5_q[3]), .e2(counter_5_q[2]), .e3(counter_5_q[1]), .e4(counter_5_q[0]),
    .segment_a(sevenSegDecoder_5_segment_a), .segment_b(sevenSegDecoder_5_segment_b),
    .segment_c(sevenSegDecoder_5_segment_c), .segment_d(sevenSegDecoder_5_segment_d),
    .segment_e(sevenSegDecoder_5_segment_e), .segment_f(sevenSegDecoder_5_segment_f),
    .segment_g(sevenSegDecoder_5_segment_g));
  D_Flip_Flop d_ff_4 (.D(counter_5_carry), .clk(clock_1_out), .Q(d_ff_4_q));  // open: Qn, preset, reset
  _7_Segment_Display L_7_Segment_Display_5 (
    .g(sevenSegDecoder_5_segment_g), .f(sevenSegDecoder_5_segment_f), .a(sevenSegDecoder_5_segment_a),
    .b(sevenSegDecoder_5_segment_b), .e(sevenSegDecoder_5_segment_e), .d(sevenSegDecoder_5_segment_d),
    .c(sevenSegDecoder_5_segment_c), .dp(1'b0));
  Counter #(.width(4), .max('h9)) counter_6 (
    .clr(d_ff_5_q), .load(1'b0), .up(1'b1), .count(counter_5_carry), .clk(clock_1_out),
    .carry(counter_6_carry), .Q(counter_6_q));  // open: D
  sevenSegDecoder sevenSegDecoder_6 (
    .e1(counter_6_q[3]), .e2(counter_6_q[2]), .e3(counter_6_q[1]), .e4(counter_6_q[0]),
    .segment_a(sevenSegDecoder_6_segment_a), .segment_b(sevenSegDecoder_6_segment_b),
    .segment_c(sevenSegDecoder_6_segment_c), .segment_d(sevenSegDecoder_6_segment_d),
    .segment_e(sevenSegDecoder_6_segment_e), .segment_f(sevenSegDecoder_6_segment_f),
    .segment_g(sevenSegDecoder_6_segment_g));
  D_Flip_Flop d_ff_5 (.D(counter_6_carry), .clk(clock_1_out), .Q(d_ff_5_q));  // open: Qn, preset, reset
  _7_Segment_Display L_7_Segment_Display_6 (
    .g(sevenSegDecoder_6_segment_g), .f(sevenSegDecoder_6_segment_f), .a(sevenSegDecoder_6_segment_a),
    .b(sevenSegDecoder_6_segment_b), .e(sevenSegDecoder_6_segment_e), .d(sevenSegDecoder_6_segment_d),
    .c(sevenSegDecoder_6_segment_c), .dp(1'b0));
  Counter #(.width(4), .max('h9)) counter_7 (
    .clr(d_ff_6_q), .load(1'b0), .up(1'b1), .count(counter_6_carry), .clk(clock_1_out),
    .carry(counter_7_carry), .Q(counter_7_q));  // open: D
  sevenSegDecoder sevenSegDecoder_7 (
    .e1(counter_7_q[3]), .e2(counter_7_q[2]), .e3(counter_7_q[1]), .e4(counter_7_q[0]),
    .segment_a(sevenSegDecoder_7_segment_a), .segment_b(sevenSegDecoder_7_segment_b),
    .segment_c(sevenSegDecoder_7_segment_c), .segment_d(sevenSegDecoder_7_segment_d),
    .segment_e(sevenSegDecoder_7_segment_e), .segment_f(sevenSegDecoder_7_segment_f),
    .segment_g(sevenSegDecoder_7_segment_g));
  D_Flip_Flop d_ff_6 (.D(counter_7_carry), .clk(clock_1_out), .Q(d_ff_6_q));  // open: Qn, preset, reset
  _7_Segment_Display L_7_Segment_Display_7 (
    .g(sevenSegDecoder_7_segment_g), .f(sevenSegDecoder_7_segment_f), .a(sevenSegDecoder_7_segment_a),
    .b(sevenSegDecoder_7_segment_b), .e(sevenSegDecoder_7_segment_e), .d(sevenSegDecoder_7_segment_d),
    .c(sevenSegDecoder_7_segment_c), .dp(1'b0));
  Counter #(.width(4), .max('h9)) counter_8 (
    .clr(undriven), .load(1'b0), .up(1'b1), .count(counter_7_carry), .clk(clock_1_out), .Q(counter_8_q));  // open: D, carry
  sevenSegDecoder sevenSegDecoder_8 (
    .e1(counter_8_q[3]), .e2(counter_8_q[2]), .e3(counter_8_q[1]), .e4(counter_8_q[0]),
    .segment_a(sevenSegDecoder_8_segment_a), .segment_b(sevenSegDecoder_8_segment_b),
    .segment_c(sevenSegDecoder_8_segment_c), .segment_d(sevenSegDecoder_8_segment_d),
    .segment_e(sevenSegDecoder_8_segment_e), .segment_f(sevenSegDecoder_8_segment_f),
    .segment_g(sevenSegDecoder_8_segment_g));
  _7_Segment_Display L_7_Segment_Display_8 (
    .g(sevenSegDecoder_8_segment_g), .f(sevenSegDecoder_8_segment_f), .a(sevenSegDecoder_8_segment_a),
    .b(sevenSegDecoder_8_segment_b), .e(sevenSegDecoder_8_segment_e), .d(sevenSegDecoder_8_segment_d),
    .c(sevenSegDecoder_8_segment_c), .dp(1'b0));
endmodule

module sevenSegDecoder (
  input  e1,
  input  e2,
  input  e3,
  input  e4,
  output segment_a,
  output segment_b,
  output segment_c,
  output segment_d,
  output segment_e,
  output segment_f,
  output segment_g
);

  wire and_1_out, and_2_out, and_3_out, and_4_out, and_5_out, and_6_out, and_7_out, and_8_out, and_9_out,
       and_10_out, and_11_out, and_12_out, and_13_out, and_14_out, and_15_out, and_16_out, and_17_out,
       and_18_out, and_19_out, and_20_out, and_21_out, and_22_out, and_23_out, and_24_out, and_25_out,
       and_26_out, and_27_out, and_28_out, and_29_out, and_30_out, and_31_out, and_32_out, and_33_out,
       and_34_out, and_35_out, and_36_out, not_1_out, not_2_out, not_3_out, not_4_out, not_5_out, not_6_out,
       not_7_out, not_8_out, not_9_out, not_10_out, not_11_out, not_12_out, not_13_out, not_14_out,
       not_15_out, not_16_out, not_17_out, not_18_out, not_19_out, not_20_out, not_21_out, not_22_out,
       not_23_out, not_24_out, not_25_out, not_26_out, not_27_out, not_28_out, not_29_out, not_30_out,
       not_31_out, not_32_out, not_33_out, not_34_out, not_35_out, not_36_out, not_37_out, not_38_out,
       not_39_out, not_40_out, not_41_out, not_42_out, not_43_out, not_44_out, not_45_out;

  not not_1 (not_1_out, e2);
  and and_1 (and_1_out, not_1_out, not_2_out);
  not not_2 (not_2_out, e4);
  not not_3 (not_3_out, e1);
  and and_2 (and_2_out, not_3_out, e3);
  not not_4 (not_4_out, e1);
  and and_3 (and_3_out, not_4_out, e2, e4);
  and and_4 (and_4_out, e2, e3);
  not not_5 (not_5_out, e2);
  and and_5 (and_5_out, e1, not_5_out, not_6_out);
  not not_6 (not_6_out, e3);
  and and_6 (and_6_out, e1, not_7_out);
  not not_7 (not_7_out, e4);
  not not_8 (not_8_out, e1);
  and and_7 (and_7_out, not_8_out, not_9_out);
  not not_9 (not_9_out, e2);
  not not_10 (not_10_out, e1);
  and and_8 (and_8_out, not_10_out, not_11_out, not_12_out);
  not not_11 (not_11_out, e3);
  not not_12 (not_12_out, e4);
  not not_13 (not_13_out, e2);
  and and_9 (and_9_out, not_13_out, not_14_out);
  not not_14 (not_14_out, e3);
  not not_15 (not_15_out, e2);
  and and_10 (and_10_out, not_15_out, not_16_out);
  not not_16 (not_16_out, e4);
  not not_17 (not_17_out, e1);
  and and_11 (and_11_out, not_17_out, e3, e4);
  not not_18 (not_18_out, e3);
  and and_12 (and_12_out, e1, not_18_out, e4);
  not not_19 (not_19_out, e1);
  and and_13 (and_13_out, not_19_out, not_20_out);
  not not_20 (not_20_out, e3);
  not not_21 (not_21_out, e1);
  and and_14 (and_14_out, not_21_out, e4);
  not not_22 (not_22_out, e3);
  and and_15 (and_15_out, not_22_out, e4);
  not not_23 (not_23_out, e1);
  and and_16 (and_16_out, not_23_out, e2);
  and and_17 (and_17_out, e1, not_24_out);
  not not_24 (not_24_out, e2);
  not not_25 (not_25_out, e1);
  not not_26 (not_26_out, e2);
  and and_18 (and_18_out, not_25_out, not_26_out, not_27_out);
  not not_27 (not_27_out, e4);
  not not_28 (not_28_out, e2);
  and and_19 (and_19_out, not_28_out, e3, e4);
  not not_29 (not_29_out, e3);
  and and_20 (and_20_out, e2, not_29_out, e4);
  and and_21 (and_21_out, e2, e3, not_30_out);
  not not_30 (not_30_out, e4);
  and and_22 (and_22_out, e1, not_31_out);
  not not_31 (not_31_out, e3);
  not not_32 (not_32_out, e2);
  and and_23 (and_23_out, not_32_out, not_33_out);
  not not_33 (not_33_out, e4);
  and and_24 (and_24_out, e3, not_34_out);
  not not_34 (not_34_out, e4);
  and and_25 (and_25_out, e1, e3);
  and and_26 (and_26_out, e1, e2);
  not not_35 (not_35_out, e3);
  and and_27 (and_27_out, not_35_out, not_36_out);
  not not_36 (not_36_out, e4);
  not not_37 (not_37_out, e1);
  and and_28 (and_28_out, not_37_out, e2, not_38_out);
  not not_38 (not_38_out, e3);
  and and_29 (and_29_out, e2, not_39_out);
  not not_39 (not_39_out, e4);
  and and_30 (and_30_out, e1, not_40_out);
  not not_40 (not_40_out, e2);
  and and_31 (and_31_out, e1, e3);
  not not_41 (not_41_out, e2);
  and and_32 (and_32_out, not_41_out, e3);
  and and_33 (and_33_out, e3, not_42_out);
  not not_42 (not_42_out, e4);
  not not_43 (not_43_out, e1);
  and and_34 (and_34_out, not_43_out, e2, not_44_out);
  not not_44 (not_44_out, e3);
  and and_35 (and_35_out, e1, not_45_out);
  not not_45 (not_45_out, e2);
  and and_36 (and_36_out, e1, e4);
  or or_1 (segment_c, and_13_out, and_14_out, and_15_out, and_16_out, and_17_out);
  or or_2 (segment_d, and_18_out, and_19_out, and_20_out, and_21_out, and_22_out);
  or or_3 (segment_e, and_23_out, and_24_out, and_25_out, and_26_out);
  or or_4 (segment_f, and_27_out, and_28_out, and_29_out, and_30_out, and_31_out);
  or or_5 (segment_g, and_32_out, and_33_out, and_34_out, and_35_out, and_36_out);
  or or_6 (segment_a, and_1_out, and_2_out, and_3_out, and_4_out, and_5_out, and_6_out);
  or or_7 (segment_b, and_7_out, and_8_out, and_9_out, and_10_out, and_11_out, and_12_out);
endmodule
