// Logisim project ALU.circ as structural Verilog: 1 circuit, main circuit ALU
module ALU (
  input  [31:0] A,
  input  [31:0] B,
  input  [4:0] Shift,
  input  [3:0] Codop,
  input  CarryIn,
  output [31:0] S,
  output [3:0] Flags
);

  wire adder_1_cout, adder_2_cout, and_1_out, and_2_out, and_6_out, and_7_out, and_8_out, and_9_out,
       and_10_out, bitselector_1_out, bitselector_2_out, multiplexer_2_out, multiplexer_3_out, not_3_out,
       not_4_out, or_2_out, subtractor_1_bout, xor_2_out, xor_3_out, xor_4_out;
  wire [1:0] multiplexer_4_out;
  wire [4:0] subtractor_2_out, subtractor_3_out;
  wire [31:0] adder_1_out, adder_2_out, and_3_out, and_4_out, and_5_out, multiplexer_1_out, multiplier_1_out,
       not_1_out, not_2_out, or_1_out, shifter_1_out, shifter_2_out, shifter_3_out, shifter_4_out,
       subtractor_1_out, xor_1_out;

  and and_1 (and_1_out, Codop[2], CarryIn);
  and and_2 (and_2_out, Codop[2], ~CarryIn);  // AND_Gate
  assign and_3_out = A & B;  // AND_Gate and_3, 32 bits wide
  assign xor_1_out = A ^ B;  // XOR_Gate xor_1, 32 bits wide
  Shifter #(.width(32)) shifter_1 (.in(B), .\dist (Shift), .out(shifter_1_out));
  Shifter #(.shift("lr"), .width(32)) shifter_2 (.in(B), .\dist (Shift), .out(shifter_2_out));
  Shifter #(.shift("ar"), .width(32)) shifter_3 (.in(B), .\dist (Shift), .out(shifter_3_out));
  Adder #(.width(32)) adder_1 (.a(A), .b(B), .out(adder_1_out), .cin(and_1_out), .cout(adder_1_cout));
  Subtractor #(.width(32)) subtractor_1 (
    .a(B), .b(A), .out(subtractor_1_out), .bin(and_2_out), .bout(subtractor_1_bout));
  Shifter #(.shift("rr"), .width(32)) shifter_4 (.in(B), .\dist (Shift), .out(shifter_4_out));
  assign and_4_out = A & B;  // AND_Gate and_4, 32 bits wide
  assign not_1_out = ~A;  // NOT_Gate not_1, 32 bits wide
  assign or_1_out = A | B;  // OR_Gate or_1, 32 bits wide
  Multiplier #(.width(32)) multiplier_1 (.a(A), .b(B), .out(multiplier_1_out), .cin({32{1'b0}}));  // open: cout
  assign not_2_out = ~A;  // NOT_Gate not_2, 32 bits wide
  not not_3 (not_3_out, subtractor_1_bout);
  Adder #(.width(32)) adder_2 (.a(not_1_out), .b(32'h1), .out(adder_2_out), .cout(adder_2_cout));  // open: cin
  assign and_5_out = ~A & B;  // AND_Gate and_5, 32 bits wide
  not not_4 (not_4_out, Codop[0]);
  Multiplexer #(.select(4), .width(32)) multiplexer_1 (
    .in0(and_3_out), .in1(xor_1_out), .in2(shifter_1_out), .in3(shifter_2_out), .in4(shifter_3_out),
    .in5(adder_1_out), .in6(subtractor_1_out), .in7(shifter_4_out), .in8(and_4_out), .in9(adder_2_out),
    .in10(subtractor_1_out), .in11(adder_1_out), .in12(or_1_out), .in13(multiplier_1_out), .in14(and_5_out),
    .in15(not_2_out), .out(multiplexer_1_out), .sel(Codop));
  Multiplexer multiplexer_2 (.in0(adder_1_cout), .in1(not_3_out), .out(multiplexer_2_out), .sel(not_4_out));
  // Probe on multiplexer_1_out
  Multiplexer multiplexer_3 (.in0(multiplexer_2_out), .in1(adder_2_cout), .out(multiplexer_3_out), .sel(and_6_out));
  and and_6 (and_6_out, ~Codop[2], ~Codop[1]);  // AND_Gate
  Multiplexer #(.select(4), .width(2)) multiplexer_4 (
    .in0(2'b00), .in1(2'b00), .in2(2'b11), .in3(2'b10), .in4(2'b10), .in5(2'b01), .in6(2'b01), .in7(2'b10),
    .in8(2'b00), .in9(2'b01), .in10(2'b01), .in11(2'b01), .in12(2'b00), .in13(2'b00), .in14(2'b00),
    .in15(2'b00), .out(multiplexer_4_out), .sel(Codop));
  or or_2 (or_2_out, ~Codop[0], Codop[1]);  // OR_Gate
  Multiplexer #(.width(32)) multiplexer_5 (.in0(multiplexer_1_out), .in1(B), .out(S), .sel(and_7_out));
  and and_7 (and_7_out, or_2_out, ~Codop[2], Codop[3]);  // AND_Gate
  xor xor_2 (xor_2_out, Codop[1], Codop[2]);
  and and_8 (and_8_out, xor_2_out, Codop[0]);
  Comparator #(.width(32)) comparator_1 (
    .a(multiplexer_1_out), .b({32{1'b0}}), .eq(Flags[2]), .lt(Flags[3]));  // open: gt
  and and_9 (and_9_out, ~xor_2_out, Codop[0]);  // AND_Gate
  and and_10 (and_10_out, ~and_9_out, B[31]);  // AND_Gate
  BitSelector #(.width(32)) bitselector_1 (.in(B), .out(bitselector_1_out), .sel(subtractor_3_out));
  Subtractor #(.width(5)) subtractor_2 (.a({5{1'b0}}), .b(Shift), .out(subtractor_2_out));  // open: bin, bout
  Subtractor #(.width(5)) subtractor_3 (.a(Shift), .b(5'b00001), .out(subtractor_3_out));  // open: bin, bout
  xor xor_3 (xor_3_out, Flags[3], and_10_out);
  ExactlyOne xor_4 (.out(xor_4_out), .in0(and_10_out), .in1(and_8_out), .in2(A[31]));
  BitSelector #(.width(32)) bitselector_2 (.in(B), .out(bitselector_2_out), .sel(subtractor_2_out));
  and and_11 (Flags[0], xor_3_out, xor_4_out, multiplexer_4_out[0]);
  Multiplexer #(.select(2)) multiplexer_6 (
    .in0(1'b0), .in1(multiplexer_3_out), .in2(bitselector_1_out), .in3(bitselector_2_out), .out(Flags[1]),
    .sel(multiplexer_4_out));

  // Other names for the same wires on the sheet: V = Flags[0]; C = Flags[1]; Z = Flags[2]; N = Flags[3];
  //   Op[3:0] = Codop; S_t[4:0] = Shift

  // Notes on the sheet:
  //   Note: for ROR, C = N
  //   Note 2: assume that shift > 0 for LSL and LSR
  //   2=LSL
  //   1=ADC, SBC, CMP, CMN
  //   3=LSR, ROR
  //   TST, CMP, CMN
endmodule
