// Logisim project ARM_ALL.circ as structural Verilog: 1 circuit, main circuit main
module main (
  input  clock,
  input  rst,
  output r01,
  output r11,
  output r21,
  output r31,
  output r02,
  output r12,
  output r22,
  output r32,
  output r03,
  output r13,
  output r23,
  output r33,
  output r04,
  output r14,
  output r24,
  output r34
);

  wire Clk, Load, not_1_out, ShiftImme, Store;
  wire [2:0] RegA, RegB, RegDest;
  wire [3:0] Codop, Flags;
  wire [4:0] Immo5, Shifter;
  wire [7:0] Adr, AdrRom;
  wire [15:0] Inst;
  wire [31:0] AOut, BancRegistre_1_p4, BancRegistre_1_p6, BancRegistre_1_p7, BancRegistre_1_p8,
       BancRegistre_1_p11, DataOut, multiplexer_1_out, S;

  // Probe on BancRegistre_1_p4
  BitSelector #(.width(32)) bitselector_1 (.in(BancRegistre_1_p4), .out(r01), .sel({5{1'b0}}));
  BitSelector #(.width(32)) bitselector_2 (.in(BancRegistre_1_p4), .out(r02), .sel(5'b00001));
  BitSelector #(.width(32)) bitselector_3 (.in(BancRegistre_1_p4), .out(r03), .sel(5'b00010));
  BitSelector #(.width(32)) bitselector_4 (.in(BancRegistre_1_p4), .out(r04), .sel(5'b00011));
  // Probe on BancRegistre_1_p6
  // Probe on Inst
  BitSelector #(.width(32)) bitselector_5 (.in(BancRegistre_1_p6), .out(r11), .sel({5{1'b0}}));
  BitSelector #(.width(32)) bitselector_6 (.in(BancRegistre_1_p6), .out(r12), .sel(5'b00001));
  BitSelector #(.width(32)) bitselector_7 (.in(BancRegistre_1_p6), .out(r13), .sel(5'b00010));
  BitSelector #(.width(32)) bitselector_8 (.in(BancRegistre_1_p6), .out(r14), .sel(5'b00011));
  Multiplexer #(.width(32), .enable("false")) multiplexer_1 (
    .in0(DataOut), .in1(S), .out(multiplexer_1_out), .sel(not_1_out));
  not not_1 (not_1_out, Load);
  // Probe on AdrRom
  mainControl mainControl_1 (
    .Inst(Inst), .Clk(Clk), .Reset(rst), .PCOut(AdrRom), .Store(Store), .Codop(Codop), .Rm(RegA),
    .Rd(RegDest), .Rn(RegB), .Imm8(Adr), .Imm5(Immo5), .Flags(Flags), .Load(Load), .ShifterImme(ShiftImme));
  BitSelector #(.width(32)) bitselector_9 (.in(BancRegistre_1_p7), .out(r21), .sel({5{1'b0}}));
  BitSelector #(.width(32)) bitselector_10 (.in(BancRegistre_1_p7), .out(r22), .sel(5'b00001));
  BitSelector #(.width(32)) bitselector_11 (.in(BancRegistre_1_p7), .out(r23), .sel(5'b00010));
  BitSelector #(.width(32)) bitselector_12 (.in(BancRegistre_1_p7), .out(r24), .sel(5'b00011));
  Multiplexer #(.width(5), .enable("false")) multiplexer_2 (
    .in0(AOut[4:0]), .in1(Immo5), .out(Shifter), .sel(ShiftImme));
  BitSelector #(.width(32)) bitselector_13 (.in(BancRegistre_1_p8), .out(r31), .sel({5{1'b0}}));
  BitSelector #(.width(32)) bitselector_14 (.in(BancRegistre_1_p8), .out(r32), .sel(5'b00001));
  BitSelector #(.width(32)) bitselector_15 (.in(BancRegistre_1_p8), .out(r33), .sel(5'b00010));
  BitSelector #(.width(32)) bitselector_16 (.in(BancRegistre_1_p8), .out(r34), .sel(5'b00011));
  // Probe on BancRegistre_1_p7
  // BancRegistre BancRegistre_1: pin names not known; wires that end beside it: multiplexer_1_out, RegDest, Clk, BancRegistre_1_p4, rst, BancRegistre_1_p6, BancRegistre_1_p7, BancRegistre_1_p8, RegA, RegB, BancRegistre_1_p11, AOut
  ALU ALU_1 (
    .S(S), .Flags(Flags), .A(AOut), .B(BancRegistre_1_p11), .Shift(Shifter), .CarryIn(Flags[2]), .Codop(Codop));
  Button Button_1 (.out(Clk));
  ROM #(.dataWidth(32)) DataStorage (.addr(Adr), .data(DataOut));
  ROM #(.dataWidth(16)) Program (.addr(AdrRom), .data(Inst));

  // Other names for the same wires on the sheet: Reset = rst

  // Notes on the sheet:
  //   contents of DataStorage (hex, n*v repeats v):
  //   1 3 2 4
  //   contents of Program (hex, n*v repeats v):
  //   9800 9900 1a08 d005 9a02 9801 c9 4308
endmodule
