// Logisim project Alu32.circ as structural Verilog: 19 circuits, main circuit main
module main (
  input  A,
  input  B,
  input  Sub,
  input  Less,
  input  Cin,
  output RESULT,
  output [2:0] out_7,
  output Cout,
  output Set
);

  wire and_1_out, nor_1_out, or_1_out, xor_1_out, xor_2_out;

  xor xor_1 (xor_1_out, B, Sub);
  and and_1 (and_1_out, A, B);
  or or_1 (or_1_out, A, B);
  xor xor_2 (xor_2_out, A, B);
  nor nor_1 (nor_1_out, A, B);
  Adder #(.width(1)) adder_1 (.a(A), .b(xor_1_out), .out(Set), .cin(Cin), .cout(Cout));
  Multiplexer #(.select(3), .enable("false")) multiplexer_1 (
    .in0(and_1_out), .in1(or_1_out), .in2(xor_2_out), .in3(nor_1_out), .in4(Set), .in5(Less), .out(RESULT),
    .sel(out_7));  // open: in6, in7
endmodule

module Add (
  input  [31:0] A,
  input  [31:0] B,
  output [31:0] S,
  output overflow,
  output V
);

  wire and_1_out, and_2_out, and_3_out, and_4_out, bitselector_1_out, bitselector_2_out, bitselector_3_out,
       bitselector_4_out, bitselector_5_out, bitselector_6_out, not_1_out, not_2_out, not_3_out;

  Adder #(.width(32)) adder_1 (.a(A), .b(B), .out(S), .cout(overflow));  // open: cin
  BitSelector #(.width(32)) bitselector_1 (.in(A), .out(bitselector_1_out), .sel({5{1'b1}}));
  BitSelector #(.width(32)) bitselector_2 (.in(B), .out(bitselector_2_out), .sel({5{1'b1}}));
  BitSelector #(.width(32)) bitselector_3 (.in(A), .out(bitselector_3_out), .sel({5{1'b1}}));
  BitSelector #(.width(32)) bitselector_4 (.in(B), .out(bitselector_4_out), .sel({5{1'b1}}));
  and and_1 (and_1_out, bitselector_1_out, bitselector_2_out);
  not not_1 (not_1_out, bitselector_3_out);
  and and_2 (and_2_out, not_1_out, not_2_out);
  not not_2 (not_2_out, bitselector_4_out);
  BitSelector #(.width(32)) bitselector_5 (.in(S), .out(bitselector_5_out), .sel({5{1'b1}}));
  BitSelector #(.width(32)) bitselector_6 (.in(S), .out(bitselector_6_out), .sel({5{1'b1}}));
  not not_3 (not_3_out, bitselector_5_out);
  and and_3 (and_3_out, not_3_out, and_1_out);
  and and_4 (and_4_out, bitselector_6_out, and_2_out);
  or or_1 (V, and_3_out, and_4_out);
endmodule

module AND_ALU (
  input  [31:0] A,
  input  [31:0] B,
  output [31:0] S
);

  assign S = A & B;  // AND_Gate and_1, 32 bits wide

  // Notes on the sheet:
  //   AND
endmodule

module EOR (
  input  [31:0] A,
  input  [31:0] B,
  output [31:0] S
);

  assign S = A ^ B;  // XOR_Gate xor_1, 32 bits wide
endmodule

module LSL (
  input  [31:0] B,
  input  [4:0] Shifter_LSL,
  output [31:0] S
);

  Shifter #(.width(32)) shifter_1 (.in(B), .\dist (Shifter_LSL), .out(S));
endmodule

module ASR (
  input  [31:0] B,
  input  [4:0] Shifter_ASR,
  output [31:0] S
);

  Shifter #(.width(32), .shift("ar")) shifter_1 (.in(B), .\dist (Shifter_ASR), .out(S));
endmodule

module LSR (
  input  [31:0] B,
  input  [4:0] Shifter_LSR,
  output [31:0] S
);

  Shifter #(.width(32), .shift("lr")) shifter_1 (.in(B), .\dist (Shifter_LSR), .out(S));
endmodule

module ROR_ALU (
  input  [31:0] B,
  input  [4:0] Shifter_ROR,
  output [31:0] S
);

  Shifter #(.width(32), .shift("rr")) shifter_1 (.in(B), .\dist (Shifter_ROR), .out(S));
endmodule

module CMP (
  input  [31:0] A,
  input  [31:0] B,
  output [31:0] S,
  output Cout,
  output V
);

  wire and_1_out, and_2_out, and_3_out, and_4_out, bitselector_1_out, bitselector_2_out, bitselector_3_out,
       bitselector_4_out, bitselector_5_out, bitselector_6_out, not_1_out, not_2_out, not_3_out;

  BitSelector #(.width(32)) bitselector_1 (.in(B), .out(bitselector_1_out), .sel({5{1'b1}}));
  not not_1 (not_1_out, bitselector_1_out);
  BitSelector #(.width(32)) bitselector_2 (.in(A), .out(bitselector_2_out), .sel({5{1'b1}}));
  BitSelector #(.width(32)) bitselector_3 (.in(B), .out(bitselector_3_out), .sel({5{1'b1}}));
  BitSelector #(.width(32)) bitselector_4 (.in(A), .out(bitselector_4_out), .sel({5{1'b1}}));
  not not_2 (not_2_out, bitselector_4_out);
  Subtractor #(.width(32)) subtractor_1 (.a(A), .b(B), .out(S), .bout(Cout));  // open: bin
  and and_1 (and_1_out, not_1_out, bitselector_2_out);
  and and_2 (and_2_out, bitselector_3_out, not_2_out);
  BitSelector #(.width(32)) bitselector_5 (.in(S), .out(bitselector_5_out), .sel({5{1'b1}}));
  not not_3 (not_3_out, bitselector_5_out);
  BitSelector #(.width(32)) bitselector_6 (.in(S), .out(bitselector_6_out), .sel({5{1'b1}}));
  and and_3 (and_3_out, not_3_out, and_1_out);
  and and_4 (and_4_out, bitselector_6_out, and_2_out);
  or or_1 (V, and_3_out, and_4_out);
endmodule

module CMN (
  input  [31:0] A,
  input  [31:0] B,
  output [31:0] S,
  output Cout,
  output V
);

  wire and_1_out, and_2_out, and_3_out, and_4_out, bitselector_1_out, bitselector_2_out, bitselector_3_out,
       bitselector_4_out, bitselector_5_out, bitselector_6_out, not_1_out, not_2_out, not_3_out;

  BitSelector #(.width(32)) bitselector_1 (.in(B), .out(bitselector_1_out), .sel({5{1'b1}}));
  BitSelector #(.width(32)) bitselector_2 (.in(A), .out(bitselector_2_out), .sel({5{1'b1}}));
  BitSelector #(.width(32)) bitselector_3 (.in(B), .out(bitselector_3_out), .sel({5{1'b1}}));
  BitSelector #(.width(32)) bitselector_4 (.in(A), .out(bitselector_4_out), .sel({5{1'b1}}));
  Adder #(.width(32)) adder_1 (.a(A), .b(B), .out(S), .cout(Cout));  // open: cin
  not not_1 (not_1_out, bitselector_3_out);
  not not_2 (not_2_out, bitselector_4_out);
  and and_1 (and_1_out, bitselector_1_out, bitselector_2_out);
  and and_2 (and_2_out, not_1_out, not_2_out);
  BitSelector #(.width(32)) bitselector_5 (.in(S), .out(bitselector_5_out), .sel({5{1'b1}}));
  BitSelector #(.width(32)) bitselector_6 (.in(S), .out(bitselector_6_out), .sel({5{1'b1}}));
  not not_3 (not_3_out, bitselector_5_out);
  and and_3 (and_3_out, not_3_out, and_1_out);
  and and_4 (and_4_out, bitselector_6_out, and_2_out);
  or or_1 (V, and_3_out, and_4_out);
endmodule

module RSB (
  input  [31:0] B,
  output [31:0] S
);

  Negator #(.width(32)) negator_1 (.in(B), .out(S));
endmodule

module ORR (
  input  [31:0] A,
  input  [31:0] B,
  output [31:0] S
);

  assign S = A | B;  // OR_Gate or_1, 32 bits wide
endmodule

module MUL (
  input  [31:0] A,
  input  [31:0] B,
  output [31:0] S,
  output [31:0] Cout
);

  Multiplier #(.width(32)) multiplier_1 (.a(A), .b(B), .out(S), .cout(Cout));  // open: cin
endmodule

module BIC (
  input  [31:0] A,
  input  [31:0] B,
  output [31:0] S
);

  wire [31:0] not_1_out;

  assign not_1_out = ~B;  // NOT_Gate not_1, 32 bits wide
  assign S = A & not_1_out;  // AND_Gate and_1, 32 bits wide
endmodule

module MVN (
  input  [31:0] B,
  output [31:0] S
);

  assign S = ~B;  // NOT_Gate not_1, 32 bits wide
endmodule

module ADC (
  input  [31:0] A,
  input  Cin,
  input  [31:0] B,
  output [31:0] S,
  output Cout,
  output V
);

  wire and_1_out, and_2_out, and_3_out, and_4_out, bitselector_1_out, bitselector_2_out, bitselector_3_out,
       bitselector_4_out, bitselector_5_out, bitselector_6_out, not_1_out, not_2_out, not_3_out;

  Adder #(.width(32)) adder_1 (.a(A), .b(B), .out(S), .cin(Cin), .cout(Cout));
  BitSelector #(.width(32)) bitselector_1 (.in(B), .out(bitselector_1_out), .sel({5{1'b1}}));
  BitSelector #(.width(32)) bitselector_2 (.in(A), .out(bitselector_2_out), .sel({5{1'b1}}));
  BitSelector #(.width(32)) bitselector_3 (.in(B), .out(bitselector_3_out), .sel({5{1'b1}}));
  not not_1 (not_1_out, bitselector_3_out);
  BitSelector #(.width(32)) bitselector_4 (.in(A), .out(bitselector_4_out), .sel({5{1'b1}}));
  not not_2 (not_2_out, bitselector_4_out);
  and and_1 (and_1_out, bitselector_1_out, bitselector_2_out);
  and and_2 (and_2_out, not_1_out, not_2_out);
  BitSelector #(.width(32)) bitselector_5 (.in(S), .out(bitselector_5_out), .sel({5{1'b1}}));
  BitSelector #(.width(32)) bitselector_6 (.in(S), .out(bitselector_6_out), .sel({5{1'b1}}));
  not not_3 (not_3_out, bitselector_5_out);
  and and_3 (and_3_out, not_3_out, and_1_out);
  and and_4 (and_4_out, bitselector_6_out, and_2_out);
  or or_1 (V, and_3_out, and_4_out);
endmodule

module SBC (
  input  [31:0] A,
  input  Cin,
  input  [31:0] B,
  output [31:0] S,
  output Cout,
  output V
);

  wire and_1_out, and_2_out, and_3_out, and_4_out, bitselector_1_out, bitselector_2_out, bitselector_3_out,
       bitselector_4_out, bitselector_5_out, bitselector_6_out, not_1_out, not_2_out, not_3_out;

  BitSelector #(.width(32)) bitselector_1 (.in(B), .out(bitselector_1_out), .sel({5{1'b1}}));
  not not_1 (not_1_out, bitselector_1_out);
  BitSelector #(.width(32)) bitselector_2 (.in(A), .out(bitselector_2_out), .sel({5{1'b1}}));
  BitSelector #(.width(32)) bitselector_3 (.in(B), .out(bitselector_3_out), .sel({5{1'b1}}));
  not not_2 (not_2_out, bitselector_4_out);
  BitSelector #(.width(32)) bitselector_4 (.in(A), .out(bitselector_4_out), .sel({5{1'b1}}));
  Subtractor #(.width(32)) subtractor_1 (.a(A), .b(B), .out(S), .bin(Cin), .bout(Cout));
  and and_1 (and_1_out, not_1_out, bitselector_2_out);
  and and_2 (and_2_out, bitselector_3_out, not_2_out);
  BitSelector #(.width(32)) bitselector_5 (.in(S), .out(bitselector_5_out), .sel({5{1'b1}}));
  BitSelector #(.width(32)) bitselector_6 (.in(S), .out(bitselector_6_out), .sel({5{1'b1}}));
  not not_3 (not_3_out, bitselector_5_out);
  and and_3 (and_3_out, not_3_out, and_1_out);
  and and_4 (and_4_out, bitselector_6_out, and_2_out);
  or or_1 (V, and_3_out, and_4_out);
endmodule

module TST (
  input  [31:0] A,
  input  [31:0] B,
  output [31:0] S
);

  assign S = A & B;  // AND_Gate and_1, 32 bits wide
endmodule

module ALU_32 (
  input  [31:0] A,
  input  [31:0] B,
  input  [4:0] Shifter,
  input  Cin,
  input  [3:0] Codop,
  output [31:0] S,
  output [3:0] Flags
);

  wire and_1_out, and_2_out, and_3_out, and_4_out, and_5_out, and_6_out, and_7_out, and_8_out,
       comparator_1_eq, comparator_2_eq, comparator_3_eq, comparator_4_eq, comparator_5_eq, comparator_6_eq,
       comparator_7_eq, comparator_8_eq, CoutADC, CoutCMN, CoutCMP, CoutSBC, VADC, VCMN, VCMP, VSBC;
  wire [31:0] CoutMUL, SADC, SAND, SASR, SBIC, SCMN, SCMP, SEOR, SLSL, SLSR, SMUL, SMVN, SORR, SROR, SRSB,
       SSBC, STST;

  AND_ALU AND_ALU_1 (.A(A), .B(B), .S(SAND));
  EOR EOR_1 (.A(A), .B(B), .S(SEOR));
  LSL LSL_1 (.B(B), .Shifter_LSL(Shifter), .S(SLSL));
  LSR LSR_1 (.B(B), .Shifter_LSR(Shifter), .S(SLSR));
  Comparator #(.width(4)) comparator_1 (.a(4'b0101), .b(Codop), .eq(comparator_1_eq));  // open: gt, lt
  and and_1 (and_1_out, comparator_1_eq, VADC);
  Comparator #(.width(4)) comparator_2 (.a(4'b0110), .b(Codop), .eq(comparator_2_eq));  // open: gt, lt
  and and_2 (and_2_out, comparator_2_eq, VSBC);
  Comparator #(.width(4)) comparator_3 (.a(4'b1011), .b(Codop), .eq(comparator_3_eq));  // open: gt, lt
  and and_3 (and_3_out, comparator_3_eq, VCMP);
  Comparator #(.width(4)) comparator_4 (.a(4'b1100), .b(Codop), .eq(comparator_4_eq));  // open: gt, lt
  and and_4 (and_4_out, comparator_4_eq, VCMN);
  ASR ASR_1 (.B(B), .Shifter_ASR(Shifter), .S(SASR));
  ADC ADC_1 (.A(A), .B(B), .S(SADC), .Cin(Cin), .Cout(CoutADC), .V(VADC));
  SBC SBC_1 (.A(A), .B(B), .S(SSBC), .Cin(Cin), .Cout(CoutSBC), .V(VSBC));
  ROR_ALU ROR_ALU_1 (.B(B), .Shifter_ROR(Shifter), .S(SROR));
  or or_1 (Flags[2], and_1_out, and_2_out, and_3_out, and_4_out);
  TST TST_1 (.A(A), .B(B), .S(STST));
  RSB RSB_1 (.B(B), .S(SRSB));
  CMP CMP_1 (.A(A), .B(B), .S(SCMP), .Cout(CoutCMP), .V(VCMP));
  CMN CMN_1 (.A(A), .B(B), .S(SCMN), .Cout(CoutCMN), .V(VCMN));
  Comparator #(.width(4)) comparator_5 (.a(4'b0101), .b(Codop), .eq(comparator_5_eq));  // open: gt, lt
  Comparator #(.width(4)) comparator_6 (.a(4'b0110), .b(Codop), .eq(comparator_6_eq));  // open: gt, lt
  Comparator #(.width(4)) comparator_7 (.a(4'b1011), .b(Codop), .eq(comparator_7_eq));  // open: gt, lt
  Comparator #(.width(4)) comparator_8 (.a(4'b1100), .b(Codop), .eq(comparator_8_eq));  // open: gt, lt
  ORR ORR_1 (.A(A), .B(B), .S(SORR));
  MUL MUL_1 (.A(A), .B(B), .S(SMUL), .Cout(CoutMUL));
  BIC BIC_1 (.A(A), .B(B), .S(SBIC));
  MVN MVN_1 (.B(B), .S(SMVN));
  and and_5 (and_5_out, comparator_5_eq, CoutADC);
  and and_6 (and_6_out, comparator_6_eq, CoutSBC);
  and and_7 (and_7_out, comparator_7_eq, CoutCMP);
  and and_8 (and_8_out, comparator_8_eq, CoutCMN);
  or or_2 (Flags[3], and_5_out, and_6_out, and_7_out, and_8_out);
  BitSelector #(.width(32)) bitselector_1 (.in(S), .out(Flags[1]), .sel({5{1'b1}}));
  Multiplexer #(.select(4), .width(32), .enable("false")) multiplexer_1 (
    .in0(SAND), .in1(SEOR), .in2(SLSL), .in3(SLSR), .in4(SASR), .in5(SADC), .in6(SSBC), .in7(SROR),
    .in8(STST), .in9(SRSB), .in10(SCMP), .in11(SCMN), .in12(SORR), .in13(SMUL), .in14(SBIC), .in15(SMVN),
    .out(S), .sel(Codop));
  Comparator #(.width(32)) comparator_9 (.a(S), .b({32{1'b0}}), .eq(Flags[0]));  // open: gt, lt

  // Other names for the same wires on the sheet: Z = Flags[0]; N = Flags[1]; V = Flags[2]; C = Flags[3]
endmodule
