// Logisim project BancDeRegistres.circ as structural Verilog: 1 circuit, main circuit BancRegistre
module BancRegistre (
  input  [31:0] Input_bus_2,
  input  [2:0] Input_bus_1,
  input  Input_1,
  input  Input_2,
  input  [2:0] Input_bus_4,
  input  [2:0] Input_bus_3,
  output [31:0] Output_bus_7,
  output [31:0] Output_bus_10,
  output [31:0] Output_bus_9,
  output [31:0] Output_bus_8,
  output [31:0] Output_bus_6,
  output [31:0] Output_bus_5,
  output [31:0] Output_bus_3,
  output [31:0] Output_bus_2,
  output [31:0] Output_bus_4,
  output [31:0] Output_bus_1
);

  wire decoder_1_out0, decoder_1_out1, decoder_1_out2, decoder_1_out3, decoder_1_out4, decoder_1_out5,
       decoder_1_out6, decoder_1_out7;

  Decoder #(.select(3), .enable("false")) decoder_1 (
    .out0(decoder_1_out0), .out1(decoder_1_out1), .out2(decoder_1_out2), .out3(decoder_1_out3),
    .out4(decoder_1_out4), .out5(decoder_1_out5), .out6(decoder_1_out6), .out7(decoder_1_out7),
    .sel(Input_bus_4));
  Register #(.width(32)) register_1 (
    .D(Input_bus_2), .en(decoder_1_out0), .clk(Input_1), .Q(Output_bus_10), .clr(Input_2));
  Register #(.width(32)) register_2 (
    .D(Input_bus_2), .en(decoder_1_out1), .clk(Input_1), .Q(Output_bus_9), .clr(Input_2));
  Register #(.width(32)) register_3 (
    .D(Input_bus_2), .en(decoder_1_out2), .clk(Input_1), .Q(Output_bus_8), .clr(Input_2));
  Register #(.width(32)) register_4 (
    .D(Input_bus_2), .en(decoder_1_out3), .clk(Input_1), .Q(Output_bus_6), .clr(Input_2));
  Register #(.width(32)) register_5 (
    .D(Input_bus_2), .en(decoder_1_out4), .clk(Input_1), .Q(Output_bus_5), .clr(Input_2));
  Register #(.width(32)) register_6 (
    .D(Input_bus_2), .en(decoder_1_out5), .clk(Input_1), .Q(Output_bus_3), .clr(Input_2));
  Register #(.width(32)) register_7 (
    .D(Input_bus_2), .en(decoder_1_out6), .clk(Input_1), .Q(Output_bus_2), .clr(Input_2));
  Register #(.width(32)) register_8 (
    .D(Input_bus_2), .en(decoder_1_out7), .clk(Input_1), .Q(Output_bus_4), .clr(Input_2));
  Multiplexer #(.select(3), .width(32), .enable("false")) multiplexer_1 (
    .in0(Output_bus_10), .in1(Output_bus_9), .in2(Output_bus_8), .in3(Output_bus_6), .in4(Output_bus_5),
    .in5(Output_bus_3), .in6(Output_bus_2), .in7(Output_bus_4), .out(Output_bus_7), .sel(Input_bus_1));
  Multiplexer #(.select(3), .width(32), .enable("false")) multiplexer_2 (
    .in0(Output_bus_10), .in1(Output_bus_9), .in2(Output_bus_8), .in3(Output_bus_6), .in4(Output_bus_5),
    .in5(Output_bus_3), .in6(Output_bus_2), .in7(Output_bus_4), .out(Output_bus_1), .sel(Input_bus_3));

  // Other names for the same wires on the sheet: r0[31:0] = Output_bus_10; r1[31:0] = Output_bus_9;
  //   r2[31:0] = Output_bus_8; r3[31:0] = Output_bus_6; r4[31:0] = Output_bus_5; r5[31:0] = Output_bus_3;
  //   r6[31:0] = Output_bus_2; r7[31:0] = Output_bus_4
endmodule
