// Logisim project Controleur.circ as structural Verilog: 6 circuits, main circuit mainControl
module mainControl (
  input  [15:0] Inst,
  input  Clk,
  input  Reset,
  input  [3:0] Flags,
  output [7:0] PCOut,
  output Load,
  output Store,
  output [3:0] Codop,
  output [2:0] Rm,
  output [2:0] Rd,
  output [2:0] Rn,
  output [7:0] Imm8,
  output [4:0] Imm5,
  output ShifterImme
);

  wire and_1_out, comparator_1_eq, comparator_2_eq, comparator_3_eq, Load_t, or_1_out, or_2_out, or_3_out,
       SelBranch, SelDP, SelL_S, SelShift, Store_t;
  wire [2:0] DataRd, DataRm, Load_and_Store_1_rt, RdLoad, RmStore, ShiftRd, ShiftRm, ShiftRn;
  wire [3:0] CodopData, CodopShift, multiplexer_5_out;
  wire [4:0] ShiftImmo5;
  wire [7:0] L_SImmo8, multiplexer_3_out, ShiftImmo8;

  Comparator #(.width(4), .mode("unsigned")) comparator_1 (
    .a(CodopShift), .b(4'b0010), .eq(comparator_1_eq));  // open: gt, lt
  Comparator #(.width(4), .mode("unsigned")) comparator_2 (
    .a(CodopShift), .b(4'b0011), .eq(comparator_2_eq));  // open: gt, lt
  Comparator #(.width(4), .mode("unsigned")) comparator_3 (
    .a(CodopShift), .b(4'b0100), .eq(comparator_3_eq));  // open: gt, lt
  Multiplexer #(.select(3), .width(3), .enable("false")) multiplexer_1 (
    .in0(3'b000), .in1(DataRm), .in2(RmStore), .in3(3'b000), .in4(ShiftRn), .in5(3'b000), .in6(3'b000),
    .in7(3'b000), .out(Rm), .sel({SelShift, SelL_S, SelDP}));
  or or_1 (or_1_out, comparator_1_eq, comparator_2_eq, comparator_3_eq);
  Selecteur_de_type_de_calcul Selecteur_de_type_de_calcul_1 (
    .Input_bus_1(Inst), .Shift(SelShift), .DataProcessing(SelDP), .LoadStore(SelL_S), .Branch(SelBranch));
  Load_and_Store Load_and_Store_1 (
    .Load(Load_t), .Store(Store_t), .Imm8(L_SImmo8), .Input_bus_1(Inst), .Rt(Load_and_Store_1_rt));
  Shiftertoto Shifter_1 (
    .Immo8(ShiftImmo8), .Rd(ShiftRd), .Rm(ShiftRm), .Rn(ShiftRn), .Immo5(ShiftImmo5), .Input_bus_1(Inst),
    .Codop(CodopShift));
  Data_Processing Data_Processing_1 (.Rm(DataRm), .Input_bus_1(Inst), .Rd(DataRd), .Codop(CodopData));
  and and_1 (and_1_out, Flags[1], SelBranch);
  and and_2 (ShifterImme, SelShift, or_1_out);
  Demultiplexer #(.width(3), .enable("false")) demultiplexer_1 (
    .out0(RdLoad), .out1(RmStore), .in(Load_and_Store_1_rt), .sel(Store_t));
  Counter counter_1 (
    .clr(Reset), .load(and_1_out), .count(1'b1), .clk(Clk), .D(Inst[7:0]), .Q(PCOut));  // open: up, carry
  Multiplexer #(.select(3), .width(3), .enable("false")) multiplexer_2 (
    .in0(3'b000), .in1(DataRd), .in2(RdLoad), .in3(3'b000), .in4(ShiftRd), .in5(3'b000), .in6(3'b000),
    .in7(3'b000), .out(Rd), .sel({SelShift, SelL_S, SelDP}));
  Multiplexer #(.width(8), .enable("false")) multiplexer_3 (
    .in0(ShiftImmo8), .in1(L_SImmo8), .out(multiplexer_3_out), .sel(SelL_S));
  or or_2 (or_2_out, SelShift, SelL_S);
  Multiplexer #(.width(8), .enable("false")) multiplexer_4 (
    .in0({8{1'b0}}), .in1(multiplexer_3_out), .out(Imm8), .sel(or_2_out));
  Multiplexer #(.width(4), .enable("false")) multiplexer_5 (
    .in0(CodopShift), .in1(CodopData), .out(multiplexer_5_out), .sel(SelDP));
  Multiplexer #(.width(4), .enable("false")) multiplexer_6 (
    .in0(4'b0000), .in1(multiplexer_5_out), .out(Codop), .sel(or_3_out));
  or or_3 (or_3_out, SelShift, SelDP);
  and and_3 (Store, SelL_S, Store_t);
  and and_4 (Load, SelL_S, Load_t);
  Multiplexer #(.width(5), .enable("false")) multiplexer_7 (
    .in0({5{1'b0}}), .in1(ShiftImmo5), .out(Imm5), .sel(SelShift));
  Multiplexer #(.width(3), .enable("false")) multiplexer_8 (.in0(3'b000), .in1(ShiftRm), .out(Rn), .sel(SelShift));

  // Other names for the same wires on the sheet: CodopFinal[3:0] = Codop; Immo5Final[4:0] = Imm5;
  //   Immo8Final[7:0] = Imm8; LoadFinal = Load; PCFinal[7:0] = PCOut; RdFinal[2:0] = Rd; RmFinal[2:0] = Rm;
  //   RnFinal[2:0] = Rn; StoreFinal = Store
endmodule

module Selecteur_de_type_de_calcul (
  input  [15:0] Input_bus_1,
  output Shift,
  output DataProcessing,
  output LoadStore,
  output Branch
);

  wire bitselector_1_out, bitselector_2_out, bitselector_3_out, bitselector_4_out, bitselector_5_out,
       bitselector_6_out, not_1_out, not_2_out, not_3_out, not_4_out, not_5_out, not_6_out, not_7_out,
       not_8_out, not_9_out, not_10_out;

  BitSelector #(.width(16)) bitselector_1 (.in(Input_bus_1), .out(bitselector_1_out), .sel(4'b1111));
  BitSelector #(.width(16)) bitselector_2 (.in(Input_bus_1), .out(bitselector_2_out), .sel(4'b1110));
  BitSelector #(.width(16)) bitselector_3 (.in(Input_bus_1), .out(bitselector_3_out), .sel(4'b1101));
  BitSelector #(.width(16)) bitselector_4 (.in(Input_bus_1), .out(bitselector_4_out), .sel(4'b1100));
  BitSelector #(.width(16)) bitselector_5 (.in(Input_bus_1), .out(bitselector_5_out), .sel(4'b1011));
  BitSelector #(.width(16)) bitselector_6 (.in(Input_bus_1), .out(bitselector_6_out), .sel(4'b1010));
  not not_1 (not_1_out, bitselector_1_out);
  not not_2 (not_2_out, bitselector_2_out);
  not not_3 (not_3_out, bitselector_1_out);
  not not_4 (not_4_out, bitselector_3_out);
  not not_5 (not_5_out, bitselector_4_out);
  not not_6 (not_6_out, bitselector_5_out);
  not not_7 (not_7_out, bitselector_6_out);
  not not_8 (not_8_out, bitselector_2_out);
  not not_9 (not_9_out, bitselector_3_out);
  not not_10 (not_10_out, bitselector_3_out);
  and and_1 (Shift, not_1_out, not_2_out);
  and and_2 (DataProcessing, not_3_out, bitselector_2_out, not_4_out, not_5_out, not_6_out, not_7_out);
  and and_3 (LoadStore, bitselector_1_out, not_8_out, not_9_out, bitselector_4_out);
  and and_4 (Branch, bitselector_1_out, bitselector_2_out, not_10_out, bitselector_4_out);
endmodule

module Data_Processing (
  input  [15:0] Input_bus_1,
  output [2:0] Rd,
  output [2:0] Rm,
  output [3:0] Codop
);


  assign Codop = Input_bus_1[9:6];
  assign Rd = Input_bus_1[2:0];
  assign Rm = Input_bus_1[5:3];
endmodule

module Load_and_Store (
  input  [15:0] Input_bus_1,
  output Load,
  output Store,
  output [7:0] Imm8,
  output [2:0] Rt
);

  BitSelector #(.width(16)) bitselector_1 (.in(Input_bus_1), .out(Load), .sel(4'b1011));
  not not_1 (Store, Load);

  assign Imm8 = Input_bus_1[7:0];
  assign Rt = Input_bus_1[10:8];
endmodule

module Shiftertoto (
  input  [15:0] Input_bus_1,
  output [7:0] Immo8,
  output [2:0] Rd,
  output [2:0] Rm,
  output [2:0] Rn,
  output [4:0] Immo5,
  output [3:0] Codop
);

  wire ADD_SUB, ADDI, ADDR, ASR, LSL, LSL_LSR_ASR, LSR, MOV;
  wire [3:0] multiplexer_6_out;
  wire [4:0] Sel;

  Selecteur_Shifter Selecteur_Shifter_1 (
    .LSL(LSL), .LSR(LSR), .ADDR(ADDR), .ASR(ASR), .SUB(Sel[3]), .ADDI(ADDI), .MOV(MOV),
    .Instruction(Input_bus_1[13:9]));
  Multiplexer #(.width(8), .enable("false")) multiplexer_1 (
    .in0({8{1'b0}}), .in1(Input_bus_1[7:0]), .out(Immo8), .sel(MOV));
  Multiplexer #(.width(5), .enable("false")) multiplexer_2 (
    .in0({5{1'b0}}), .in1(Input_bus_1[10:6]), .out(Immo5), .sel(LSL_LSR_ASR));
  or or_1 (LSL_LSR_ASR, LSL, LSR, ASR);
  or or_2 (ADD_SUB, Sel[3], ADDI, ADDR);
  Multiplexer #(.width(3), .enable("false")) multiplexer_3 (
    .in0(3'b000), .in1(Input_bus_1[5:3]), .out(Rn), .sel(ADD_SUB));
  Multiplexer #(.select(3), .width(3), .enable("false")) multiplexer_4 (
    .in0(3'b000), .in1(Input_bus_1[2:0]), .in2(Input_bus_1[2:0]), .in3(3'b000), .in4(Input_bus_1[10:8]),
    .in5(3'b000), .in6(3'b000), .in7(3'b000), .out(Rd), .sel({MOV, LSL_LSR_ASR, ADD_SUB}));
  Multiplexer #(.select(2), .width(3), .enable("false")) multiplexer_5 (
    .in0(3'b000), .in1(Input_bus_1[8:6]), .in2(Input_bus_1[5:3]), .in3(3'b000), .out(Rm),
    .sel({LSL_LSR_ASR, ADD_SUB}));
  or or_3 (Sel[0], LSL, LSR);
  or or_4 (Sel[4], ADDI, ADDR);
  Multiplexer #(.width(4), .enable("false")) multiplexer_6 (
    .in0(4'b0010), .in1(4'b0011), .out(multiplexer_6_out), .sel(LSR));
  Multiplexer #(.select(5), .width(4), .enable("false")) multiplexer_7 (
    .in0(4'b0000), .in1(multiplexer_6_out), .in2(4'b0100), .in3(4'b0000), .in4(4'b0000), .in5(4'b0000),
    .in6(4'b0000), .in7(4'b0000), .in8(4'b1010), .in9(4'b0000), .in10(4'b0000), .in11(4'b0000),
    .in12(4'b0000), .in13(4'b0000), .in14(4'b0000), .in15(4'b0000), .in16(4'b0101), .in17(4'b0000),
    .in18(4'b0000), .in19(4'b0000), .in20(4'b0000), .in21(4'b0000), .in22(4'b0000), .in23(4'b0000),
    .in24(4'b0000), .in25(4'b0000), .in26(4'b0000), .in27(4'b0000), .in28(4'b0000), .in29(4'b0000),
    .in30(4'b0000), .in31(4'b0000), .out(Codop), .sel({Sel[4:3], MOV, ASR, Sel[0]}));
  // Probe on Codop
  // Probe on {Sel[4:3], MOV, ASR, Sel[0]}

  // Other names for the same wires on the sheet: CodopFinal[3:0] = Codop; Immo5Final[4:0] = Immo5;
  //   Immo8Final[7:0] = Immo8; Immo8_MOV[7:0] = Input_bus_1[7:0]; RdADD_SUB[2:0] = Input_bus_1[2:0];
  //   RdLSL_LSR_ASR[2:0] = Input_bus_1[2:0]; Reste[10:0] = Input_bus_1[10:0]; Reste_ADD_SUB[8:0] = Input_bus_1[8:0];
  //   RmLSL_LSR_ASR[2:0] = Input_bus_1[5:3]; Rn_ADD_SUB[2:0] = Input_bus_1[5:3];
  //   Immo5LSL_LSR_ASR[4:0] = Input_bus_1[10:6]; RmADD_SUB[2:0] = Input_bus_1[8:6]; Rd_MOV[2:0] = Input_bus_1[10:8];
  //   Inst[4:0] = Input_bus_1[13:9]; RdFinal[2:0] = Rd; RmFinal[2:0] = Rm; RnFinal[2:0] = Rn; Sel[2:1] = {MOV, ASR};
  //   SUB = Sel[3]
endmodule

module Selecteur_Shifter (
  input  [4:0] Instruction,
  output LSL,
  output LSR,
  output ADDR,
  output ASR,
  output SUB,
  output ADDI,
  output MOV
);

  wire ADD_SUB, comparator_6_eq, comparator_7_eq, comparator_8_eq;

  Comparator #(.width(3)) comparator_1 (.a(3'b000), .b(Instruction[4:2]), .eq(LSL));  // open: gt, lt
  Comparator #(.width(3)) comparator_2 (.a(3'b001), .b(Instruction[4:2]), .eq(LSR));  // open: gt, lt
  Comparator #(.width(3)) comparator_3 (.a(3'b010), .b(Instruction[4:2]), .eq(ASR));  // open: gt, lt
  Comparator #(.width(3)) comparator_4 (.a(3'b011), .b(Instruction[4:2]), .eq(ADD_SUB));  // open: gt, lt
  Comparator #(.width(3)) comparator_5 (.a(3'b100), .b(Instruction[4:2]), .eq(MOV));  // open: gt, lt
  Comparator #(.width(2)) comparator_6 (.a(2'b00), .b(Instruction[1:0]), .eq(comparator_6_eq));  // open: gt, lt
  Comparator #(.width(2)) comparator_7 (.a(2'b01), .b(Instruction[1:0]), .eq(comparator_7_eq));  // open: gt, lt
  Comparator #(.width(2)) comparator_8 (.a(2'b10), .b(Instruction[1:0]), .eq(comparator_8_eq));  // open: gt, lt
  and and_1 (ADDR, ADD_SUB, comparator_6_eq);
  and and_2 (SUB, ADD_SUB, comparator_7_eq);
  and and_3 (ADDI, ADD_SUB, comparator_8_eq);

  // Other names for the same wires on the sheet: Reste[1:0] = Instruction[1:0]; Code[2:0] = Instruction[4:2]
endmodule
