// Logisim project Ctl_Load_Store.circ as structural Verilog: 1 circuit, main circuit Load_Store
module Load_Store (
  input  [15:0] Instruction,
  input  [31:0] R0,
  input  Enable,
  input  [31:0] R1,
  input  Clk,
  input  [31:0] R2,
  input  Reset,
  input  [31:0] R3,
  input  [31:0] R4,
  input  [31:0] R5,
  input  [31:0] R6,
  input  [31:0] R7,
  input  [31:0] Stack_Pointer,
  input  [31:0] Program_Counter,
  input  [31:0] Old_Value,
  output [2:0] Mask,
  output [31:0] Imm32,
  output [2:0] Rmd,
  output Store,
  output Load,
  output PC_Hold,
  output [31:0] RAM_Addr
);

  wire and_1_out, and_2_out, and_3_out, and_4_out, and_5_out, and_6_out, and_8_out, and_9_out, and_11_out,
       and_12_out, and_13_out, and_14_out, and_19_out, d_ff_1_q, d_ff_1_qn, or_1_out, or_2_out, or_3_out,
       or_6_out, xor_1_out;
  wire [2:0] or_4_out, t;
  wire [31:0] adder_1_out, adder_2_out, adder_3_out, adder_4_out, adder_5_out, adder_6_out, and_7_out,
       and_15_out, bit_extender_1_out, bit_extender_2_out, bit_extender_3_out, multiplexer_4_out,
       multiplexer_5_out, multiplexer_7_out, multiplexer_8_out, multiplexer_9_out, multiplexer_10_out,
       multiplier_1_out, multiplier_2_out, multiplier_3_out, Rb, Ro, Rt, shifter_2_out;

  Multiplexer #(.select(3), .width(32)) multiplexer_1 (
    .in0(R0), .in1(R1), .in2(R2), .in3(R3), .in4(R4), .in5(R5), .in6(R6), .in7(R7), .out(Rb),
    .sel(Instruction[5:3]));
  Multiplexer #(.select(3), .width(32)) multiplexer_2 (
    .in0(R0), .in1(R1), .in2(R2), .in3(R3), .in4(R4), .in5(R5), .in6(R6), .in7(R7), .out(Ro),
    .sel(Instruction[8:6]));
  Multiplexer #(.select(3), .width(32)) multiplexer_3 (
    .in0(R0), .in1(R1), .in2(R2), .in3(R3), .in4(R4), .in5(R5), .in6(R6), .in7(R7), .out(Rt), .sel(t));
  assign bit_extender_1_out = {{24{1'b0}}, Instruction[7:0]};  // Bit_Extender bit_extender_1
  xor xor_1 (xor_1_out, Instruction[11], Instruction[9]);
  and and_1 (and_1_out, Instruction[9], Instruction[10], ~Instruction[11], ~Instruction[13], Instruction[14], ~Instruction[15]);  // AND_Gate
  and and_2 (and_2_out, ~Instruction[15], Instruction[14], Instruction[13], Instruction[12], Instruction[11]);  // AND_Gate
  and and_3 (and_3_out, ~Instruction[15], Instruction[14], ~Instruction[13], Instruction[12]);  // AND_Gate
  and and_4 (and_4_out, Instruction[15], ~Instruction[14], ~Instruction[13], ~Instruction[12], Instruction[11]);  // AND_Gate
  and and_5 (and_5_out, ~Instruction[15], Instruction[14], ~Instruction[13], Instruction[12], ~Instruction[11], Instruction[10], ~Instruction[9]);  // AND_Gate
  and and_6 (and_6_out, ~Instruction[15], Instruction[14], Instruction[13], Instruction[12], ~Instruction[11]);  // AND_Gate
  or or_1 (or_1_out, Instruction[11], and_1_out);
  Adder #(.width(32)) adder_1 (.a(Program_Counter), .b(32'h4), .out(adder_1_out));  // open: cin, cout
  assign and_7_out = adder_1_out & ~32'h2;  // AND_Gate and_7, 32 bits wide
  Multiplier #(.width(32)) multiplier_1 (.a(bit_extender_1_out), .b(32'h4), .out(multiplier_1_out));  // open: cin, cout
  Shifter #(.shift("lr"), .width(32)) shifter_1 (.\dist (5'b00010));  // open: in, out
  Shifter #(.width(32)) shifter_2 (.in(bit_extender_1_out), .\dist (5'b00010), .out(shifter_2_out));
  and and_8 (and_8_out, and_3_out, Instruction[10], xor_1_out);
  and and_9 (and_9_out, and_3_out, Instruction[11], Instruction[9]);
  and and_10 (or_4_out[2], and_3_out, Instruction[10], Instruction[9]);
  or or_2 (or_2_out, and_5_out, and_6_out);
  and and_11 (and_11_out, Instruction[12], ~Instruction[14]);  // AND_Gate
  and and_12 (and_12_out, ~Instruction[12], ~Instruction[13], ~Instruction[15]);  // AND_Gate
  D_Flip_Flop #(.trigger("falling")) d_ff_1 (
    .D(and_13_out), .clk(Clk), .Q(d_ff_1_q), .Qn(d_ff_1_qn), .reset(or_3_out));  // open: preset
  buf and_13 (and_13_out, ~d_ff_1_q);  // AND_Gate AND_Gate
  or or_3 (or_3_out, ~1'b1, Reset, ~Enable);  // OR_Gate
  Adder #(.width(32)) adder_2 (.a(and_7_out), .b(multiplier_1_out), .out(adder_2_out));  // open: cin, cout
  Adder #(.width(32)) adder_3 (.a(Rb), .b(Ro), .out(adder_3_out));  // open: cin, cout
  assign bit_extender_2_out = {{27{1'b0}}, Instruction[10:6]};  // Bit_Extender bit_extender_2
  Multiplier #(.width(32)) multiplier_2 (.a(bit_extender_2_out), .b(32'h4), .out(multiplier_2_out));  // open: cin, cout
  assign bit_extender_3_out = {{27{1'b0}}, Instruction[10:6]};  // Bit_Extender bit_extender_3
  Adder #(.width(32)) adder_4 (.a(shifter_2_out), .b(Stack_Pointer), .out(adder_4_out), .cin(1'b0));  // open: cout
  or or_4 (or_4_out[0], and_2_out, and_8_out);
  or or_5 (or_4_out[1], and_9_out, and_4_out);
  or or_6 (or_6_out, and_11_out, and_12_out);
  Multiplexer #(.width(32)) multiplexer_4 (
    .in0(adder_2_out), .in1(adder_3_out), .out(multiplexer_4_out), .sel(Instruction[12]));
  Multiplexer #(.width(32)) multiplexer_5 (
    .in0(multiplier_2_out), .in1(bit_extender_2_out), .out(multiplexer_5_out), .sel(Instruction[12]));
  Multiplier #(.width(32)) multiplier_3 (.a(bit_extender_3_out), .b(32'h2), .out(multiplier_3_out));  // open: cin, cout
  Multiplexer #(.width(3)) multiplexer_6 (.in0(Instruction[2:0]), .in1(Instruction[10:8]), .out(t), .sel(or_6_out));
  buf and_14 (and_14_out, d_ff_1_qn);  // AND_Gate
  Adder #(.width(32)) adder_5 (.a(Rb), .b(multiplexer_5_out), .out(adder_5_out));  // open: cin, cout
  Adder #(.width(32)) adder_6 (.a(Rb), .b(multiplier_3_out), .out(adder_6_out));  // open: cin, cout
  assign and_15_out = Rt & 32'hff;  // AND_Gate and_15, 32 bits wide
  and and_16 (Store, ~or_1_out, d_ff_1_q, Enable);  // AND_Gate
  and and_17 (Load, Enable, or_1_out, d_ff_1_q);
  and and_18 (PC_Hold, Enable, and_14_out);
  Multiplexer #(.width(32)) multiplexer_7 (
    .in0(multiplexer_4_out), .in1(adder_5_out), .out(multiplexer_7_out), .sel(Instruction[13]));
  Multiplexer #(.width(32)) multiplexer_8 (
    .in0(adder_6_out), .in1(adder_4_out), .out(multiplexer_8_out), .sel(Instruction[12]));
  Multiplexer #(.width(32)) multiplexer_9 (.in0(Rt), .in1(and_15_out), .out(multiplexer_9_out), .sel(or_2_out));
  Multiplexer #(.width(32)) multiplexer_10 (
    .in0(multiplexer_7_out), .in1(multiplexer_8_out), .out(multiplexer_10_out), .sel(Instruction[15]));
  Pull_Resistor pull_resistor_1 (.node(Mask));
  assign Mask = and_19_out ? or_4_out : 3'bz;  // Controlled_Buffer controlled_buffer_1
  and and_19 (and_19_out, Load, Enable);
  Pull_Resistor pull_resistor_2 (.node(Imm32));
  assign Imm32 = Enable ? multiplexer_9_out : 32'bz;  // Controlled_Buffer controlled_buffer_2
  Pull_Resistor pull_resistor_3 (.node(Rmd));
  assign Rmd = Enable ? t : 3'bz;  // Controlled_Buffer controlled_buffer_3
  Pull_Resistor pull_resistor_4 (.node(RAM_Addr));
  assign RAM_Addr = Enable ? multiplexer_10_out : 32'bz;  // Controlled_Buffer controlled_buffer_4
  Multiplexer #(.select(2), .width(32)) multiplexer_11 ();  // open: in0, in1, in2, in3, out, sel

  // Other names for the same wires on the sheet: b[2:0] = Instruction[5:3]; o[2:0] = Instruction[8:6];
  //   Old[31:0] = Old_Value

  // Notes on the sheet:
  //   Instruction: pull=down
  //   ldrb imm
  //   01110 strb imm
  //   ldrb/ldrsb Ro
  //   Delay load and hold PC for 1 cycle for the RAM to send out requested data 
endmodule
