// Logisim project Ctl_Opcode_Decoder.circ as structural Verilog: 1 circuit, main circuit Opcode_Decoder
module Opcode_Decoder (
  input  [6:0] Opcode,
  output Shift,
  output Data_Processing,
  output Load_Store,
  output SP_Address,
  output Conditional,
  output Load_Address,
  output Long_Branch,
  output High_Register_Op
);

  wire and_1_out, and_2_out, and_4_out, and_5_out, and_6_out, and_7_out, and_8_out, and_10_out, and_11_out;

  and and_1 (and_1_out, ~Opcode[6], ~Opcode[5]);  // AND_Gate
  or or_1 (Shift, and_1_out, and_2_out);
  and and_2 (and_2_out, Opcode[6], ~Opcode[5], Opcode[4], Opcode[3], Opcode[0]);  // AND_Gate
  and and_3 (Data_Processing, ~Opcode[6], Opcode[5], ~Opcode[4], ~Opcode[3], ~Opcode[2], ~Opcode[1]);  // AND_Gate
  and and_4 (and_4_out, ~Opcode[6], Opcode[5], ~Opcode[4], ~Opcode[3], Opcode[2]);  // AND_Gate
  and and_5 (and_5_out, Opcode[6], ~Opcode[5], ~Opcode[4], Opcode[3]);  // AND_Gate
  and and_6 (and_6_out, ~Opcode[6], Opcode[5], ~Opcode[4], Opcode[3]);  // AND_Gate
  and and_7 (and_7_out, ~Opcode[6], Opcode[5], Opcode[4]);  // AND_Gate
  and and_8 (and_8_out, Opcode[6], ~Opcode[5], ~Opcode[4]);  // AND_Gate
  and and_9 (SP_Address, Opcode[6], ~Opcode[5], Opcode[4], Opcode[3], ~Opcode[0]);  // AND_Gate
  and and_10 (and_10_out, Opcode[6], Opcode[5], ~Opcode[4], Opcode[3]);  // AND_Gate
  or or_2 (Conditional, and_10_out, and_11_out);
  and and_11 (and_11_out, Opcode[6], Opcode[5], Opcode[4], ~Opcode[3], ~Opcode[2]);  // AND_Gate
  and and_12 (Load_Address, Opcode[6], ~Opcode[5], Opcode[4], ~Opcode[3]);  // AND_Gate
  and and_13 (Long_Branch, Opcode[6], Opcode[5], Opcode[4], Opcode[3]);
  and and_14 (High_Register_Op, ~Opcode[6], Opcode[5], ~Opcode[4], ~Opcode[3], ~Opcode[2], Opcode[1]);  // AND_Gate
  or or_3 (Load_Store, and_4_out, and_5_out, and_6_out, and_7_out, and_8_out);

  // Notes on the sheet:
  //   Shift, add, sub, mov
  //   Load/Store
  //   SP Address
  //   Conditional branch
  //   Data Processing
endmodule
