// Logisim project Ctl_SP_Address.circ as structural Verilog: 1 circuit, main circuit SP_Address
module SP_Address (
  input  [31:0] Stack_Pointer,
  input  [15:0] Instruction,
  input  Enable,
  output [31:0] New_Stack_Pointer,
  output Write_Enable
);

  wire and_1_out;
  wire [31:0] adder_1_out, bit_extender_1_out, multiplexer_1_out, shifter_1_out, subtractor_1_out;

  and and_1 (and_1_out, ~Instruction[8], ~Instruction[9], ~Instruction[10], ~Instruction[11]);  // AND_Gate
  assign bit_extender_1_out = {{25{1'b0}}, Instruction[6:0]};  // Bit_Extender bit_extender_1
  Shifter #(.width(32)) shifter_1 (.in(bit_extender_1_out), .\dist (5'b00010), .out(shifter_1_out));
  Adder #(.width(32)) adder_1 (.a(Stack_Pointer), .b(shifter_1_out), .out(adder_1_out));  // open: cin, cout
  Subtractor #(.width(32)) subtractor_1 (
    .a(Stack_Pointer), .b(shifter_1_out), .out(subtractor_1_out));  // open: bin, bout
  assign New_Stack_Pointer = Write_Enable ? multiplexer_1_out : 32'bz;  // Controlled_Buffer controlled_buffer_1
  Multiplexer #(.width(32)) multiplexer_1 (
    .in0(adder_1_out), .in1(subtractor_1_out), .out(multiplexer_1_out), .sel(Instruction[7]));
  and and_2 (Write_Enable, and_1_out, Enable);
  Pull_Resistor pull_resistor_1 (.node(New_Stack_Pointer));

  // Notes on the sheet:
  //   Pull output low on Enable = 0
endmodule
