// Logisim project Ctl_Shift_Add_Sub_Mov.circ as structural Verilog: 1 circuit, main circuit Shift_Add_Sub_Mov
module Shift_Add_Sub_Mov (
  input  Enable,
  input  [15:0] Instruction,
  output [3:0] Flags_Update_Mask,
  output Carry,
  output Imm32_Enable,
  output [2:0] Rm,
  output [2:0] Rn,
  output [2:0] Rd,
  output [4:0] Imm5,
  output [31:0] Imm32,
  output [3:0] ALU_Opcode
);

  wire and_1_out, and_3_out, and_4_out, and_5_out, comparator_1_eq, or_3_out;
  wire [0:0] and_2_out;
  wire [1:0] or_2_out;
  wire [2:0] multiplexer_3_out, multiplexer_4_out;
  wire [3:0] adder_1_out, adder_2_out, multiplexer_2_out, multiplexer_6_out;
  wire [31:0] bit_extender_1_out, bit_extender_2_out, multiplexer_1_out, multiplexer_5_out, negator_1_out;

  and and_1 (and_1_out, Instruction[11], Instruction[12]);
  assign bit_extender_1_out = {{24{1'b0}}, Instruction[7:0]};  // Bit_Extender bit_extender_1
  and and_2 (and_2_out[0], and_1_out, Instruction[9]);
  Adder #(.width(4)) adder_1 (.a(4'b0010), .b(Instruction[14:11]), .out(adder_1_out), .cin(1'b0));  // open: cout
  or or_1 (or_2_out[1], Instruction[11], Instruction[12], ~Instruction[13]);  // OR_Gate
  and and_3 (and_3_out, or_2_out[1], Instruction[13]);
  and and_4 (and_4_out, Instruction[10], Instruction[11], Instruction[12]);
  and and_5 (and_5_out, ~Instruction[11], ~Instruction[12]);  // AND_Gate
  assign bit_extender_2_out = {{29{1'b0}}, Instruction[8:6]};  // Bit_Extender bit_extender_2
  Multiplexer #(.enable("false"), .width(32)) multiplexer_1 (
    .in0(bit_extender_1_out), .in1(negator_1_out), .out(multiplexer_1_out), .sel(and_5_out));
  Negator #(.width(32)) negator_1 (.in(bit_extender_1_out), .out(negator_1_out));
  Adder #(.width(4)) adder_2 (
    .a({3'b000, and_2_out[0]}), .b(adder_1_out), .out(adder_2_out), .cin(1'b0));  // open: cout
  Multiplexer #(.enable("false"), .select(2), .width(4)) multiplexer_2 (
    .in0(4'b1001), .in1(4'b1010), .in2(4'b0101), .in3(4'b0110), .out(multiplexer_2_out),
    .sel(Instruction[12:11]));
  or or_2 (or_2_out[0], and_3_out, and_1_out);
  or or_3 (or_3_out, and_4_out, Instruction[13]);
  Multiplexer #(.enable("false"), .width(3)) multiplexer_3 (
    .in0(Instruction[5:3]), .in1(Instruction[10:8]), .out(multiplexer_3_out), .sel(Instruction[13]));
  Multiplexer #(.enable("false"), .width(3)) multiplexer_4 (
    .in0(Instruction[2:0]), .in1(Instruction[10:8]), .out(multiplexer_4_out), .sel(Instruction[13]));
  Multiplexer #(.enable("false"), .width(32)) multiplexer_5 (
    .in0(bit_extender_2_out), .in1(multiplexer_1_out), .out(multiplexer_5_out), .sel(Instruction[13]));
  Multiplexer #(.enable("false"), .width(4)) multiplexer_6 (
    .in0(adder_2_out), .in1(multiplexer_2_out), .out(multiplexer_6_out), .sel(Instruction[13]));
  Comparator #(.mode("unsigned"), .width(4)) comparator_1 (
    .a(4'b0110), .b(multiplexer_6_out), .eq(comparator_1_eq));  // open: gt, lt
  Pull_Resistor pull_resistor_1 (.node(Flags_Update_Mask));
  assign Flags_Update_Mask = Enable ? {2'b11, or_2_out} : 4'bz;  // Controlled_Buffer controlled_buffer_1
  and and_6 (Carry, Enable, comparator_1_eq);
  and and_7 (Imm32_Enable, Enable, or_3_out);
  Pull_Resistor pull_resistor_2 (.node(Rm));
  assign Rm = Enable ? Instruction[8:6] : 3'bz;  // Controlled_Buffer controlled_buffer_2
  Pull_Resistor pull_resistor_3 (.node(Rn));
  assign Rn = Enable ? multiplexer_3_out : 3'bz;  // Controlled_Buffer controlled_buffer_3
  Pull_Resistor pull_resistor_4 (.node(Rd));
  assign Rd = Enable ? multiplexer_4_out : 3'bz;  // Controlled_Buffer controlled_buffer_4
  Pull_Resistor pull_resistor_5 (.node(Imm5));
  assign Imm5 = Enable ? Instruction[10:6] : 5'bz;  // Controlled_Buffer controlled_buffer_5
  Pull_Resistor pull_resistor_6 (.node(Imm32));
  assign Imm32 = Enable ? multiplexer_5_out : 32'bz;  // Controlled_Buffer controlled_buffer_6
  Pull_Resistor pull_resistor_7 (.node(ALU_Opcode));
  assign ALU_Opcode = Enable ? multiplexer_6_out : 4'bz;  // Controlled_Buffer controlled_buffer_7

  // Notes on the sheet:
  //   ADD, SUB
  //   LSL
  //   b11,b12
  //   Note: ALU uses Rn register for shifts. Use Rn instead of Rm for shifts (immediate) here too
  //   Note 3: Imm32_Enable forces the use of the immediate for Rm register
  //   !MOV
  //   Note 2: MOV uses RSB ALU opcode with Imm8 reversed so that it is copied to output register
  //   Pull output low on Enable = 0
  //   SUB
  //   ADDi, SUBi
  //   only ADD and SUB use Rm
  //   Enable carry for SUB since it is reversed in ALU
  //   ALU will use Imm32 instead of Rm
endmodule
