// Logisim project Machine.circ as structural Verilog: 2 circuits, main circuit main
module main (
);

  wire and_1_out, clock_1_out, comparator_1_lt, CPU_1_store, decoder_1_out0, decoder_1_out1, decoder_1_out2,
       decoder_1_out3, decoder_1_out4, decoder_1_out5, decoder_1_out6, decoder_1_out7, not_1_out, or_1_out,
       Rst, sevenSegDecoder_1_segment_a, sevenSegDecoder_1_segment_b, sevenSegDecoder_1_segment_c,
       sevenSegDecoder_1_segment_d, sevenSegDecoder_1_segment_e, sevenSegDecoder_1_segment_f,
       sevenSegDecoder_1_segment_g;
  wire [1:0] r2_I;
  wire [7:0] r0_I, r1_I, RAM_Addr, ROM_Addr;
  wire [8:0] shifter_1_out;
  wire [8:8] VMEM;
  wire [15:0] ROMa_data;
  wire [31:0] CPU_1_r0, CPU_1_r1, CPU_1_r2, CPU_1_r3, CPU_1_r4, CPU_1_r5, CPU_1_r6, CPU_1_r7, CPU_1_ram_out,
       multiplexer_1_out, multiplexer_2_out, multiplexer_3_out, r3_I, r4_O, r5_O, r6_O, r7_O, RAMa_dout,
       register_1_q, register_2_q, register_3_q, register_4_q;

  RAM #(.dataWidth(32), .databus("bibus")) RAMa (
    .addr(RAM_Addr), .we(and_1_out), .oe(1'b1), .clk(clock_1_out), .din(CPU_1_ram_out), .dout(RAMa_dout));
  and and_1 (and_1_out, CPU_1_store, comparator_1_lt);
  Shifter #(.width(9), .shift("lr")) shifter_1 (.in({VMEM[8], RAM_Addr}), .\dist (4'b0010), .out(shifter_1_out));
  // Probe on shifter_1_out
  Comparator #(.width(9), .mode("unsigned")) comparator_1 (
    .a({VMEM[8], RAM_Addr}), .b(9'h100), .lt(comparator_1_lt));  // open: gt, eq
  or or_1 (or_1_out, ~CPU_1_store, comparator_1_lt);  // OR_Gate
  Multiplexer #(.width(32), .enable("false")) multiplexer_1 (
    .in0(CPU_1_ram_out), .in1(multiplexer_3_out), .out(multiplexer_1_out), .sel(or_1_out));
  Clock clock_1 (.out(clock_1_out));
  not not_1 (not_1_out, comparator_1_lt);
  Decoder #(.select(3), .enable("false")) decoder_1 (
    .out0(decoder_1_out0), .out1(decoder_1_out1), .out2(decoder_1_out2), .out3(decoder_1_out3),
    .out4(decoder_1_out4), .out5(decoder_1_out5), .out6(decoder_1_out6), .out7(decoder_1_out7),
    .sel(shifter_1_out[2:0]));
  ROM #(.dataWidth(16)) ROMa (.addr(ROM_Addr), .data(ROMa_data));
  Multiplexer #(.width(32), .enable("false")) multiplexer_2 (
    .in0(RAMa_dout), .in1(multiplexer_3_out), .out(multiplexer_2_out), .sel(not_1_out));
  Button Rst_Button (.out(Rst));
  LED A0 (.in(multiplexer_2_out[0]));
  LED A1 (.in(multiplexer_2_out[1]));
  // Probe on {{24{1'b0}}, r0_I}
  // Probe on {{24{1'b0}}, r1_I}
  // Probe on {{30{1'b0}}, r2_I}
  LED A3 (.in(multiplexer_2_out[3]));
  LED A4 (.in(multiplexer_2_out[4]));
  LED A2 (.in(multiplexer_2_out[2]));
  // Probe on shifter_1_out[2:0]
  LED L0 (.in(CPU_1_r0[0]));
  // Probe on CPU_1_r1
  // Probe on CPU_1_r0
  LED A5 (.in(multiplexer_2_out[5]));
  LED A6 (.in(multiplexer_2_out[6]));
  LED A7 (.in(multiplexer_2_out[7]));
  Button opA0 (.out(r0_I[0]));
  Button opA1 (.out(r0_I[1]));
  Button opA2 (.out(r0_I[2]));
  Button opA3 (.out(r0_I[3]));
  Button opA4 (.out(r0_I[4]));
  Button opA5 (.out(r0_I[5]));
  Button opA6 (.out(r0_I[6]));
  Button opA7 (.out(r0_I[7]));
  Button opB0 (.out(r1_I[0]));
  Button opB1 (.out(r1_I[1]));
  Button opB2 (.out(r1_I[2]));
  Button opB3 (.out(r1_I[3]));
  Button opB4 (.out(r1_I[4]));
  Button opB5 (.out(r1_I[5]));
  Button opB6 (.out(r1_I[6]));
  Button opB7 (.out(r1_I[7]));
  Register #(.width(32)) register_1 (.D({{24{1'b0}}, r0_I}), .en(1'b1), .clk(clock_1_out), .Q(register_1_q), .clr(Rst));
  Register #(.width(32)) register_2 (.D({{24{1'b0}}, r1_I}), .en(1'b1), .clk(clock_1_out), .Q(register_2_q), .clr(Rst));
  Register #(.width(32)) register_3 (.D({{30{1'b0}}, r2_I}), .en(1'b1), .clk(clock_1_out), .Q(register_3_q), .clr(Rst));
  Register #(.width(32)) register_4 (.D(r3_I), .en(1'b1), .clk(clock_1_out), .Q(register_4_q), .clr(Rst));
  Register #(.width(32)) register_5 (
    .D(multiplexer_1_out), .en(decoder_1_out4), .clk(clock_1_out), .Q(r4_O), .clr(Rst));
  Register #(.width(32)) register_6 (
    .D(multiplexer_1_out), .en(decoder_1_out5), .clk(clock_1_out), .Q(r5_O), .clr(Rst));
  Register #(.width(32)) register_7 (
    .D(multiplexer_1_out), .en(decoder_1_out6), .clk(clock_1_out), .Q(r6_O), .clr(Rst));
  Register #(.width(32)) register_8 (
    .D(multiplexer_1_out), .en(decoder_1_out7), .clk(clock_1_out), .Q(r7_O), .clr(Rst));
  LED L3 (.in(CPU_1_r0[3]));
  LED L1 (.in(CPU_1_r0[1]));
  LED L2 (.in(CPU_1_r0[2]));
  // Probe on CPU_1_r3
  // Probe on CPU_1_r2
  // Probe on CPU_1_r5
  // Probe on CPU_1_r4
  // Probe on CPU_1_r7
  // Probe on CPU_1_r6
  CPU CPU_1 (
    .ROM_Addr(ROM_Addr), .RAM_In(multiplexer_2_out), .Rst(Rst), .RAM_Addr({VMEM[8], RAM_Addr}),
    .ROM_In(ROMa_data), .Clk(clock_1_out), .RAM_Out(CPU_1_ram_out), .R0(CPU_1_r0), .R1(CPU_1_r1),
    .R2(CPU_1_r2), .R3(CPU_1_r3), .R4(CPU_1_r4), .R5(CPU_1_r5), .R6(CPU_1_r6), .R7(CPU_1_r7),
    .Store(CPU_1_store));
  Button cmd0 (.out(r2_I[0]));
  Button cmd1 (.out(r2_I[1]));
  LED LED_1 (.in(RAM_Addr[0]));
  LED LED_2 (.in(RAM_Addr[1]));
  LED LED_3 (.in(RAM_Addr[2]));
  LED res0 (.in(r4_O[0]));
  LED res1 (.in(r4_O[1]));
  LED res2 (.in(r4_O[2]));
  LED res3 (.in(r4_O[3]));
  LED res4 (.in(r4_O[4]));
  LED res5 (.in(r4_O[5]));
  LED res6 (.in(r4_O[6]));
  LED res7 (.in(r4_O[7]));
  Multiplexer #(.select(3), .width(32), .enable("false")) multiplexer_3 (
    .in0(register_1_q), .in1(register_2_q), .in2(register_3_q), .in3(register_4_q), .in4(r4_O), .in5(r5_O),
    .in6(r6_O), .in7(r7_O), .out(multiplexer_3_out), .sel(shifter_1_out[2:0]));
  LED LED_4 (.in(RAM_Addr[3]));
  sevenSegDecoder sevenSegDecoder_1 (
    .e1(r4_O[3]), .e2(r4_O[2]), .e3(r4_O[1]), .e4(r4_O[0]), .segment_a(sevenSegDecoder_1_segment_a),
    .segment_b(sevenSegDecoder_1_segment_b), .segment_c(sevenSegDecoder_1_segment_c),
    .segment_d(sevenSegDecoder_1_segment_d), .segment_e(sevenSegDecoder_1_segment_e),
    .segment_f(sevenSegDecoder_1_segment_f), .segment_g(sevenSegDecoder_1_segment_g));
  _7_Segment_Display L_7_Segment_Display_1 (
    .g(sevenSegDecoder_1_segment_g), .f(sevenSegDecoder_1_segment_f), .a(sevenSegDecoder_1_segment_a),
    .b(sevenSegDecoder_1_segment_b), .e(sevenSegDecoder_1_segment_e), .d(sevenSegDecoder_1_segment_d),
    .c(sevenSegDecoder_1_segment_c), .dp(1'b0));

  // Other names for the same wires on the sheet: VMEM[7:0] = RAM_Addr

  // Notes on the sheet:
  //   Clk
  //   Memory Mapping
  //   0-255: RAM
  //   256-262: IO
  //   Select RegDest
  //   DataIn
  //   AOut
  //   contents of ROMa (hex, n*v repeats v):
  //   b098 2000 9014 9010 900c 2001 9008 2002 9004 2003 9000 defe 9820 990c 4288 d104 defe 9818 991c 1840
  //   9028 defe 9820 9908 4288 d104 defe 9818 991c 1a40 9028 defe 9820 9904 4288 d104 defe 9818 991c 4341
  //   9128 defe 9820 9900 4288 d104 defe 9818 991c 4088 9028 defe ded5
  //   opA
  //   opB
  //   cmd
  //   res
  //   Select RegA
  //   Use only 8 bit adresses
endmodule

module CPU (
  input  [31:0] RAM_In,
  input  [15:0] ROM_In,
  input  Clk,
  input  Rst,
  output [7:0] ROM_Addr,
  output [8:0] RAM_Addr,
  output [31:0] R3,
  output [31:0] R7,
  output [31:0] RAM_Out,
  output [31:0] R2,
  output [31:0] R6,
  output [31:0] R1,
  output [31:0] R5,
  output [31:0] R0,
  output [31:0] R4,
  output Store
);

  wire Controller_1_carry, Controller_1_dp_shift, Controller_1_imm32_enable, Controller_1_load;
  wire [2:0] Controller_1_rd, Controller_1_rm, Controller_1_rn;
  wire [3:0] ALU_1_flags, Controller_1_alu_opcode;
  wire [4:0] Controller_1_imm5, multiplexer_3_out;
  wire [31:0] ALU_1_s, Controller_1_imm32, multiplexer_1_out, multiplexer_2_out, Regs_1_p15;

  Controller Controller_1 (
    .Inst(ROM_In), .Rm(Controller_1_rm), .PC(ROM_Addr), .ALU_Opcode(Controller_1_alu_opcode),
    .Imm5(Controller_1_imm5), .Rn(Controller_1_rn), .Flags(ALU_1_flags),
    .Imm32_Enable(Controller_1_imm32_enable), .Rd(Controller_1_rd), .Imm32(Controller_1_imm32),
    .DP_Shift(Controller_1_dp_shift), .Carry(Controller_1_carry), .RAM_Addr(RAM_Addr),
    .Load(Controller_1_load), .Store(Store), .Clk(Clk), .Reset(Rst));
  Multiplexer #(.width(32), .enable("false")) multiplexer_1 (
    .in0(ALU_1_s), .in1(RAM_In), .out(multiplexer_1_out), .sel(Controller_1_load));
  // BancRegistre Regs_1: pin names not known; wires that end beside it: multiplexer_1_out, Controller_1_rd, Clk, R0, Rst, R1, R2, R3, R4, Controller_1_rm, R5, R6, Controller_1_rn, R7, Regs_1_p15, RAM_Out
  Multiplexer #(.width(32), .enable("false")) multiplexer_2 (
    .in0(RAM_Out), .in1(Controller_1_imm32), .out(multiplexer_2_out), .sel(Controller_1_imm32_enable));
  Multiplexer #(.width(5), .enable("false")) multiplexer_3 (
    .in0(multiplexer_2_out[4:0]), .in1(Controller_1_imm5), .out(multiplexer_3_out),
    .sel(Controller_1_dp_shift));
  ALU ALU_1 (
    .S(ALU_1_s), .Flags(ALU_1_flags), .Codop(Controller_1_alu_opcode), .CarryIn(Controller_1_carry),
    .A(multiplexer_2_out), .B(Regs_1_p15), .Shift(multiplexer_3_out));
  // Probe on ALU_1_flags

  // Notes on the sheet:
  //   RAM/ALU Input selector
  //   Use data frpm Imm8 instead of A register
  //   Use data from register or immediate for shift
  //   Trigger carry for additionner
  //   Imm8 input for Move
endmodule
