// Logisim project Machine2.circ as structural Verilog: 3 circuits, main circuit main
module main (
);

  wire Rst_Button_out, vhdl_component_1_p1, vhdl_component_1_p4, vhdl_component_1_p7;
  wire [7:0] RAM_Addr, ROM_Addr;
  wire [15:0] ROMa_data;
  wire [31:0] CPU_1_r0, CPU_1_r1, CPU_1_r2, CPU_1_r3, CPU_1_r4, CPU_1_r5, CPU_1_r6, CPU_1_r7,
       vhdl_component_1_p5, vhdl_component_1_p9;
  wire [31:8] CPU_1_ram_addr;

  // Probe on RAM_Addr
  // VHDL_Entity #(.content("--------------------------------------------------------------------------------\n-- HEIG-VD, institute REDS, 1400 Yverdon-les-Bains\n-- Project :\n-- File    :\n-- Autor   :\n-- Date    :\n--\n--------------------------------------------------------------------------------\n-- Description :\n--\n--------------------------------------------------------------------------------\n\nlibrary ieee;\n  use ieee.std_logic_1164.all;\n  use ieee.numeric_std.all;\n\nentity VHDL_Component is\n  port(\n      Clock: IN   std_logic;\n      DataIn:  IN   std_logic_vector (31 DOWNTO 0);\n      Address:    IN std_logic_vector (7 DOWNTO 0);\n      WE:    IN   std_logic;\n      OE:    IN   std_logic;\n      DataOut:     OUT  std_logic_vector (31 DOWNTO 0)\n    );\nend VHDL_Component;\n\n--------------------------------------------------------------------------------\n--Complete your VHDL description below\narchitecture type_architecture of VHDL_Component is\n   TYPE mem IS ARRAY(0 TO 255) OF std_logic_vector(31 DOWNTO 0);\n   SIGNAL ram_block : mem;\nBEGIN\n   PROCESS (Clock)\n   BEGIN\n      IF (Clock'event AND clock = '1') THEN\n         IF (WE = '1') THEN\n            ram_block(to_integer(unsigned(Address))) <= DataIn;\n         END IF;\n         IF (OE = '1') THEN\n	         DataOut <= ram_block(to_integer(unsigned(Address)));\n	    END IF;\n      END IF;\n   END PROCESS;\nend type_architecture;")) vhdl_component_1: pin names not known; wires that end beside it: vhdl_component_1_p1, 1'b1, RAM_Addr, vhdl_component_1_p4, vhdl_component_1_p5, RAM_Addr, vhdl_component_1_p7, 1'b1, vhdl_component_1_p9, vhdl_component_1_p9
  LED A0 (.in(vhdl_component_1_p9[0]));
  LED A3 (.in(vhdl_component_1_p9[3]));
  LED A1 (.in(vhdl_component_1_p9[1]));
  LED A2 (.in(vhdl_component_1_p9[2]));
  // Probe on nothing
  // Probe on nothing
  ROM #(.dataWidth(16)) ROMa (.addr(ROM_Addr), .data(ROMa_data));
  Button Clk_Button (.out(vhdl_component_1_p4));
  Button Rst_Button (.out(Rst_Button_out));
  LED A4 (.in(vhdl_component_1_p9[4]));
  LED A5 (.in(vhdl_component_1_p9[5]));
  // Probe on nothing
  // Probe on nothing
  LED A6 (.in(vhdl_component_1_p9[6]));
  LED A7 (.in(vhdl_component_1_p9[7]));
  LED L0 (.in(CPU_1_r0[0]));
  // Probe on CPU_1_r1
  // Probe on CPU_1_r0
  LED L3 (.in(CPU_1_r0[3]));
  LED L1 (.in(CPU_1_r0[1]));
  LED L2 (.in(CPU_1_r0[2]));
  // Probe on CPU_1_r3
  // Probe on CPU_1_r2
  // Probe on CPU_1_r5
  // Probe on CPU_1_r4
  LED L4 (.in(CPU_1_r0[4]));
  LED L5 (.in(CPU_1_r0[5]));
  // Probe on CPU_1_r7
  // Probe on CPU_1_r6
  CPU CPU_1 (
    .Clk(vhdl_component_1_p4), .ROM_In(ROMa_data), .RAM_Addr({CPU_1_ram_addr, RAM_Addr}),
    .RAM_Out(vhdl_component_1_p5), .Rst(Rst_Button_out), .RAM_In(vhdl_component_1_p9), .ROM_Addr(ROM_Addr),
    .R0(CPU_1_r0), .R1(CPU_1_r1), .R2(CPU_1_r2), .R3(CPU_1_r3), .R4(CPU_1_r4), .R5(CPU_1_r5), .R6(CPU_1_r6),
    .R7(CPU_1_r7), .Store(vhdl_component_1_p7), .Load(vhdl_component_1_p1));
  LED L6 (.in(CPU_1_r0[6]));
  LED L7 (.in(CPU_1_r0[7]));
  LED LED_1 (.in(RAM_Addr[0]));
  LED LED_2 (.in(RAM_Addr[1]));
  // Probe on nothing
  LED LED_4 (.in(RAM_Addr[3]));
  LED LED_3 (.in(RAM_Addr[2]));
  // Probe on nothing
  // Probe on nothing
  LED LED_5 (.in(RAM_Addr[4]));
  LED LED_6 (.in(RAM_Addr[5]));
  // Probe on nothing
  LED LED_7 (.in(RAM_Addr[6]));
  LED LED_8 (.in(RAM_Addr[7]));

  // Notes on the sheet:
  //   contents of ROMa (hex, n*v repeats v):
  //   b090 2005 900c 2002 980c 9008 9808 2003 9004 9804 2004 9000 9804
  //   Use only 8 bit adresses
endmodule

module CPU (
  input  [31:0] RAM_In,
  input  [15:0] ROM_In,
  input  Clk,
  input  Rst,
  output [7:0] ROM_Addr,
  output [31:0] RAM_Addr,
  output [31:0] R3,
  output [31:0] R7,
  output [31:0] RAM_Out,
  output [31:0] R2,
  output [31:0] R6,
  output [31:0] R1,
  output [31:0] R5,
  output [31:0] R0,
  output [31:0] R4,
  output Load,
  output Store
);

  wire Controller_1_carry, Controller_1_dp_shift, Controller_1_move;
  wire [2:0] Controller_1_rd, Controller_1_rm, Controller_1_rn;
  wire [3:0] ALU_1_flags, Controller_1_alu_opcode;
  wire [4:0] Controller_1_imm5, multiplexer_3_out;
  wire [7:0] Controller_1_imm8;
  wire [31:0] ALU_1_s, bit_extender_1_out, multiplexer_1_out, multiplexer_2_out, Regs_1_p15;

  Controller Controller_1 (
    .Load(Load), .Rd(Controller_1_rd), .Reset(Rst), .Rm(Controller_1_rm), .Rn(Controller_1_rn),
    .Imm8(Controller_1_imm8), .Imm5(Controller_1_imm5), .Inst(ROM_In), .PC(ROM_Addr), .Flags(ALU_1_flags),
    .ALU_Opcode(Controller_1_alu_opcode), .Move(Controller_1_move), .DP_Shift(Controller_1_dp_shift),
    .Carry(Controller_1_carry), .Store(Store), .RAM_Addr(RAM_Addr), .Clk(Clk));
  Multiplexer #(.width(32), .enable("false")) multiplexer_1 (
    .in0(ALU_1_s), .in1(RAM_In), .out(multiplexer_1_out), .sel(Load));
  assign bit_extender_1_out = {{24{1'b0}}, Controller_1_imm8};  // Bit_Extender bit_extender_1
  Multiplexer #(.width(32), .enable("false")) multiplexer_2 (
    .in0(multiplexer_1_out), .in1(bit_extender_1_out), .out(multiplexer_2_out), .sel(Controller_1_move));
  // BancRegistre Regs_1: pin names not known; wires that end beside it: multiplexer_2_out, Controller_1_rd, Clk, R0, Rst, R1, R2, R3, R4, Controller_1_rm, R5, R6, Controller_1_rn, R7, Regs_1_p15, RAM_Out
  Multiplexer #(.width(5), .enable("false")) multiplexer_3 (
    .in0(RAM_Out[4:0]), .in1(Controller_1_imm5), .out(multiplexer_3_out), .sel(Controller_1_dp_shift));
  ALU ALU_1 (
    .S(ALU_1_s), .Flags(ALU_1_flags), .Codop(Controller_1_alu_opcode), .CarryIn(Controller_1_carry),
    .A(RAM_Out), .B(Regs_1_p15), .Shift(multiplexer_3_out));

  // Notes on the sheet:
  //   RAM/ALU Input selector
  //   Use data from register or immediate for shift
  //   Imm8 input for Move
endmodule

module Altera_RAM (
);

  // VHDL_Entity #(.content("--------------------------------------------------------------------------------\n-- HEIG-VD, institute REDS, 1400 Yverdon-les-Bains\n-- Project :\n-- File    :\n-- Autor   :\n-- Date    :\n--\n--------------------------------------------------------------------------------\n-- Description :\n--\n--------------------------------------------------------------------------------\n\nlibrary ieee;\n  use ieee.std_logic_1164.all;\n  use ieee.numeric_std.all;\n\nentity VHDL_Component is\n  port(\n      Clock: IN   std_logic;\n      DataIn:  IN   std_logic_vector (31 DOWNTO 0);\n      Address:    IN std_logic_vector (7 DOWNTO 0);\n      WE:    IN   std_logic;\n      OE:    IN   std_logic;\n      DataOut:     OUT  std_logic_vector (31 DOWNTO 0)\n    );\nend VHDL_Component;\n\n--------------------------------------------------------------------------------\n--Complete your VHDL description below\narchitecture type_architecture of VHDL_Component is\n   TYPE mem IS ARRAY(0 TO 255) OF std_logic_vector(31 DOWNTO 0);\n   SIGNAL ram_block : mem;\nBEGIN\n   PROCESS (Clock)\n   BEGIN\n      IF (Clock'event AND clock = '1') THEN\n         IF (WE = '1') THEN\n            ram_block(to_integer(unsigned(Address))) <= DataIn;\n         END IF;\n         IF (OE = '1') THEN\n	         DataOut <= ram_block(to_integer(unsigned(Address)));\n	    END IF;\n      END IF;\n   END PROCESS;\nend type_architecture;")) vhdl_component_1: pin names not known
endmodule
