// Logisim project RAM_Altera_VHDL.circ as structural Verilog: 1 circuit, main circuit main
module main (
);

  wire Clk_out, SL_out, vhdl_component_1_p6;
  wire [3:0] vhdl_component_1_p1, vhdl_component_1_p4;
  wire [31:0] vhdl_component_1_p7;

  Button Clk (.out(Clk_out));
  Button SL (.out(SL_out));
  // VHDL_Entity #(.content("--------------------------------------------------------------------------------\n-- HEIG-VD, institute REDS, 1400 Yverdon-les-Bains\n-- Project :\n-- File    :\n-- Autor   :\n-- Date    :\n--\n--------------------------------------------------------------------------------\n-- Description :\n--\n--------------------------------------------------------------------------------\n\nlibrary ieee;\n  use ieee.std_logic_1164.all;\n  use ieee.numeric_std.all;\n\nentity VHDL_Component is\n  port(\n      Clock: IN   std_logic;\n      DataIn:  IN   std_logic_vector (31 DOWNTO 0);\n      Address:    IN std_logic_vector (7 DOWNTO 0);\n      WE:    IN   std_logic;\n      OE:    IN   std_logic;\n      DataOut:     OUT  std_logic_vector (31 DOWNTO 0)\n    );\nend VHDL_Component;\n\n--------------------------------------------------------------------------------\n--Complete your VHDL description below\narchitecture type_architecture of VHDL_Component is\n   TYPE mem IS ARRAY(0 TO 255) OF std_logic_vector(31 DOWNTO 0);\n   SIGNAL ram_block : mem;\nBEGIN\n   PROCESS (Clock)\n   BEGIN\n      IF (Clock'event AND clock = '1') THEN\n         IF (WE = '1') THEN\n            ram_block(to_integer(unsigned(Address))) <= DataIn;\n         END IF;\n         IF (OE = '1') THEN\n	         DataOut <= ram_block(to_integer(unsigned(Address)));\n	    END IF;\n      END IF;\n   END PROCESS;\nend type_architecture;")) vhdl_component_1: pin names not known; wires that end beside it: {{28{1'b0}}, vhdl_component_1_p1}, Clk_out, {{28{1'b0}}, vhdl_component_1_p1}, {4'b0000, vhdl_component_1_p4}, SL_out, vhdl_component_1_p6, vhdl_component_1_p7
  not not_1 (vhdl_component_1_p6, SL_out);
  Button a1 (.out(vhdl_component_1_p4[0]));
  Button a2 (.out(vhdl_component_1_p4[1]));
  Button a3 (.out(vhdl_component_1_p4[2]));
  Button a4 (.out(vhdl_component_1_p4[3]));
  Button d1 (.out(vhdl_component_1_p1[0]));
  Button d2 (.out(vhdl_component_1_p1[1]));
  Button d3 (.out(vhdl_component_1_p1[2]));
  Button d5 (.out(vhdl_component_1_p1[3]));
  LED LED_1 (.in(vhdl_component_1_p7[0]));
  LED LED_2 (.in(vhdl_component_1_p7[1]));
  LED LED_3 (.in(vhdl_component_1_p7[2]));
  LED LED_4 (.in(vhdl_component_1_p7[3]));
endmodule
