// Logisim project RAM_Logisim.circ as structural Verilog: 1 circuit, main circuit main
module main (
);

  wire clk_out, ls_out, not_1_out;
  wire [3:0] a1_out, d1_out;
  wire [31:0] RAMa_dout;

  Button clk (.out(clk_out));
  Button ls (.out(ls_out));
  Button d1 (.out(d1_out[0]));
  Button d2 (.out(d1_out[1]));
  Button d3 (.out(d1_out[2]));
  Button d4 (.out(d1_out[3]));
  not not_1 (not_1_out, ls_out);
  Button a1 (.out(a1_out[0]));
  Button a2 (.out(a1_out[1]));
  Button a3 (.out(a1_out[2]));
  Button a4 (.out(a1_out[3]));
  RAM #(.dataWidth(32), .databus("bibus")) RAMa (
    .addr({4'b0000, a1_out}), .we(ls_out), .oe(not_1_out), .clk(clk_out), .din({{28{1'b0}}, d1_out}),
    .dout(RAMa_dout));
  LED l1 (.in(RAMa_dout[0]));
  LED l3 (.in(RAMa_dout[1]));
  LED l4 (.in(RAMa_dout[2]));
  LED l5 (.in(RAMa_dout[3]));
endmodule
